// Logisim project orthogonal_isa.circ as structural Verilog: 2 circuits, main circuit main
module main (
  input  ENABLE,
  input  in_2
);

  wire clock_1_out, ortho_goodenough_arch_1_clk_out, ortho_goodenough_arch_1_read,
       ortho_goodenough_arch_1_write;
  wire [15:0] ortho_goodenough_arch_1_address_out, ortho_goodenough_arch_1_data_out, ram_1_dout;

  Clock clock_1 (.out(clock_1_out));
  ortho_goodenough_arch ortho_goodenough_arch_1 (
    .CLK_in(clock_1_out), .Enable(ENABLE), .Data_in(ram_1_dout), .Interrupt(in_2),
    .CLK_out(ortho_goodenough_arch_1_clk_out), .DATA_out(ortho_goodenough_arch_1_data_out),
    .write(ortho_goodenough_arch_1_write), .read(ortho_goodenough_arch_1_read),
    .address_out(ortho_goodenough_arch_1_address_out));  // open: Interrupt_maskable
  RAM #(.addrWidth(16), .asyncread("true"), .dataWidth(16), .\type ("nonvolatile")) ram_1 (
    .addr(ortho_goodenough_arch_1_address_out), .we(ortho_goodenough_arch_1_write),
    .oe(ortho_goodenough_arch_1_read), .clk(ortho_goodenough_arch_1_clk_out),
    .din(ortho_goodenough_arch_1_data_out), .dout(ram_1_dout));

  // Notes on the sheet:
  //   ENABLE: initial=0x1
  //   solve branch misspredictions and reg to reg
endmodule

module ortho_goodenough_arch (
  input  CLK_in,
  input  Enable,
  input  [15:0] Data_in,
  input  Interrupt,
  input  Interrupt_maskable,
  output [15:0] address_out,
  output CLK_out,
  output [15:0] DATA_out,
  output write,
  output read
);

  wire adder_1_cout, and_1_out, and_2_out, and_4_out, and_5_out, and_6_out, and_7_out, and_8_out, and_9_out,
       and_10_out, and_11_out, and_12_out, and_13_out, and_14_out, and_15_out, and_16_out, and_17_out,
       and_18_out, and_19_out, and_20_out, and_21_out, and_23_out, and_24_out, and_25_out, and_26_out,
       and_27_out, and_28_out, and_29_out, and_30_out, and_31_out, and_32_out, and_33_out, and_34_out,
       and_35_out, and_36_out, and_37_out, and_38_out, and_39_out, and_40_out, and_41_out, and_42_out,
       and_43_out, and_44_out, and_45_out, and_46_out, and_47_out, and_48_out, and_50_out, and_51_out,
       and_52_out, and_53_out, and_54_out, and_55_out, and_56_out, and_57_out, and_59_out, and_60_out,
       comparator_1_eq, comparator_2_eq, comparator_3_eq, comparator_4_eq, comparator_5_eq, comparator_6_eq,
       comparator_7_eq, comparator_8_eq, comparator_9_eq, comparator_10_eq, comparator_11_eq,
       comparator_12_eq, comparator_13_eq, comparator_14_eq, comparator_15_eq, comparator_16_eq,
       comparator_17_eq, comparator_18_eq, comparator_19_eq, comparator_20_eq, comparator_21_eq,
       comparator_22_eq, comparator_23_eq, comparator_24_eq, comparator_25_eq, comparator_26_eq,
       comparator_27_eq, comparator_28_eq, comparator_29_eq, comparator_30_eq, comparator_31_eq,
       comparator_32_eq, comparator_33_eq, comparator_34_eq, comparator_35_eq, comparator_36_eq,
       comparator_37_eq, comparator_38_eq, comparator_39_eq, comparator_40_eq, comparator_41_eq,
       comparator_42_eq, comparator_43_eq, comparator_44_eq, comparator_45_eq, comparator_46_eq,
       comparator_47_eq, comparator_48_gt, comparator_49_gt, comparator_50_eq, comparator_51_eq,
       comparator_51_lt, comparator_52_eq, comparator_52_lt, comparator_53_eq, comparator_53_lt,
       comparator_54_eq, comparator_55_eq, comparator_56_eq, comparator_57_eq, comparator_58_lt,
       comparator_59_eq, comparator_60_eq, comparator_61_eq, comparator_62_eq, comparator_63_eq,
       comparator_63_gt, comparator_63_lt, comparator_64_eq, comparator_64_gt, comparator_64_lt,
       comparator_65_eq, comparator_66_eq, controlled_buffer_36_out, controlled_buffer_39_out,
       controlled_buffer_123_out, controlled_buffer_125_out, controlled_buffer_126_out,
       controlled_buffer_128_out, controlled_buffer_130_out, counter_2_carry, d_ff_1_q, d_ff_2_q,
       decoder_1_out0, decoder_1_out1, decoder_1_out2, decoder_1_out3, decoder_1_out4, decoder_1_out5,
       decoder_1_out6, decoder_1_out7, decoder_1_out8, decoder_1_out9, decoder_1_out10, decoder_1_out11,
       decoder_1_out12, decoder_1_out13, decoder_1_out14, decoder_1_out15, decoder_2_out0, decoder_2_out1,
       decoder_2_out2, decoder_2_out3, decoder_2_out4, decoder_2_out5, decoder_2_out6, decoder_2_out7,
       decoder_3_out0, decoder_3_out1, decoder_3_out2, decoder_3_out3, decoder_4_out0, decoder_4_out1,
       decoder_4_out2, decoder_4_out3, decoder_5_out0, decoder_5_out1, decoder_5_out2, decoder_5_out3,
       decoder_6_out0, decoder_6_out1, decoder_6_out2, decoder_6_out3, decoder_7_out0, decoder_7_out1,
       decoder_7_out2, decoder_7_out3, decoder_8_out0, decoder_8_out1, decoder_8_out2, decoder_8_out3,
       decoder_9_out0, decoder_9_out1, decoder_9_out2, decoder_9_out3, decoder_10_out0, decoder_10_out1,
       decoder_11_out0, decoder_11_out1, decoder_11_out2, decoder_11_out3, decoder_11_out4, decoder_11_out5,
       decoder_11_out6, decoder_11_out7, decoder_11_out8, decoder_11_out9, decoder_11_out10,
       decoder_11_out11, decoder_11_out12, decoder_11_out13, decoder_11_out14, decoder_11_out15,
       decoder_11_out16, decoder_11_out18, decoder_11_out19, decoder_11_out20, decoder_11_out22, nand_1_out,
       not_2_out, not_3_out, not_5_out, not_6_out, not_7_out, not_8_out, not_9_out, not_10_out, not_11_out,
       not_12_out, not_13_out, not_14_out, or_1_out, or_2_out, or_3_out, or_4_out, or_5_out, or_6_out,
       or_7_out, or_8_out, or_9_out, or_10_out, or_11_out, or_12_out, or_13_out, or_14_out, or_15_out,
       or_16_out, or_17_out, or_18_out, or_19_out, or_21_out, or_23_out, or_24_out, or_25_out, or_26_out,
       or_27_out, or_28_out, or_29_out, or_30_out, or_31_out, or_32_out, or_33_out, or_34_out, or_35_out,
       or_36_out, or_37_out, or_40_out, or_41_out, or_42_out, or_43_out, or_44_out, or_45_out, or_47_out,
       or_48_out, or_49_out, or_50_out, or_51_out, or_52_out, or_53_out, or_54_out, or_55_out, or_56_out,
       or_58_out, or_59_out, or_60_out, or_61_out, or_66_out, pull_resistor_3_node, pull_resistor_5_node,
       pull_resistor_6_node, pull_resistor_10_node, pull_resistor_12_node, pull_resistor_13_node,
       pull_resistor_19_node, pull_resistor_21_node, s_r_ff_1_q, s_r_ff_2_q, subtractor_2_bout, T0_carry,
       T1_carry;
  wire [0:0] controlled_buffer_131_out, or_62_out;
  wire [1:0] controlled_buffer_111_out, counter_2_q, counter_3_q, counter_4_q, counter_5_q, counter_6_q,
       counter_7_q, counter_8_q, counter_9_q, counter_10_q, counter_11_q, counter_12_q, counter_13_q,
       counter_14_q, counter_15_q, counter_16_q, counter_17_q, counter_18_q, not_1_out, pull_resistor_1_node;
  wire [2:0] controlled_buffer_111_out_2;
  wire [3:0] counter_1_q;
  wire [4:0] multiplexer_7_out, multiplexer_9_out, multiplexer_26_out;
  wire [5:0] or_64_out;
  wire [11:0] ST_R_q;
  wire [11:11] or_46_out;
  wire [14:0] EXECUTE_stage_q;
  wire [14:1] controlled_buffer_114_out;
  wire [15:0] adder_1_out, address_out_t, and_58_out, controlled_buffer_1_out, controlled_buffer_35_out,
       controlled_buffer_110_out, controlled_buffer_112_out, controlled_buffer_113_out, data_1_q, data_2_q,
       fpadder_1_out, fpmultiplier_1_out, fpsubtractor_1_out, int_vec_q, multiplexer_1_out,
       multiplexer_2_out, multiplexer_3_out, multiplexer_4_out, multiplexer_5_out, multiplexer_8_out,
       multiplexer_10_out, multiplexer_11_out, multiplexer_12_out, multiplexer_13_out, multiplexer_14_out,
       multiplexer_15_out, multiplexer_16_out, multiplexer_17_out, multiplexer_18_out, multiplexer_19_out,
       multiplexer_20_out, multiplexer_21_out, multiplexer_22_out, multiplexer_23_out, multiplexer_24_out,
       multiplexer_25_out, multiplexer_28_out, multiplexer_29_out, multiplexer_30_out, multiplexer_31_out,
       multiplexer_32_out, multiplexer_33_out, multiplexer_34_out, multiplexer_36_out, multiplexer_37_out,
       multiplexer_38_out, multiplier_1_out, negator_1_out, or_39_out, or_57_out, PC_q, pull_resistor_4_node,
       pull_resistor_8_node, pull_resistor_16_node, pull_resistor_26_node, r0_q, r4_q, r8_q, r12_q, r16_q,
       r20_q, r21_q, r22_q, register_1_q, register_2_q, register_3_q, register_4_q, register_5_q,
       register_6_q, register_7_q, register_8_q, register_9_q, register_10_q, register_11_q, register_12_q,
       register_13_q, register_14_q, register_15_q, register_16_q, register_17_q, register_18_q,
       register_19_q, register_20_q, register_21_q, register_22_q, register_23_q, register_24_q,
       register_25_q, register_26_q, register_27_q, register_28_q, register_29_q, register_30_q,
       register_31_q, register_32_q, register_33_q, register_34_q, register_35_q, register_36_q,
       register_37_q, register_38_q, register_39_q, register_40_q, register_41_q, register_42_q,
       register_43_q, register_44_q, register_45_q, register_46_q, register_47_q, register_48_q,
       register_49_q, register_50_q, register_51_q, SP_q, SSP_q, subtractor_1_out, subtractor_2_out, T0_q,
       T1_q, undriven, xor_1_out;
  wire [15:10] IR_q;
  wire [15:15] controlled_buffer_124_out;
  wire [21:0] IR_q_2, READ_stage_q;

  and and_1 (and_1_out, not_2_out, IR_q_2[19]);
  Decoder #(.select(4)) decoder_1 (
    .out0(decoder_1_out0), .out1(decoder_1_out1), .out2(decoder_1_out2), .out3(decoder_1_out3),
    .out4(decoder_1_out4), .out5(decoder_1_out5), .out6(decoder_1_out6), .out7(decoder_1_out7),
    .out8(decoder_1_out8), .out9(decoder_1_out9), .out10(decoder_1_out10), .out11(decoder_1_out11),
    .out12(decoder_1_out12), .out13(decoder_1_out13), .out14(decoder_1_out14), .out15(decoder_1_out15),
    .sel(counter_1_q), .en(and_1_out));
  Register #(.trigger("falling"), .width(16)) register_1 (
    .D(PC_q), .en(IR_q_2[19]), .clk(CLK_out), .Q(register_1_q));  // open: clr
  Counter #(.max('hf), .width(4)) counter_1 (
    .count(and_1_out), .Q(counter_1_q), .clk(not_1_out[1]));  // open: load, D, carry, up, clr
  Multiplexer #(.select(2), .width(16)) multiplexer_1 (
    .in0(16'h7385), .in1(16'h3bc), .in2({16{1'b0}}), .in3({16{1'b0}}), .out(multiplexer_1_out),
    .sel(counter_2_q));
  Counter #(.max('h3), .ongoal("stay"), .width(2)) counter_2 (
    .count(or_44_out), .Q(counter_2_q), .carry(counter_2_carry), .clk(CLK_out));  // open: load, D, up, clr
  Comparator #(.mode("unsigned"), .width(2)) comparator_1 (
    .a(counter_2_q), .b(pull_resistor_1_node), .eq(comparator_1_eq));  // open: gt, lt
  Pull_Resistor pull_resistor_1 (.node(pull_resistor_1_node));
  and and_2 (and_2_out, comparator_1_eq, or_44_out);
  and and_3 (CLK_out, CLK_in, Enable);
  assign controlled_buffer_1_out = not_3_out ? Data_in : 16'bz;  // Controlled_Buffer controlled_buffer_1
  Pull_Resistor pull_resistor_2 (.node(controlled_buffer_1_out));
  Pull_Resistor #(.pull(1)) pull_resistor_3 (.node(pull_resistor_3_node));
  Subtractor #(.width(16)) subtractor_1 (
    .a(register_1_q), .b(pull_resistor_4_node), .out(subtractor_1_out), .bin(pull_resistor_3_node));  // open: bout
  Pull_Resistor pull_resistor_4 (.node(pull_resistor_4_node));
  not not_1 (not_1_out[0], not_1_out[1]);
  and and_4 (and_4_out, not_1_out[1], decoder_1_out1);
  or or_1 (or_1_out, comparator_3_eq, EXECUTE_stage_q[12]);
  and and_5 (and_5_out, not_1_out[1], decoder_1_out2);
  or or_2 (or_2_out, comparator_4_eq, EXECUTE_stage_q[12]);
  and and_6 (and_6_out, not_1_out[1], decoder_1_out3);
  or or_3 (or_3_out, comparator_5_eq, EXECUTE_stage_q[12]);
  and and_7 (and_7_out, not_1_out[1], decoder_1_out4);
  or or_4 (or_4_out, comparator_6_eq, EXECUTE_stage_q[12]);
  and and_8 (and_8_out, not_1_out[1], decoder_1_out5);
  or or_5 (or_5_out, comparator_7_eq, EXECUTE_stage_q[12]);
  and and_9 (and_9_out, not_1_out[1], decoder_1_out6);
  or or_6 (or_6_out, comparator_8_eq, EXECUTE_stage_q[12]);
  and and_10 (and_10_out, not_1_out[1], decoder_1_out7);
  or or_7 (or_7_out, comparator_9_eq, EXECUTE_stage_q[12]);
  and and_11 (and_11_out, not_1_out[1], decoder_1_out8);
  or or_8 (or_8_out, comparator_10_eq, EXECUTE_stage_q[12]);
  and and_12 (and_12_out, not_1_out[1], decoder_1_out9);
  or or_9 (or_9_out, comparator_11_eq, EXECUTE_stage_q[12]);
  and and_13 (and_13_out, not_1_out[1], decoder_1_out10);
  or or_10 (or_10_out, comparator_12_eq, EXECUTE_stage_q[12]);
  and and_14 (and_14_out, not_1_out[1], decoder_1_out11);
  or or_11 (or_11_out, comparator_13_eq, EXECUTE_stage_q[12]);
  and and_15 (and_15_out, not_1_out[1], decoder_1_out12);
  or or_12 (or_12_out, comparator_14_eq, EXECUTE_stage_q[12]);
  and and_16 (and_16_out, not_1_out[1], decoder_1_out13);
  or or_13 (or_13_out, comparator_15_eq, EXECUTE_stage_q[12]);
  and and_17 (and_17_out, not_1_out[1], decoder_1_out14);
  or or_14 (or_14_out, comparator_16_eq, EXECUTE_stage_q[12]);
  and and_18 (and_18_out, not_1_out[1], decoder_1_out15);
  or or_15 (or_15_out, comparator_17_eq, EXECUTE_stage_q[12]);
  Multiplexer #(.width(16)) multiplexer_2 (
    .in0(multiplexer_1_out), .in1(controlled_buffer_1_out), .out(multiplexer_2_out), .sel(and_19_out));
  Pull_Resistor pull_resistor_5 (.node(pull_resistor_5_node));
  assign pull_resistor_5_node = nand_1_out ? CLK_out : 1'bz;  // Controlled_Buffer controlled_buffer_2
  and and_19 (and_19_out, nand_1_out, ~or_44_out);  // AND_Gate
  Counter #(.max('h3), .ongoal("stay"), .width(2)) counter_3 (
    .load(decoder_1_out0), .D(not_1_out), .count(EXECUTE_stage_q[12]), .Q(counter_3_q), .up(not_1_out[1]),
    .clk(CLK_out));  // open: carry, clr
  Counter #(.max('h3), .ongoal("stay"), .width(2)) counter_4 (
    .load(EXECUTE_stage_q[12]), .D(not_1_out), .count(or_1_out), .Q(counter_4_q), .up(and_4_out),
    .clk(CLK_out));  // open: carry, clr
  Counter #(.max('h3), .ongoal("stay"), .width(2)) counter_5 (
    .load(EXECUTE_stage_q[12]), .D(not_1_out), .count(or_2_out), .Q(counter_5_q), .up(and_5_out),
    .clk(CLK_out));  // open: carry, clr
  Counter #(.max('h3), .ongoal("stay"), .width(2)) counter_6 (
    .load(EXECUTE_stage_q[12]), .D(not_1_out), .count(or_3_out), .Q(counter_6_q), .up(and_6_out),
    .clk(CLK_out));  // open: carry, clr
  Counter #(.max('h3), .ongoal("stay"), .width(2)) counter_7 (
    .load(EXECUTE_stage_q[12]), .D(not_1_out), .count(or_4_out), .Q(counter_7_q), .up(and_7_out),
    .clk(CLK_out));  // open: carry, clr
  Counter #(.max('h3), .ongoal("stay"), .width(2)) counter_8 (
    .load(EXECUTE_stage_q[12]), .D(not_1_out), .count(or_5_out), .Q(counter_8_q), .up(and_8_out),
    .clk(CLK_out));  // open: carry, clr
  Counter #(.max('h3), .ongoal("stay"), .width(2)) counter_9 (
    .load(EXECUTE_stage_q[12]), .D(not_1_out), .count(or_6_out), .Q(counter_9_q), .up(and_9_out),
    .clk(CLK_out));  // open: carry, clr
  Counter #(.max('h3), .ongoal("stay"), .width(2)) counter_10 (
    .load(EXECUTE_stage_q[12]), .D(not_1_out), .count(or_7_out), .Q(counter_10_q), .up(and_10_out),
    .clk(CLK_out));  // open: carry, clr
  Counter #(.max('h3), .ongoal("stay"), .width(2)) counter_11 (
    .load(EXECUTE_stage_q[12]), .D(not_1_out), .count(or_8_out), .Q(counter_11_q), .up(and_11_out),
    .clk(CLK_out));  // open: carry, clr
  Counter #(.max('h3), .ongoal("stay"), .width(2)) counter_12 (
    .load(EXECUTE_stage_q[12]), .D(not_1_out), .count(or_9_out), .Q(counter_12_q), .up(and_12_out),
    .clk(CLK_out));  // open: carry, clr
  Counter #(.max('h3), .ongoal("stay"), .width(2)) counter_13 (
    .load(EXECUTE_stage_q[12]), .D(not_1_out), .count(or_10_out), .Q(counter_13_q), .up(and_13_out),
    .clk(CLK_out));  // open: carry, clr
  Counter #(.max('h3), .ongoal("stay"), .width(2)) counter_14 (
    .load(EXECUTE_stage_q[12]), .D(not_1_out), .count(or_11_out), .Q(counter_14_q), .up(and_14_out),
    .clk(CLK_out));  // open: carry, clr
  Counter #(.max('h3), .ongoal("stay"), .width(2)) counter_15 (
    .load(EXECUTE_stage_q[12]), .D(not_1_out), .count(or_12_out), .Q(counter_15_q), .up(and_15_out),
    .clk(CLK_out));  // open: carry, clr
  Counter #(.max('h3), .ongoal("stay"), .width(2)) counter_16 (
    .load(EXECUTE_stage_q[12]), .D(not_1_out), .count(or_13_out), .Q(counter_16_q), .up(and_16_out),
    .clk(CLK_out));  // open: carry, clr
  Counter #(.max('h3), .ongoal("stay"), .width(2)) counter_17 (
    .load(EXECUTE_stage_q[12]), .D(not_1_out), .count(or_14_out), .Q(counter_17_q), .up(and_17_out),
    .clk(CLK_out));  // open: carry, clr
  Counter #(.max('h3), .ongoal("stay"), .width(2)) counter_18 (
    .load(EXECUTE_stage_q[12]), .D(not_1_out), .count(or_15_out), .Q(counter_18_q), .up(and_18_out),
    .clk(CLK_out));  // open: carry, clr
  Register #(.width(16)) IR (
    .D(multiplexer_2_out), .en(pull_resistor_5_node), .clk(pull_resistor_5_node), .Q({IR_q, IR_q_2[9:0]}));  // open: clr
  nand nand_1 (nand_1_out, or_49_out, or_16_out);
  Register #(.width(16)) register_2 (
    .D(subtractor_1_out), .en(decoder_1_out0), .clk(CLK_out), .Q(register_2_q));  // open: clr
  Register #(.width(16)) register_3 (
    .D(subtractor_1_out), .en(decoder_1_out1), .clk(CLK_out), .Q(register_3_q));  // open: clr
  Register #(.width(16)) register_4 (
    .D(subtractor_1_out), .en(decoder_1_out2), .clk(CLK_out), .Q(register_4_q));  // open: clr
  Register #(.width(16)) register_5 (
    .D(subtractor_1_out), .en(decoder_1_out3), .clk(CLK_out), .Q(register_5_q));  // open: clr
  Register #(.width(16)) register_6 (
    .D(subtractor_1_out), .en(decoder_1_out4), .clk(CLK_out), .Q(register_6_q));  // open: clr
  Register #(.width(16)) register_7 (
    .D(subtractor_1_out), .en(decoder_1_out5), .clk(CLK_out), .Q(register_7_q));  // open: clr
  Register #(.width(16)) register_8 (
    .D(subtractor_1_out), .en(decoder_1_out6), .clk(CLK_out), .Q(register_8_q));  // open: clr
  Register #(.width(16)) register_9 (
    .D(subtractor_1_out), .en(decoder_1_out7), .clk(CLK_out), .Q(register_9_q));  // open: clr
  Register #(.width(16)) register_10 (
    .D(subtractor_1_out), .en(decoder_1_out8), .clk(CLK_out), .Q(register_10_q));  // open: clr
  Register #(.width(16)) register_11 (
    .D(subtractor_1_out), .en(decoder_1_out9), .clk(CLK_out), .Q(register_11_q));  // open: clr
  Register #(.width(16)) register_12 (
    .D(subtractor_1_out), .en(decoder_1_out10), .clk(CLK_out), .Q(register_12_q));  // open: clr
  Register #(.width(16)) register_13 (
    .D(subtractor_1_out), .en(decoder_1_out11), .clk(CLK_out), .Q(register_13_q));  // open: clr
  Register #(.width(16)) register_14 (
    .D(subtractor_1_out), .en(decoder_1_out12), .clk(CLK_out), .Q(register_14_q));  // open: clr
  Register #(.width(16)) register_15 (
    .D(subtractor_1_out), .en(decoder_1_out13), .clk(CLK_out), .Q(register_15_q));  // open: clr
  Register #(.width(16)) register_16 (
    .D(subtractor_1_out), .en(decoder_1_out14), .clk(CLK_out), .Q(register_16_q));  // open: clr
  Register #(.width(16)) register_17 (
    .D(subtractor_1_out), .en(decoder_1_out15), .clk(CLK_out), .Q(register_17_q));  // open: clr
  Comparator #(.width(16)) comparator_2 (.a(PC_q), .b(register_2_q), .eq(comparator_2_eq));  // open: gt, lt
  Register #(.width(16)) register_18 (
    .D(data_2_q), .en(comparator_2_eq), .clk(CLK_out), .Q(register_18_q));  // open: clr
  Comparator #(.width(16)) comparator_3 (.a(PC_q), .b(register_3_q), .eq(comparator_3_eq));  // open: gt, lt
  Register #(.width(16)) register_19 (
    .D(data_2_q), .en(comparator_3_eq), .clk(CLK_out), .Q(register_19_q));  // open: clr
  Comparator #(.width(16)) comparator_4 (.a(PC_q), .b(register_4_q), .eq(comparator_4_eq));  // open: gt, lt
  Register #(.width(16)) register_20 (
    .D(data_2_q), .en(comparator_4_eq), .clk(CLK_out), .Q(register_20_q));  // open: clr
  Comparator #(.width(16)) comparator_5 (.a(PC_q), .b(register_5_q), .eq(comparator_5_eq));  // open: gt, lt
  Register #(.width(16)) register_21 (
    .D(data_2_q), .en(comparator_5_eq), .clk(CLK_out), .Q(register_21_q));  // open: clr
  Comparator #(.width(16)) comparator_6 (.a(PC_q), .b(register_6_q), .eq(comparator_6_eq));  // open: gt, lt
  Register #(.width(16)) register_22 (
    .D(data_2_q), .en(comparator_6_eq), .clk(CLK_out), .Q(register_22_q));  // open: clr
  Comparator #(.width(16)) comparator_7 (.a(PC_q), .b(register_7_q), .eq(comparator_7_eq));  // open: gt, lt
  Register #(.width(16)) register_23 (
    .D(data_2_q), .en(comparator_7_eq), .clk(CLK_out), .Q(register_23_q));  // open: clr
  Comparator #(.width(16)) comparator_8 (.a(PC_q), .b(register_8_q), .eq(comparator_8_eq));  // open: gt, lt
  Register #(.width(16)) register_24 (
    .D(data_2_q), .en(comparator_8_eq), .clk(CLK_out), .Q(register_24_q));  // open: clr
  Comparator #(.width(16)) comparator_9 (.a(PC_q), .b(register_9_q), .eq(comparator_9_eq));  // open: gt, lt
  Register #(.width(16)) register_25 (
    .D(data_2_q), .en(comparator_9_eq), .clk(CLK_out), .Q(register_25_q));  // open: clr
  Comparator #(.width(16)) comparator_10 (.a(PC_q), .b(register_10_q), .eq(comparator_10_eq));  // open: gt, lt
  Register #(.width(16)) register_26 (
    .D(data_2_q), .en(comparator_10_eq), .clk(CLK_out), .Q(register_26_q));  // open: clr
  Comparator #(.width(16)) comparator_11 (.a(PC_q), .b(register_11_q), .eq(comparator_11_eq));  // open: gt, lt
  Register #(.width(16)) register_27 (
    .D(data_2_q), .en(comparator_11_eq), .clk(CLK_out), .Q(register_27_q));  // open: clr
  Comparator #(.width(16)) comparator_12 (.a(PC_q), .b(register_12_q), .eq(comparator_12_eq));  // open: gt, lt
  Register #(.width(16)) register_28 (
    .D(data_2_q), .en(comparator_12_eq), .clk(CLK_out), .Q(register_28_q));  // open: clr
  Comparator #(.width(16)) comparator_13 (.a(PC_q), .b(register_13_q), .eq(comparator_13_eq));  // open: gt, lt
  Register #(.width(16)) register_29 (
    .D(data_2_q), .en(comparator_13_eq), .clk(CLK_out), .Q(register_29_q));  // open: clr
  Comparator #(.width(16)) comparator_14 (.a(PC_q), .b(register_14_q), .eq(comparator_14_eq));  // open: gt, lt
  Register #(.width(16)) register_30 (
    .D(data_2_q), .en(comparator_14_eq), .clk(CLK_out), .Q(register_30_q));  // open: clr
  Comparator #(.width(16)) comparator_15 (.a(PC_q), .b(register_15_q), .eq(comparator_15_eq));  // open: gt, lt
  Register #(.width(16)) register_31 (
    .D(data_2_q), .en(comparator_15_eq), .clk(CLK_out), .Q(register_31_q));  // open: clr
  Comparator #(.width(16)) comparator_16 (.a(PC_q), .b(register_16_q), .eq(comparator_16_eq));  // open: gt, lt
  Register #(.width(16)) register_32 (
    .D(data_2_q), .en(comparator_16_eq), .clk(CLK_out), .Q(register_32_q));  // open: clr
  Comparator #(.width(16)) comparator_17 (.a(PC_q), .b(register_17_q), .eq(comparator_17_eq));  // open: gt, lt
  Register #(.width(16)) register_33 (
    .D(data_2_q), .en(comparator_17_eq), .clk(CLK_out), .Q(register_33_q));  // open: clr
  Comparator #(.mode("unsigned"), .width(6)) comparator_18 (
    .a(IR_q), .b({6{1'b0}}), .eq(comparator_18_eq));  // open: gt, lt
  assign IR_q_2[19] = comparator_19_eq ? comparator_19_eq : 1'bz;  // Controlled_Buffer controlled_buffer_3
  Comparator #(.mode("unsigned"), .width(6)) comparator_19 (
    .a(IR_q), .b(6'b000010), .eq(comparator_19_eq));  // open: gt, lt
  assign IR_q_2[13] = comparator_19_eq ? comparator_19_eq : 1'bz;  // Controlled_Buffer controlled_buffer_4
  assign IR_q_2[11] = comparator_20_eq ? comparator_20_eq : 1'bz;  // Controlled_Buffer controlled_buffer_5
  Comparator #(.mode("unsigned"), .width(6)) comparator_20 (
    .a(IR_q), .b(6'b001000), .eq(comparator_20_eq));  // open: gt, lt
  assign IR_q_2[14] = comparator_20_eq ? comparator_20_eq : 1'bz;  // Controlled_Buffer controlled_buffer_6
  assign IR_q_2[13] = comparator_20_eq ? comparator_20_eq : 1'bz;  // Controlled_Buffer controlled_buffer_7
  assign IR_q_2[11] = comparator_21_eq ? comparator_21_eq : 1'bz;  // Controlled_Buffer controlled_buffer_8
  Comparator #(.mode("unsigned"), .width(6)) comparator_21 (
    .a(IR_q), .b(6'b001001), .eq(comparator_21_eq));  // open: gt, lt
  assign IR_q_2[15] = comparator_21_eq ? comparator_21_eq : 1'bz;  // Controlled_Buffer controlled_buffer_9
  assign IR_q_2[13] = comparator_21_eq ? comparator_21_eq : 1'bz;  // Controlled_Buffer controlled_buffer_10
  assign IR_q_2[11] = comparator_22_eq ? comparator_22_eq : 1'bz;  // Controlled_Buffer controlled_buffer_11
  Comparator #(.mode("unsigned"), .width(6)) comparator_22 (
    .a(IR_q), .b(6'b001010), .eq(comparator_22_eq));  // open: gt, lt
  assign IR_q_2[14] = comparator_22_eq ? comparator_22_eq : 1'bz;  // Controlled_Buffer controlled_buffer_12
  assign IR_q_2[15] = comparator_22_eq ? comparator_22_eq : 1'bz;  // Controlled_Buffer controlled_buffer_13
  assign IR_q_2[13] = comparator_22_eq ? comparator_22_eq : 1'bz;  // Controlled_Buffer controlled_buffer_14
  assign IR_q_2[11] = comparator_23_eq ? comparator_23_eq : 1'bz;  // Controlled_Buffer controlled_buffer_15
  Comparator #(.mode("unsigned"), .width(6)) comparator_23 (
    .a(IR_q), .b(6'b001100), .eq(comparator_23_eq));  // open: gt, lt
  assign IR_q_2[16] = comparator_23_eq ? comparator_23_eq : 1'bz;  // Controlled_Buffer controlled_buffer_16
  assign IR_q_2[13] = comparator_23_eq ? comparator_23_eq : 1'bz;  // Controlled_Buffer controlled_buffer_17
  assign IR_q_2[11] = comparator_24_eq ? comparator_24_eq : 1'bz;  // Controlled_Buffer controlled_buffer_18
  Comparator #(.mode("unsigned"), .width(6)) comparator_24 (
    .a(IR_q), .b(6'b001101), .eq(comparator_24_eq));  // open: gt, lt
  assign IR_q_2[14] = comparator_24_eq ? comparator_24_eq : 1'bz;  // Controlled_Buffer controlled_buffer_19
  assign IR_q_2[16] = comparator_24_eq ? comparator_24_eq : 1'bz;  // Controlled_Buffer controlled_buffer_20
  assign IR_q_2[13] = comparator_24_eq ? comparator_24_eq : 1'bz;  // Controlled_Buffer controlled_buffer_21
  Comparator #(.mode("unsigned"), .width(6)) comparator_25 (
    .a(IR_q), .b(6'b001110), .eq(comparator_25_eq));  // open: gt, lt
  Comparator #(.mode("unsigned"), .width(6)) comparator_26 (
    .a(IR_q), .b(6'b001111), .eq(comparator_26_eq));  // open: gt, lt
  assign IR_q_2[11] = comparator_27_eq ? comparator_27_eq : 1'bz;  // Controlled_Buffer controlled_buffer_22
  Comparator #(.mode("unsigned"), .width(6)) comparator_27 (
    .a(IR_q), .b(6'b000011), .eq(comparator_27_eq));  // open: gt, lt
  assign IR_q_2[14] = comparator_27_eq ? comparator_27_eq : 1'bz;  // Controlled_Buffer controlled_buffer_23
  assign IR_q_2[15] = comparator_27_eq ? comparator_27_eq : 1'bz;  // Controlled_Buffer controlled_buffer_24
  assign IR_q_2[16] = comparator_27_eq ? comparator_27_eq : 1'bz;  // Controlled_Buffer controlled_buffer_25
  assign IR_q_2[13] = comparator_27_eq ? comparator_27_eq : 1'bz;  // Controlled_Buffer controlled_buffer_26
  assign IR_q_2[11] = comparator_28_eq ? comparator_28_eq : 1'bz;  // Controlled_Buffer controlled_buffer_27
  Comparator #(.mode("unsigned"), .width(6)) comparator_28 (
    .a(IR_q), .b(6'b000100), .eq(comparator_28_eq));  // open: gt, lt
  assign IR_q_2[17] = comparator_28_eq ? comparator_28_eq : 1'bz;  // Controlled_Buffer controlled_buffer_28
  assign IR_q_2[13] = comparator_28_eq ? comparator_28_eq : 1'bz;  // Controlled_Buffer controlled_buffer_29
  assign IR_q_2[11] = comparator_29_eq ? comparator_29_eq : 1'bz;  // Controlled_Buffer controlled_buffer_30
  Comparator #(.mode("unsigned"), .width(6)) comparator_29 (
    .a(IR_q), .b(6'b000101), .eq(comparator_29_eq));  // open: gt, lt
  assign IR_q_2[14] = comparator_29_eq ? comparator_29_eq : 1'bz;  // Controlled_Buffer controlled_buffer_31
  assign IR_q_2[17] = comparator_29_eq ? comparator_29_eq : 1'bz;  // Controlled_Buffer controlled_buffer_32
  assign IR_q_2[13] = comparator_29_eq ? comparator_29_eq : 1'bz;  // Controlled_Buffer controlled_buffer_33
  Comparator #(.mode("unsigned"), .width(6)) comparator_30 (
    .a(IR_q), .b(6'b000110), .eq(comparator_30_eq));  // open: gt, lt
  Comparator #(.mode("unsigned"), .width(6)) comparator_31 (
    .a(IR_q), .b(6'b000111), .eq(comparator_31_eq));  // open: gt, lt
  and and_20 (and_20_out, ~IR_q[13], IR_q[14], ~IR_q[15]);  // AND_Gate
  Comparator #(.mode("unsigned"), .width(6)) comparator_32 (
    .a(IR_q), .b(6'b011100), .eq(comparator_32_eq));  // open: gt, lt
  Comparator #(.mode("unsigned"), .width(5)) comparator_33 (
    .a(IR_q_2[4:0]), .b({5{1'b0}}), .eq(comparator_33_eq));  // open: gt, lt
  Comparator #(.mode("unsigned"), .width(5)) comparator_34 (
    .a(IR_q_2[4:0]), .b(5'b00001), .eq(comparator_34_eq));  // open: gt, lt
  Comparator #(.mode("unsigned"), .width(5)) comparator_35 (
    .a(IR_q_2[4:0]), .b(5'b00010), .eq(comparator_35_eq));  // open: gt, lt
  Comparator #(.mode("unsigned"), .width(5)) comparator_36 (
    .a(IR_q_2[4:0]), .b(5'b00011), .eq(comparator_36_eq));  // open: gt, lt
  Comparator #(.mode("unsigned"), .width(5)) comparator_37 (
    .a(IR_q_2[4:0]), .b(5'b01000), .eq(comparator_37_eq));  // open: gt, lt
  Comparator #(.mode("unsigned"), .width(5)) comparator_38 (
    .a(IR_q_2[4:0]), .b(5'b01001), .eq(comparator_38_eq));  // open: gt, lt
  Comparator #(.mode("unsigned"), .width(5)) comparator_39 (
    .a(IR_q_2[4:0]), .b(5'b00100), .eq(comparator_39_eq));  // open: gt, lt
  Comparator #(.mode("unsigned"), .width(5)) comparator_40 (
    .a(IR_q_2[4:0]), .b(5'b00101), .eq(comparator_40_eq));  // open: gt, lt
  Comparator #(.mode("unsigned"), .width(5)) comparator_41 (
    .a(IR_q_2[4:0]), .b(5'b00110), .eq(comparator_41_eq));  // open: gt, lt
  Comparator #(.mode("unsigned"), .width(5)) comparator_42 (
    .a(IR_q_2[4:0]), .b(5'b00111), .eq(comparator_42_eq));  // open: gt, lt
  Pull_Resistor pull_resistor_6 (.node(pull_resistor_6_node));
  not not_2 (not_2_out, pull_resistor_6_node);
  assign pull_resistor_6_node = comparator_2_eq ? comparator_2_eq : 1'bz;  // Controlled_Buffer controlled_buffer_34
  assign controlled_buffer_35_out = comparator_2_eq ? register_18_q : 16'bz;  // Controlled_Buffer controlled_buffer_35
  assign controlled_buffer_36_out = comparator_2_eq ? counter_3_q[1] : 1'bz;  // Controlled_Buffer controlled_buffer_36
  assign pull_resistor_6_node = comparator_3_eq ? comparator_3_eq : 1'bz;  // Controlled_Buffer controlled_buffer_37
  assign controlled_buffer_35_out = comparator_3_eq ? register_19_q : 16'bz;  // Controlled_Buffer controlled_buffer_38
  assign controlled_buffer_39_out = comparator_3_eq ? counter_4_q[1] : 1'bz;  // Controlled_Buffer controlled_buffer_39
  assign pull_resistor_6_node = comparator_4_eq ? comparator_4_eq : 1'bz;  // Controlled_Buffer controlled_buffer_40
  assign controlled_buffer_35_out = comparator_4_eq ? register_20_q : 16'bz;  // Controlled_Buffer controlled_buffer_41
  assign controlled_buffer_39_out = comparator_4_eq ? counter_5_q[1] : 1'bz;  // Controlled_Buffer controlled_buffer_42
  assign pull_resistor_6_node = comparator_5_eq ? comparator_5_eq : 1'bz;  // Controlled_Buffer controlled_buffer_43
  assign controlled_buffer_35_out = comparator_5_eq ? register_21_q : 16'bz;  // Controlled_Buffer controlled_buffer_44
  assign controlled_buffer_39_out = comparator_5_eq ? counter_6_q[1] : 1'bz;  // Controlled_Buffer controlled_buffer_45
  assign pull_resistor_6_node = comparator_6_eq ? comparator_6_eq : 1'bz;  // Controlled_Buffer controlled_buffer_46
  assign controlled_buffer_35_out = comparator_6_eq ? register_22_q : 16'bz;  // Controlled_Buffer controlled_buffer_47
  assign controlled_buffer_39_out = comparator_6_eq ? counter_7_q[1] : 1'bz;  // Controlled_Buffer controlled_buffer_48
  assign pull_resistor_6_node = comparator_7_eq ? comparator_7_eq : 1'bz;  // Controlled_Buffer controlled_buffer_49
  assign controlled_buffer_35_out = comparator_7_eq ? register_23_q : 16'bz;  // Controlled_Buffer controlled_buffer_50
  assign controlled_buffer_39_out = comparator_7_eq ? counter_8_q[1] : 1'bz;  // Controlled_Buffer controlled_buffer_51
  assign pull_resistor_6_node = comparator_8_eq ? comparator_8_eq : 1'bz;  // Controlled_Buffer controlled_buffer_52
  assign controlled_buffer_35_out = comparator_8_eq ? register_24_q : 16'bz;  // Controlled_Buffer controlled_buffer_53
  assign controlled_buffer_39_out = comparator_8_eq ? counter_9_q[1] : 1'bz;  // Controlled_Buffer controlled_buffer_54
  assign pull_resistor_6_node = comparator_9_eq ? comparator_9_eq : 1'bz;  // Controlled_Buffer controlled_buffer_55
  assign controlled_buffer_35_out = comparator_9_eq ? register_25_q : 16'bz;  // Controlled_Buffer controlled_buffer_56
  assign controlled_buffer_39_out = comparator_9_eq ? counter_10_q[1] : 1'bz;  // Controlled_Buffer controlled_buffer_57
  assign pull_resistor_6_node = comparator_10_eq ? comparator_10_eq : 1'bz;  // Controlled_Buffer controlled_buffer_58
  assign controlled_buffer_35_out = comparator_10_eq ? register_26_q : 16'bz;  // Controlled_Buffer controlled_buffer_59
  assign controlled_buffer_39_out = comparator_10_eq ? counter_11_q[1] : 1'bz;  // Controlled_Buffer controlled_buffer_60
  assign pull_resistor_6_node = comparator_11_eq ? comparator_11_eq : 1'bz;  // Controlled_Buffer controlled_buffer_61
  assign controlled_buffer_35_out = comparator_11_eq ? register_27_q : 16'bz;  // Controlled_Buffer controlled_buffer_62
  assign controlled_buffer_39_out = comparator_11_eq ? counter_12_q[1] : 1'bz;  // Controlled_Buffer controlled_buffer_63
  assign pull_resistor_6_node = comparator_12_eq ? comparator_12_eq : 1'bz;  // Controlled_Buffer controlled_buffer_64
  assign controlled_buffer_35_out = comparator_12_eq ? register_28_q : 16'bz;  // Controlled_Buffer controlled_buffer_65
  assign controlled_buffer_39_out = comparator_12_eq ? counter_13_q[1] : 1'bz;  // Controlled_Buffer controlled_buffer_66
  assign pull_resistor_6_node = comparator_13_eq ? comparator_13_eq : 1'bz;  // Controlled_Buffer controlled_buffer_67
  assign controlled_buffer_35_out = comparator_13_eq ? register_29_q : 16'bz;  // Controlled_Buffer controlled_buffer_68
  assign controlled_buffer_39_out = comparator_13_eq ? counter_14_q[1] : 1'bz;  // Controlled_Buffer controlled_buffer_69
  assign pull_resistor_6_node = comparator_14_eq ? comparator_14_eq : 1'bz;  // Controlled_Buffer controlled_buffer_70
  assign controlled_buffer_35_out = comparator_14_eq ? register_30_q : 16'bz;  // Controlled_Buffer controlled_buffer_71
  assign controlled_buffer_39_out = comparator_14_eq ? counter_15_q[1] : 1'bz;  // Controlled_Buffer controlled_buffer_72
  assign pull_resistor_6_node = comparator_15_eq ? comparator_15_eq : 1'bz;  // Controlled_Buffer controlled_buffer_73
  assign controlled_buffer_35_out = comparator_15_eq ? register_31_q : 16'bz;  // Controlled_Buffer controlled_buffer_74
  assign controlled_buffer_39_out = comparator_15_eq ? counter_16_q[1] : 1'bz;  // Controlled_Buffer controlled_buffer_75
  assign pull_resistor_6_node = comparator_16_eq ? comparator_16_eq : 1'bz;  // Controlled_Buffer controlled_buffer_76
  assign controlled_buffer_35_out = comparator_16_eq ? register_32_q : 16'bz;  // Controlled_Buffer controlled_buffer_77
  assign controlled_buffer_39_out = comparator_16_eq ? counter_17_q[1] : 1'bz;  // Controlled_Buffer controlled_buffer_78
  assign pull_resistor_6_node = comparator_17_eq ? comparator_17_eq : 1'bz;  // Controlled_Buffer controlled_buffer_79
  assign controlled_buffer_35_out = comparator_17_eq ? register_33_q : 16'bz;  // Controlled_Buffer controlled_buffer_80
  assign controlled_buffer_39_out = comparator_17_eq ? counter_18_q[1] : 1'bz;  // Controlled_Buffer controlled_buffer_81
  Comparator #(.mode("unsigned"), .width(5)) comparator_43 (
    .a(IR_q_2[4:0]), .b(IR_q_2[9:5]), .eq(comparator_43_eq));  // open: gt, lt
  or or_16 (or_16_out, comparator_47_eq, IR_q_2[21]);
  Comparator #(.mode("unsigned"), .width(5)) comparator_44 (
    .a(IR_q_2[4:0]), .b(5'b11110), .eq(comparator_44_eq));  // open: gt, lt
  and and_21 (and_21_out, comparator_43_eq, comparator_18_eq);
  and and_22 (IR_q_2[12], ~comparator_43_eq, comparator_18_eq);  // AND_Gate
  or or_17 (or_17_out, comparator_25_eq, comparator_26_eq);
  assign IR_q_2[11] = or_17_out ? or_17_out : 1'bz;  // Controlled_Buffer controlled_buffer_82
  assign IR_q_2[15] = or_17_out ? or_17_out : 1'bz;  // Controlled_Buffer controlled_buffer_83
  assign IR_q_2[16] = or_17_out ? or_17_out : 1'bz;  // Controlled_Buffer controlled_buffer_84
  assign IR_q_2[13] = or_17_out ? or_17_out : 1'bz;  // Controlled_Buffer controlled_buffer_85
  or or_18 (or_18_out, comparator_30_eq, comparator_31_eq);
  assign IR_q_2[11] = or_18_out ? or_18_out : 1'bz;  // Controlled_Buffer controlled_buffer_86
  assign IR_q_2[15] = or_18_out ? or_18_out : 1'bz;  // Controlled_Buffer controlled_buffer_87
  assign IR_q_2[17] = or_18_out ? or_18_out : 1'bz;  // Controlled_Buffer controlled_buffer_88
  assign IR_q_2[14] = comparator_31_eq ? comparator_31_eq : 1'bz;  // Controlled_Buffer controlled_buffer_89
  assign IR_q_2[14] = and_20_out ? IR_q[11] : 1'bz;  // Controlled_Buffer controlled_buffer_90
  assign IR_q_2[15] = and_20_out ? IR_q[12] : 1'bz;  // Controlled_Buffer controlled_buffer_91
  assign IR_q_2[11] = and_20_out ? and_20_out : 1'bz;  // Controlled_Buffer controlled_buffer_92
  assign IR_q_2[16] = and_20_out ? and_20_out : 1'bz;  // Controlled_Buffer controlled_buffer_93
  assign IR_q_2[17] = and_20_out ? and_20_out : 1'bz;  // Controlled_Buffer controlled_buffer_94
  assign IR_q_2[18] = and_23_out ? comparator_32_eq : 1'bz;  // Controlled_Buffer controlled_buffer_95
  and and_23 (and_23_out, comparator_32_eq, ~or_19_out);  // AND_Gate
  assign IR_q_2[11] = and_24_out ? and_24_out : 1'bz;  // Controlled_Buffer controlled_buffer_96
  and and_24 (and_24_out, comparator_33_eq, comparator_32_eq);
  assign IR_q_2[14] = and_24_out ? and_24_out : 1'bz;  // Controlled_Buffer controlled_buffer_97
  assign IR_q_2[11] = and_25_out ? and_25_out : 1'bz;  // Controlled_Buffer controlled_buffer_98
  and and_25 (and_25_out, comparator_34_eq, comparator_32_eq);
  assign IR_q_2[15] = and_25_out ? and_25_out : 1'bz;  // Controlled_Buffer controlled_buffer_99
  assign IR_q_2[11] = and_26_out ? and_26_out : 1'bz;  // Controlled_Buffer controlled_buffer_100
  and and_26 (and_26_out, comparator_35_eq, comparator_32_eq);
  assign IR_q_2[14] = and_26_out ? and_26_out : 1'bz;  // Controlled_Buffer controlled_buffer_101
  assign IR_q_2[15] = and_26_out ? and_26_out : 1'bz;  // Controlled_Buffer controlled_buffer_102
  assign IR_q_2[11] = and_27_out ? and_27_out : 1'bz;  // Controlled_Buffer controlled_buffer_103
  and and_27 (and_27_out, comparator_36_eq, comparator_32_eq);
  assign IR_q_2[16] = and_27_out ? and_27_out : 1'bz;  // Controlled_Buffer controlled_buffer_104
  and and_28 (and_28_out, comparator_37_eq, comparator_32_eq);
  and and_29 (and_29_out, comparator_38_eq, comparator_32_eq);
  assign IR_q_2[11] = and_29_out ? and_29_out : 1'bz;  // Controlled_Buffer controlled_buffer_105
  assign IR_q_2[16] = and_29_out ? and_29_out : 1'bz;  // Controlled_Buffer controlled_buffer_106
  assign IR_q_2[15] = and_29_out ? and_29_out : 1'bz;  // Controlled_Buffer controlled_buffer_107
  and and_30 (and_30_out, comparator_39_eq, comparator_32_eq);
  and and_31 (and_31_out, comparator_40_eq, comparator_32_eq);
  and and_32 (and_32_out, comparator_41_eq, comparator_32_eq);
  and and_33 (and_33_out, comparator_42_eq, comparator_32_eq);
  Pull_Resistor pull_resistor_7 (.node(controlled_buffer_36_out));
  not not_3 (not_3_out, or_23_out);
  Comparator #(.mode("unsigned"), .width(5)) comparator_45 (
    .a(5'b11100), .b(IR_q_2[9:5]), .eq(comparator_45_eq));  // open: gt, lt
  Comparator #(.mode("unsigned"), .width(5)) comparator_46 (
    .a(IR_q_2[9:5]), .b(5'b11110), .eq(comparator_46_eq));  // open: gt, lt
  Comparator #(.mode("unsigned"), .width(5)) comparator_47 (
    .a(IR_q_2[9:5]), .b({5{1'b1}}), .eq(comparator_47_eq));  // open: gt, lt
  not not_4 (IR_q_2[10], and_21_out);
  or or_19 (or_19_out, and_30_out, and_32_out);
  or or_20 (IR_q_2[20], and_30_out, and_31_out);
  or or_21 (or_21_out, and_31_out, and_33_out);
  or or_22 (IR_q_2[21], and_32_out, and_33_out);
  or or_23 (or_23_out, comparator_46_eq, comparator_47_eq, IR_q_2[19]);
  assign IR_q_2[16] = or_21_out ? or_21_out : 1'bz;  // Controlled_Buffer controlled_buffer_108
  assign IR_q_2[17] = or_21_out ? or_21_out : 1'bz;  // Controlled_Buffer controlled_buffer_109
  and and_34 (and_34_out, comparator_44_eq, IR_q_2[13]);
  assign controlled_buffer_110_out = or_23_out ? Data_in : 16'bz;  // Controlled_Buffer controlled_buffer_110
  Multiplexer #(.width(16)) multiplexer_3 (
    .in0(controlled_buffer_110_out), .in1(PC_q), .out(multiplexer_3_out), .sel(or_25_out));
  or or_24 (or_24_out, and_35_out, or_23_out);
  or or_25 (or_25_out, and_34_out, and_28_out, and_35_out);
  and and_35 (and_35_out, comparator_45_eq, IR_q_2[20]);
  Pull_Resistor pull_resistor_8 (.node(pull_resistor_8_node));
  Register #(.width(16)) register_34 (
    .D(multiplexer_3_out), .en(or_24_out), .clk(CLK_out), .Q(register_34_q));  // open: clr
  Register #(.width(22)) READ_stage (.D(IR_q_2), .en(nand_1_out), .clk(CLK_out), .Q(READ_stage_q));  // open: clr
  Pull_Resistor pull_resistor_9 (.node(IR_q_2));
  or or_26 (or_26_out, controlled_buffer_36_out, decoder_10_out0);
  Comparator #(.mode("unsigned"), .width(16)) comparator_48 (
    .a(T0_q), .b(pull_resistor_8_node), .gt(comparator_48_gt));  // open: eq, lt
  Comparator #(.mode("unsigned"), .width(16)) comparator_49 (
    .a(T1_q), .b(pull_resistor_8_node), .gt(comparator_49_gt));  // open: eq, lt
  and and_36 (and_36_out, decoder_9_out0, and_28_out);
  and and_37 (and_37_out, decoder_8_out3, and_28_out);
  D_Flip_Flop d_ff_1 (.D(and_38_out), .clk(CLK_out), .Q(d_ff_1_q));  // open: Qn, preset, reset
  and and_38 (and_38_out, ~or_39_out[13], comparator_48_gt);  // AND_Gate
  D_Flip_Flop d_ff_2 (.D(and_39_out), .clk(CLK_out), .Q(d_ff_2_q));  // open: Qn, preset, reset
  and and_39 (and_39_out, ~or_39_out[12], comparator_49_gt);  // AND_Gate
  and and_40 (and_40_out, READ_stage_q[16], READ_stage_q[17], READ_stage_q[18]);
  S_R_Flip_Flop s_r_ff_1 (
    .S(decoder_9_out0), .R(and_36_out), .clk(CLK_out), .Q(s_r_ff_1_q));  // open: reset, Qn, preset
  S_R_Flip_Flop s_r_ff_2 (
    .S(decoder_8_out3), .R(and_37_out), .clk(CLK_out), .Q(s_r_ff_2_q));  // open: reset, Qn, preset
  or or_27 (or_27_out, READ_stage_q[20], READ_stage_q[19], READ_stage_q[21]);
  Decoder #(.select(3)) decoder_2 (
    .out0(decoder_2_out0), .out1(decoder_2_out1), .out2(decoder_2_out2), .out3(decoder_2_out3),
    .out4(decoder_2_out4), .out5(decoder_2_out5), .out6(decoder_2_out6), .out7(decoder_2_out7),
    .sel(controlled_buffer_111_out_2), .en(and_55_out));
  Comparator #(.mode("unsigned"), .width(5)) comparator_50 (
    .a(5'b11100), .b(READ_stage_q[9:5]), .eq(comparator_50_eq));  // open: gt, lt
  Comparator #(.mode("unsigned"), .width(5)) comparator_51 (
    .a(READ_stage_q[4:0]), .b({5{1'b1}}), .eq(comparator_51_eq), .lt(comparator_51_lt));  // open: gt
  Comparator #(.mode("unsigned"), .width(5)) comparator_52 (
    .a(READ_stage_q[9:5]), .b(5'b11110), .eq(comparator_52_eq), .lt(comparator_52_lt));  // open: gt
  Comparator #(.mode("unsigned"), .width(5)) comparator_53 (
    .a(READ_stage_q[9:5]), .b({5{1'b1}}), .eq(comparator_53_eq), .lt(comparator_53_lt));  // open: gt
  and and_41 (and_41_out, READ_stage_q[10], READ_stage_q[11]);
  and and_42 (and_42_out, READ_stage_q[10], READ_stage_q[12]);
  or or_28 (or_28_out, or_39_out[14], or_39_out[12]);
  or or_29 (or_29_out, or_39_out[15], or_39_out[13]);
  Comparator #(.mode("unsigned"), .width(5)) comparator_54 (
    .a(READ_stage_q[9:5]), .b(5'b10111), .eq(comparator_54_eq));  // open: gt, lt
  Comparator #(.mode("unsigned"), .width(5)) comparator_55 (
    .a(READ_stage_q[9:5]), .b(5'b11000), .eq(comparator_55_eq));  // open: gt, lt
  Decoder #(.select(2)) decoder_3 (
    .out0(decoder_3_out0), .out1(decoder_3_out1), .out2(decoder_3_out2), .out3(decoder_3_out3),
    .sel(controlled_buffer_111_out), .en(decoder_2_out0));
  Decoder #(.select(2)) decoder_4 (
    .out0(decoder_4_out0), .out1(decoder_4_out1), .out2(decoder_4_out2), .out3(decoder_4_out3),
    .sel(controlled_buffer_111_out), .en(decoder_2_out1));
  Decoder #(.select(2)) decoder_5 (
    .out0(decoder_5_out0), .out1(decoder_5_out1), .out2(decoder_5_out2), .out3(decoder_5_out3),
    .sel(controlled_buffer_111_out), .en(decoder_2_out2));
  Decoder #(.select(2)) decoder_6 (
    .out0(decoder_6_out0), .out1(decoder_6_out1), .out2(decoder_6_out2), .out3(decoder_6_out3),
    .sel(controlled_buffer_111_out), .en(decoder_2_out3));
  Decoder #(.select(2)) decoder_7 (
    .out0(decoder_7_out0), .out1(decoder_7_out1), .out2(decoder_7_out2), .out3(decoder_7_out3),
    .sel(controlled_buffer_111_out), .en(decoder_2_out4));
  Decoder #(.select(2)) decoder_8 (
    .out0(decoder_8_out0), .out1(decoder_8_out1), .out2(decoder_8_out2), .out3(decoder_8_out3),
    .sel(controlled_buffer_111_out), .en(decoder_2_out5));
  Decoder #(.select(2)) decoder_9 (
    .out0(decoder_9_out0), .out1(decoder_9_out1), .out2(decoder_9_out2), .out3(decoder_9_out3),
    .sel(controlled_buffer_111_out), .en(decoder_2_out6));
  Decoder #(.select(2)) decoder_10 (
    .out0(decoder_10_out0), .out1(decoder_10_out1), .sel(controlled_buffer_111_out), .en(decoder_2_out7));  // open: out2, out3
  and and_43 (and_43_out, or_39_out[12], comparator_54_eq);
  and and_44 (and_44_out, or_39_out[13], comparator_55_eq);
  and and_45 (and_45_out, comparator_50_eq, READ_stage_q[20]);
  Register #(.width(16)) r0 (.D(multiplexer_38_out), .en(decoder_3_out0), .clk(CLK_out), .Q(r0_q));  // open: clr
  Register #(.width(16)) r4 (.D(multiplexer_38_out), .en(decoder_4_out0), .clk(CLK_out), .Q(r4_q));  // open: clr
  Register #(.width(16)) r8 (.D(multiplexer_38_out), .en(decoder_5_out0), .clk(CLK_out), .Q(r8_q));  // open: clr
  Register #(.width(16)) r12 (.D(multiplexer_38_out), .en(decoder_6_out0), .clk(CLK_out), .Q(r12_q));  // open: clr
  Register #(.width(16)) r16 (.D(multiplexer_38_out), .en(decoder_7_out0), .clk(CLK_out), .Q(r16_q));  // open: clr
  Register #(.width(16)) r20 (.D(multiplexer_38_out), .en(decoder_8_out0), .clk(CLK_out), .Q(r20_q));  // open: clr
  Counter #(.max('hffff), .width(16)) T1 (
    .load(decoder_9_out0), .D(multiplexer_38_out), .count(or_30_out), .Q(T1_q), .carry(T1_carry),
    .up(or_29_out), .clk(CLK_out));  // open: clr
  or or_30 (or_30_out, decoder_9_out0, d_ff_2_q);
  Multiplexer #(.width(16)) multiplexer_4 (
    .in0(multiplexer_38_out), .in1(controlled_buffer_35_out), .out(multiplexer_4_out),
    .sel(controlled_buffer_36_out));
  Counter #(.max('hffff), .width(16)) PC (
    .load(or_26_out), .D(multiplexer_4_out), .count(or_31_out), .Q(PC_q), .up(not_5_out), .clk(CLK_out));  // open: carry, clr
  or or_31 (or_31_out, or_26_out, or_33_out);
  or or_32 (or_32_out, and_43_out, and_44_out);
  or or_33 (or_33_out, and_46_out, and_2_out);
  not not_5 (not_5_out, and_2_out);
  and and_46 (and_46_out, or_34_out, ~or_44_out);  // AND_Gate
  or or_34 (or_34_out, ~comparator_53_eq, nand_1_out);  // OR_Gate
  or or_35 (or_35_out, comparator_51_eq, READ_stage_q[21]);
  or or_36 (or_36_out, READ_stage_q[21], comparator_52_eq);
  Register #(.width(16)) register_35 (
    .D(multiplexer_38_out), .en(decoder_3_out1), .clk(CLK_out), .Q(register_35_q));  // open: clr
  Register #(.width(16)) register_36 (
    .D(multiplexer_38_out), .en(decoder_4_out1), .clk(CLK_out), .Q(register_36_q));  // open: clr
  Register #(.width(16)) register_37 (
    .D(multiplexer_38_out), .en(decoder_5_out1), .clk(CLK_out), .Q(register_37_q));  // open: clr
  Register #(.width(16)) register_38 (
    .D(multiplexer_38_out), .en(decoder_6_out1), .clk(CLK_out), .Q(register_38_q));  // open: clr
  Register #(.width(16)) register_39 (
    .D(multiplexer_38_out), .en(decoder_7_out1), .clk(CLK_out), .Q(register_39_q));  // open: clr
  Register #(.width(16)) r21 (.D(multiplexer_38_out), .en(decoder_8_out1), .clk(CLK_out), .Q(r21_q));  // open: clr
  or or_37 (or_37_out, decoder_9_out1, and_53_out);
  Register #(.width(16)) int_vec (
    .D(multiplexer_38_out), .en(decoder_10_out1), .clk(CLK_out), .Q(int_vec_q));  // open: clr
  and and_47 (and_47_out, ~or_39_out[13], s_r_ff_1_q, T1_carry);  // AND_Gate
  and and_48 (and_48_out, s_r_ff_2_q, T0_carry, ~or_39_out[12]);  // AND_Gate
  or or_38 (or_39_out[11], and_47_out, and_48_out);
  or or_39 (or_39_out[7], or_39_out[11], Interrupt);
  Pull_Resistor pull_resistor_10 (.node(pull_resistor_10_node));
  Counter #(.max('hffff), .width(16)) SP (
    .load(decoder_9_out1), .D(multiplexer_38_out), .count(or_37_out), .Q(SP_q), .up(and_52_out), .clk(CLK_out));  // open: carry, clr
  Multiplexer #(.enable("true"), .width(16)) multiplexer_5 (
    .in0(T1_q), .in1(T0_q), .out(multiplexer_5_out), .sel(and_43_out), .en(or_32_out));
  Register #(.width(16)) register_40 (
    .D(multiplexer_38_out), .en(decoder_3_out2), .clk(CLK_out), .Q(register_40_q));  // open: clr
  Register #(.width(16)) register_41 (
    .D(multiplexer_38_out), .en(decoder_4_out2), .clk(CLK_out), .Q(register_41_q));  // open: clr
  Register #(.width(16)) register_42 (
    .D(multiplexer_38_out), .en(decoder_5_out2), .clk(CLK_out), .Q(register_42_q));  // open: clr
  Register #(.width(16)) register_43 (
    .D(multiplexer_38_out), .en(decoder_6_out2), .clk(CLK_out), .Q(register_43_q));  // open: clr
  Register #(.width(16)) register_44 (
    .D(multiplexer_38_out), .en(decoder_7_out2), .clk(CLK_out), .Q(register_44_q));  // open: clr
  Register #(.width(16)) r22 (.D(multiplexer_38_out), .en(decoder_8_out2), .clk(CLK_out), .Q(r22_q));  // open: clr
  Counter #(.max('hffff), .width(16)) SSP (
    .load(decoder_9_out2), .D(multiplexer_38_out), .count(or_40_out), .Q(SSP_q), .up(and_50_out),
    .clk(CLK_out));  // open: carry, clr
  or or_40 (or_40_out, and_51_out, decoder_9_out2);
  or or_41 (or_41_out, Interrupt_maskable, or_39_out[8]);
  Multiplexer #(.width(16)) multiplexer_6 (.in0(PC_q), .in1(multiplexer_5_out), .out(address_out_t), .sel(or_32_out));
  Multiplexer #(.width(5)) multiplexer_7 (.in0(5'b11001), .in1(5'b11010), .out(multiplexer_7_out), .sel(and_40_out));
  Register #(.width(16)) register_45 (
    .D(multiplexer_38_out), .en(decoder_3_out3), .clk(CLK_out), .Q(register_45_q));  // open: clr
  Register #(.width(16)) register_46 (
    .D(multiplexer_38_out), .en(decoder_4_out3), .clk(CLK_out), .Q(register_46_q));  // open: clr
  Register #(.width(16)) register_47 (
    .D(multiplexer_38_out), .en(decoder_5_out3), .clk(CLK_out), .Q(register_47_q));  // open: clr
  Register #(.width(16)) register_48 (
    .D(multiplexer_38_out), .en(decoder_6_out3), .clk(CLK_out), .Q(register_48_q));  // open: clr
  Register #(.width(16)) register_49 (
    .D(multiplexer_38_out), .en(decoder_7_out3), .clk(CLK_out), .Q(register_49_q));  // open: clr
  Register #(.width(16)) ST_R (
    .D(multiplexer_8_out), .en(or_42_out), .clk(CLK_out),
    .Q({or_39_out[15:12], ST_R_q[11], or_39_out[10], ST_R_q[9:0]}));  // open: clr
  or or_42 (or_42_out, decoder_9_out3, or_44_out);
  Multiplexer #(.width(16)) multiplexer_8 (
    .in0(multiplexer_38_out), .in1(or_39_out), .out(multiplexer_8_out), .sel(or_44_out));
  Multiplexer #(.width(5)) multiplexer_9 (
    .in0(READ_stage_q[4:0]), .in1(multiplexer_7_out), .out(multiplexer_9_out), .sel(or_27_out));
  Counter #(.max('hffff), .width(16)) T0 (
    .load(decoder_8_out3), .D(multiplexer_38_out), .count(or_43_out), .Q(T0_q), .carry(T0_carry),
    .up(or_28_out), .clk(CLK_out));  // open: clr
  or or_43 (or_43_out, decoder_8_out3, d_ff_1_q);
  or or_44 (or_44_out, or_39_out[7], counter_2_carry, or_39_out[9]);
  Multiplexer #(.select(2), .width(16)) multiplexer_10 (
    .in0(r0_q), .in1(register_35_q), .in2(register_40_q), .in3(register_45_q), .out(multiplexer_10_out),
    .sel(READ_stage_q[6:5]));
  Multiplexer #(.select(2), .width(16)) multiplexer_11 (
    .in0(r0_q), .in1(register_35_q), .in2(register_40_q), .in3(register_45_q), .out(multiplexer_11_out),
    .sel(multiplexer_9_out[1:0]));
  Multiplexer #(.select(2), .width(16)) multiplexer_12 (
    .in0(r4_q), .in1(register_36_q), .in2(register_41_q), .in3(register_46_q), .out(multiplexer_12_out),
    .sel(READ_stage_q[6:5]));
  Multiplexer #(.select(2), .width(16)) multiplexer_13 (
    .in0(r4_q), .in1(register_36_q), .in2(register_41_q), .in3(register_46_q), .out(multiplexer_13_out),
    .sel(multiplexer_9_out[1:0]));
  Multiplexer #(.select(2), .width(16)) multiplexer_14 (
    .in0(r8_q), .in1(register_37_q), .in2(register_42_q), .in3(register_47_q), .out(multiplexer_14_out),
    .sel(READ_stage_q[6:5]));
  Multiplexer #(.select(2), .width(16)) multiplexer_15 (
    .in0(r8_q), .in1(register_37_q), .in2(register_42_q), .in3(register_47_q), .out(multiplexer_15_out),
    .sel(multiplexer_9_out[1:0]));
  Multiplexer #(.select(2), .width(16)) multiplexer_16 (
    .in0(r12_q), .in1(register_38_q), .in2(register_43_q), .in3(register_48_q), .out(multiplexer_16_out),
    .sel(READ_stage_q[6:5]));
  Multiplexer #(.select(2), .width(16)) multiplexer_17 (
    .in0(r12_q), .in1(register_38_q), .in2(register_43_q), .in3(register_48_q), .out(multiplexer_17_out),
    .sel(multiplexer_9_out[1:0]));
  Multiplexer #(.select(2), .width(16)) multiplexer_18 (
    .in0(r16_q), .in1(register_39_q), .in2(register_44_q), .in3(register_49_q), .out(multiplexer_18_out),
    .sel(READ_stage_q[6:5]));
  Multiplexer #(.select(2), .width(16)) multiplexer_19 (
    .in0(r16_q), .in1(register_39_q), .in2(register_44_q), .in3(register_49_q), .out(multiplexer_19_out),
    .sel(multiplexer_9_out[1:0]));
  Multiplexer #(.select(2), .width(16)) multiplexer_20 (
    .in0(r20_q), .in1(r21_q), .in2(r22_q), .in3(T0_q), .out(multiplexer_20_out), .sel(READ_stage_q[6:5]));
  Multiplexer #(.select(2), .width(16)) multiplexer_21 (
    .in0(r20_q), .in1(r21_q), .in2(r22_q), .in3(T0_q), .out(multiplexer_21_out), .sel(multiplexer_9_out[1:0]));
  Multiplexer #(.select(2), .width(16)) multiplexer_22 (
    .in0(T1_q), .in1(SP_q), .in2(SSP_q), .in3({or_39_out[15:12], ST_R_q[11], or_39_out[10], ST_R_q[9:0]}),
    .out(multiplexer_22_out), .sel(READ_stage_q[6:5]));
  Multiplexer #(.select(2), .width(16)) multiplexer_23 (
    .in0(T1_q), .in1(SP_q), .in2(SSP_q), .in3({or_39_out[15:12], ST_R_q[11], or_39_out[10], ST_R_q[9:0]}),
    .out(multiplexer_23_out), .sel(multiplexer_9_out[1:0]));
  Multiplexer #(.select(2), .width(16)) multiplexer_24 (
    .in0(PC_q), .in1(int_vec_q), .in2(undriven), .in3(Data_in), .out(multiplexer_24_out),
    .sel(READ_stage_q[6:5]));
  Multiplexer #(.select(2), .width(16)) multiplexer_25 (
    .in0(PC_q), .in1(int_vec_q), .in2(undriven), .in3(Data_in), .out(multiplexer_25_out),
    .sel(multiplexer_9_out[1:0]));
  and and_49 (or_39_out[9], or_39_out[10], or_41_out);
  Multiplexer #(.width(5)) multiplexer_26 (
    .in0(READ_stage_q[4:0]), .in1(READ_stage_q[9:5]), .out(multiplexer_26_out), .sel(or_45_out));
  or or_45 (or_45_out, READ_stage_q[21], and_41_out);
  or or_46 (or_46_out[11], and_41_out, READ_stage_q[21], and_42_out);
  and and_50 (and_50_out, and_40_out, READ_stage_q[20]);
  and and_51 (and_51_out, and_40_out, or_27_out);
  and and_52 (and_52_out, ~and_40_out, READ_stage_q[20]);  // AND_Gate
  and and_53 (and_53_out, ~and_40_out, or_27_out);  // AND_Gate
  Multiplexer #(.width(6)) multiplexer_27 (.in0(ST_R_q[6:1]), .in1(or_64_out), .out(or_39_out[6:1]), .sel(or_47_out));
  or or_47 (or_47_out, and_60_out, or_66_out);
  and and_54 (and_54_out, and_28_out, ~not_7_out);  // AND_Gate
  not not_6 (not_6_out, and_28_out);
  not not_7 (not_7_out, not_6_out);
  Multiplexer #(.width(16)) multiplexer_28 (
    .in0(register_34_q), .in1(multiplexer_29_out), .out(multiplexer_28_out), .sel(READ_stage_q[21]));
  not not_8 (not_8_out, or_36_out);
  Multiplexer #(.width(16)) multiplexer_29 (
    .in0(multiplexer_30_out), .in1(multiplexer_37_out), .out(multiplexer_29_out), .sel(pull_resistor_10_node));
  Multiplexer #(.width(16)) multiplexer_30 (
    .in0(multiplexer_31_out), .in1(multiplexer_38_out), .out(multiplexer_30_out), .sel(comparator_56_eq));
  Comparator #(.mode("unsigned"), .width(5)) comparator_56 (
    .a(multiplexer_9_out), .b({controlled_buffer_111_out_2, controlled_buffer_111_out}), .eq(comparator_56_eq));  // open: gt, lt
  Multiplexer #(.select(3), .width(16)) multiplexer_31 (
    .in0(multiplexer_11_out), .in1(multiplexer_13_out), .in2(multiplexer_15_out), .in3(multiplexer_17_out),
    .in4(multiplexer_19_out), .in5(multiplexer_21_out), .in6(multiplexer_23_out), .in7(multiplexer_25_out),
    .out(multiplexer_31_out), .sel(multiplexer_9_out[4:2]));
  S_R_Flip_Flop s_r_ff_3 (
    .S(1'b0), .R(counter_2_carry), .clk(CLK_out), .Q(or_39_out[8]), .preset(and_54_out));  // open: reset, Qn
  Multiplexer #(.width(16)) multiplexer_32 (
    .in0(address_out_t), .in1(multiplexer_28_out), .out(multiplexer_32_out), .sel(or_35_out));
  Multiplexer #(.width(16)) multiplexer_33 (
    .in0(register_34_q), .in1(multiplexer_29_out), .out(multiplexer_33_out), .sel(not_8_out));
  Comparator #(.mode("unsigned"), .width(5)) comparator_57 (
    .a(READ_stage_q[9:5]), .b({controlled_buffer_111_out_2, controlled_buffer_111_out}), .eq(comparator_57_eq));  // open: gt, lt
  Multiplexer #(.select(3), .width(16)) multiplexer_34 (
    .in0(multiplexer_10_out), .in1(multiplexer_12_out), .in2(multiplexer_14_out), .in3(multiplexer_16_out),
    .in4(multiplexer_18_out), .in5(multiplexer_20_out), .in6(multiplexer_22_out), .in7(multiplexer_24_out),
    .out(multiplexer_34_out), .sel(READ_stage_q[9:7]));
  Multiplexer multiplexer_35 (.in0(ST_R_q[0]), .in1(or_62_out[0]), .out(or_39_out[0]), .sel(and_60_out));
  Multiplexer #(.width(16)) multiplexer_36 (
    .in0(multiplexer_37_out), .in1(register_34_q), .out(multiplexer_36_out), .sel(and_45_out));
  Multiplexer #(.width(16)) multiplexer_37 (
    .in0(multiplexer_34_out), .in1(multiplexer_38_out), .out(multiplexer_37_out), .sel(comparator_57_eq));
  Register #(.width(16)) data_1 (.D(multiplexer_33_out), .en(CLK_out), .clk(CLK_out), .Q(data_1_q));  // open: clr
  Register #(.width(16)) data_2 (.D(multiplexer_36_out), .en(CLK_out), .clk(CLK_out), .Q(data_2_q));  // open: clr
  Register #(.width(15)) EXECUTE_stage (
    .D({ST_R_q[0], READ_stage_q[20:19], or_46_out[11], multiplexer_26_out, READ_stage_q[18:14], READ_stage_q[10]}),
    .en(CLK_out), .clk(CLK_out), .Q(EXECUTE_stage_q));  // open: clr
  and and_55 (and_55_out, and_56_out, comparator_58_lt);
  and and_56 (and_56_out, EXECUTE_stage_q[11], EXECUTE_stage_q[0]);
  Multiplexer #(.width(16)) multiplexer_38 (
    .in0(data_1_q), .in1({or_64_out[3], controlled_buffer_114_out, or_64_out[4]}), .out(multiplexer_38_out),
    .sel(or_48_out));
  assign {controlled_buffer_111_out_2, controlled_buffer_111_out} = EXECUTE_stage_q[0] ? EXECUTE_stage_q[10:6] : 5'bz;  // Controlled_Buffer controlled_buffer_111
  or or_48 (or_48_out, and_57_out, ~decoder_11_out0);  // OR_Gate
  Pull_Resistor #(.pull(1)) pull_resistor_11 (.node({controlled_buffer_111_out_2, controlled_buffer_111_out}));
  Comparator #(.mode("unsigned"), .width(5)) comparator_58 (
    .a({controlled_buffer_111_out_2, controlled_buffer_111_out}), .b(5'b11110), .lt(comparator_58_lt));  // open: gt, eq
  Comparator #(.mode("unsigned"), .width(5)) comparator_59 (
    .a(EXECUTE_stage_q[10:6]), .b(5'b11110), .eq(comparator_59_eq));  // open: gt, lt
  Comparator #(.mode("unsigned"), .width(5)) comparator_60 (
    .a(EXECUTE_stage_q[10:6]), .b({5{1'b1}}), .eq(comparator_60_eq));  // open: gt, lt
  Decoder #(.select(5)) decoder_11 (
    .out0(decoder_11_out0), .out1(decoder_11_out1), .out2(decoder_11_out2), .out3(decoder_11_out3),
    .out4(decoder_11_out4), .out5(decoder_11_out5), .out6(decoder_11_out6), .out7(decoder_11_out7),
    .out8(decoder_11_out8), .out9(decoder_11_out9), .out10(decoder_11_out10), .out11(decoder_11_out11),
    .out12(decoder_11_out12), .out13(decoder_11_out13), .out14(decoder_11_out14), .out15(decoder_11_out15),
    .out16(decoder_11_out16), .out18(decoder_11_out18), .out19(decoder_11_out19), .out20(decoder_11_out20),
    .out22(decoder_11_out22), .sel(EXECUTE_stage_q[5:1]), .en(EXECUTE_stage_q[0]));  // open: out17, out21, out23, out24, out25, out26, out27, out28, out29, out30, out31
  or or_49 (or_49_out, comparator_59_eq, comparator_60_eq, EXECUTE_stage_q[13]);
  and and_57 (and_57_out, and_56_out, or_50_out);
  Comparator #(.mode("unsigned"), .width(5)) comparator_61 (
    .a({controlled_buffer_111_out_2, controlled_buffer_111_out}), .b(5'b11001), .eq(comparator_61_eq));  // open: gt, lt
  Comparator #(.mode("unsigned"), .width(5)) comparator_62 (
    .a(5'b11010), .b({controlled_buffer_111_out_2, controlled_buffer_111_out}), .eq(comparator_62_eq));  // open: gt, lt
  Pull_Resistor #(.pull(1)) pull_resistor_12 (.node(pull_resistor_12_node));
  not not_9 (not_9_out, ST_R_q[6]);
  not not_10 (not_10_out, ST_R_q[1]);
  Multiplexer #(.select(4)) multiplexer_39 (
    .in0(pull_resistor_12_node), .in1(ST_R_q[0]), .in2(pull_resistor_13_node), .in3(ST_R_q[6]),
    .in4(not_9_out), .in5(ST_R_q[1]), .in6(not_10_out), .in7(ST_R_q[2]), .in8(ST_R_q[3]), .in9(ST_R_q[4]),
    .in10(not_11_out), .in11(not_12_out), .in12(ST_R_q[5]), .in13(pull_resistor_13_node),
    .in14(pull_resistor_13_node), .in15(pull_resistor_13_node), .out(not_1_out[1]), .sel(EXECUTE_stage_q[4:1]));
  not not_11 (not_11_out, ST_R_q[4]);
  not not_12 (not_12_out, ST_R_q[5]);
  Pull_Resistor pull_resistor_13 (.node(pull_resistor_13_node));
  or or_50 (or_50_out, comparator_61_eq, comparator_62_eq);
  or or_51 (or_51_out, decoder_11_out19, EXECUTE_stage_q[13]);
  or or_52 (or_52_out, decoder_11_out1, EXECUTE_stage_q[13]);
  not not_13 (not_13_out, or_51_out);
  assign controlled_buffer_112_out = not_13_out ? data_2_q : 16'bz;  // Controlled_Buffer controlled_buffer_112
  or or_53 (or_53_out, and_57_out, decoder_11_out20);
  not not_14 (not_14_out, or_53_out);
  assign controlled_buffer_113_out = not_14_out ? data_2_q : 16'bz;  // Controlled_Buffer controlled_buffer_113
  or or_54 (or_54_out, EXECUTE_stage_q[14], EXECUTE_stage_q[13], or_51_out);
  Pull_Resistor pull_resistor_14 (.node(controlled_buffer_112_out));
  or or_55 (or_55_out, EXECUTE_stage_q[14], or_53_out);
  Pull_Resistor pull_resistor_15 (.node(controlled_buffer_113_out));
  Pull_Resistor pull_resistor_16 (.node(pull_resistor_16_node));
  assign {or_64_out[3], controlled_buffer_114_out, or_64_out[4]} = or_52_out ? adder_1_out : 16'bz;  // Controlled_Buffer controlled_buffer_114
  Adder #(.width(16)) adder_1 (
    .a(data_1_q), .b(controlled_buffer_112_out), .out(adder_1_out), .cin(or_54_out), .cout(adder_1_cout));
  or or_56 (or_56_out, decoder_11_out2, and_57_out);
  assign {or_64_out[3], controlled_buffer_114_out, or_64_out[4]} = or_56_out ? subtractor_2_out : 16'bz;  // Controlled_Buffer controlled_buffer_115
  Subtractor #(.width(16)) subtractor_2 (
    .a(data_1_q), .b(controlled_buffer_113_out), .out(subtractor_2_out), .bin(or_55_out),
    .bout(subtractor_2_bout));
  assign {or_64_out[3], controlled_buffer_114_out, or_64_out[4]} = decoder_11_out3 ? multiplier_1_out : 16'bz;  // Controlled_Buffer controlled_buffer_116
  Multiplier #(.mode("twosComplement"), .width(16)) multiplier_1 (
    .a(data_1_q), .b(data_2_q), .out(multiplier_1_out));  // open: cin, cout
  assign {or_64_out[3], controlled_buffer_114_out, or_64_out[4]} = decoder_11_out4 ? fpadder_1_out : 16'bz;  // Controlled_Buffer controlled_buffer_117
  FPAdder #(.fpwidth(16)) fpadder_1 (.a(data_1_q), .b(data_2_q), .out(fpadder_1_out));
  assign {or_64_out[3], controlled_buffer_114_out, or_64_out[4]} = decoder_11_out5 ? fpsubtractor_1_out : 16'bz;  // Controlled_Buffer controlled_buffer_118
  FPSubtractor #(.fpwidth(16)) fpsubtractor_1 (.a(data_1_q), .b(data_2_q), .out(fpsubtractor_1_out));
  assign {or_64_out[3], controlled_buffer_114_out, or_64_out[4]} = decoder_11_out6 ? fpmultiplier_1_out : 16'bz;  // Controlled_Buffer controlled_buffer_119
  FPMultiplier #(.fpwidth(16)) fpmultiplier_1 (.a(data_1_q), .b(data_2_q), .out(fpmultiplier_1_out));
  assign and_58_out = data_1_q & data_2_q;  // AND_Gate and_58, 16 bits wide
  assign {or_64_out[3], controlled_buffer_114_out, or_64_out[4]} = decoder_11_out7 ? and_58_out : 16'bz;  // Controlled_Buffer controlled_buffer_120
  assign or_57_out = data_1_q | data_2_q;  // OR_Gate or_57, 16 bits wide
  assign {or_64_out[3], controlled_buffer_114_out, or_64_out[4]} = decoder_11_out8 ? or_57_out : 16'bz;  // Controlled_Buffer controlled_buffer_121
  assign xor_1_out = data_1_q ^ data_2_q;  // XOR_Gate xor_1, 16 bits wide
  assign {or_64_out[3], controlled_buffer_114_out, or_64_out[4]} = decoder_11_out9 ? xor_1_out : 16'bz;  // Controlled_Buffer controlled_buffer_122
  Comparator #(.mode("unsigned"), .width(16)) comparator_63 (
    .a(data_1_q), .b(data_2_q), .gt(comparator_63_gt), .eq(comparator_63_eq), .lt(comparator_63_lt));
  Comparator #(.width(16)) comparator_64 (
    .a(data_1_q), .b(data_2_q), .gt(comparator_64_gt), .eq(comparator_64_eq), .lt(comparator_64_lt));
  or or_58 (or_58_out, decoder_11_out11, decoder_11_out10);
  assign controlled_buffer_123_out = or_58_out ? comparator_65_eq : 1'bz;  // Controlled_Buffer controlled_buffer_123
  Comparator #(.width(16)) comparator_65 (
    .a(data_1_q), .b(pull_resistor_16_node), .eq(comparator_65_eq));  // open: gt, lt
  or or_59 (or_59_out, decoder_11_out13, decoder_11_out15);
  assign controlled_buffer_124_out[15] = or_59_out ? data_1_q[0] : 1'bz;  // Controlled_Buffer controlled_buffer_124
  Pull_Resistor pull_resistor_17 (.node(controlled_buffer_124_out[15]));
  Negator #(.width(16)) negator_1 (.in(data_1_q), .out(negator_1_out));
  Pull_Resistor pull_resistor_18 (.node({or_64_out[3], controlled_buffer_114_out, or_64_out[4]}));
  Pull_Resistor pull_resistor_19 (.node(pull_resistor_19_node));
  assign controlled_buffer_125_out = decoder_11_out10 ? comparator_63_gt : 1'bz;  // Controlled_Buffer controlled_buffer_125
  assign controlled_buffer_126_out = decoder_11_out10 ? comparator_63_eq : 1'bz;  // Controlled_Buffer controlled_buffer_126
  assign pull_resistor_19_node = decoder_11_out10 ? comparator_63_lt : 1'bz;  // Controlled_Buffer controlled_buffer_127
  Pull_Resistor pull_resistor_20 (.node(controlled_buffer_126_out));
  Pull_Resistor pull_resistor_21 (.node(pull_resistor_21_node));
  assign controlled_buffer_128_out = decoder_11_out11 ? comparator_64_gt : 1'bz;  // Controlled_Buffer controlled_buffer_128
  assign pull_resistor_21_node = decoder_11_out11 ? comparator_64_eq : 1'bz;  // Controlled_Buffer controlled_buffer_129
  assign controlled_buffer_130_out = decoder_11_out11 ? comparator_64_lt : 1'bz;  // Controlled_Buffer controlled_buffer_130
  Pull_Resistor pull_resistor_22 (.node(controlled_buffer_130_out));
  or or_60 (or_60_out, decoder_11_out15, decoder_11_out14);
  or or_61 (or_61_out, decoder_11_out12, decoder_11_out13, decoder_11_out14, decoder_11_out15);
  assign controlled_buffer_131_out[0] = or_59_out ? data_1_q[15] : 1'bz;  // Controlled_Buffer controlled_buffer_131
  assign {or_64_out[3], controlled_buffer_114_out, or_64_out[4]} = decoder_11_out16 ? ~data_1_q : 16'bz;  // Controlled_Inverter controlled_inverter_1
  assign {or_64_out[3], controlled_buffer_114_out, or_64_out[4]} = decoder_11_out18 ? negator_1_out : 16'bz;  // Controlled_Buffer controlled_buffer_132
  assign {or_64_out[3], controlled_buffer_114_out, or_64_out[4]} = decoder_11_out22 ? {data_1_q[0], data_1_q[1], data_1_q[2], data_1_q[3], data_1_q[4], data_1_q[5], data_1_q[6], data_1_q[7], data_1_q[8], data_1_q[9], data_1_q[10], data_1_q[11], data_1_q[12], data_1_q[13], data_1_q[14], data_1_q[15]} : 16'bz;  // Controlled_Buffer controlled_buffer_133
  Register #(.width(16)) register_50 (
    .D({or_64_out[3], controlled_buffer_114_out, or_64_out[4]}), .en(CLK_out), .clk(CLK_out),
    .Q(register_50_q));  // open: clr
  Register #(.width(16)) register_51 (.D(data_2_q), .en(CLK_out), .clk(CLK_out), .Q(register_51_q));  // open: clr
  D_Flip_Flop d_ff_3 (.D(or_49_out), .clk(CLK_out), .Q(write), .Qn(read));  // open: preset, reset
  or or_62 (or_62_out[0], adder_1_cout, subtractor_2_bout);
  Pull_Resistor pull_resistor_23 (.node(controlled_buffer_125_out));
  or or_63 (or_64_out[1], controlled_buffer_125_out, controlled_buffer_128_out);
  or or_64 (or_64_out[0], controlled_buffer_126_out, pull_resistor_21_node);
  or or_65 (or_64_out[2], pull_resistor_19_node, controlled_buffer_130_out);
  Pull_Resistor pull_resistor_24 (.node(controlled_buffer_128_out));
  or or_66 (or_66_out, or_52_out, or_56_out);
  and and_59 (and_59_out, or_61_out, ~or_60_out);  // AND_Gate
  assign {or_64_out[3], controlled_buffer_114_out, or_64_out[4]} = and_59_out ? {data_1_q[14:0], controlled_buffer_131_out[0]} : 16'bz;  // Controlled_Buffer controlled_buffer_134
  Pull_Resistor pull_resistor_25 (.node(controlled_buffer_131_out[0]));
  assign {or_64_out[3], controlled_buffer_114_out, or_64_out[4]} = or_60_out ? {controlled_buffer_124_out[15], data_1_q[15:1]} : 16'bz;  // Controlled_Buffer controlled_buffer_135
  Comparator #(.width(16)) comparator_66 (
    .a({or_64_out[3], controlled_buffer_114_out, or_64_out[4]}), .b(pull_resistor_26_node),
    .eq(comparator_66_eq));  // open: gt, lt
  Pull_Resistor pull_resistor_26 (.node(pull_resistor_26_node));
  Multiplexer #(.width(16)) multiplexer_40 (
    .in0(multiplexer_32_out), .in1(register_50_q), .out(address_out), .sel(write));
  assign DATA_out = write ? register_51_q : 16'bz;  // Controlled_Buffer controlled_buffer_136
  or or_67 (or_64_out[5], comparator_66_eq, controlled_buffer_123_out);
  Pull_Resistor pull_resistor_27 (.node(controlled_buffer_123_out));
  and and_60 (and_60_out, ~or_66_out, EXECUTE_stage_q[0]);  // AND_Gate

  // Notes on the sheet:
  //   DECODE
  //   registrer file
  //   READ
  //   SOFTW
endmodule
