// Logisim project computer.circ as structural Verilog: 18 circuits, main circuit main
module main (
  input  Enable
);

  wire button_1_out, button_2_out, CLK_out, comparator_1_eq, comparator_2_eq, controlled_buffer_3_out,
       controlled_buffer_6_out, keyboard_1_avail, Processor_clk_out, Processor_read, Processor_read_ram,
       Processor_write, Processor_write_ram;
  wire [3:0] Processor_controll;
  wire [7:0] controlled_buffer_4_out, or_1_out, Processor_data_output, pull_resistor_1_node,
       pull_resistor_4_node, pull_resistor_5_node, ram_1_dout;
  wire [15:0] Processor_address;

  Clock CLK (.out(CLK_out));
  CPU Processor (
    .CLK_IN(CLK_out), .Enable(Enable), .Interrupt(keyboard_1_avail), .Interrupt_port(4'b0001),
    .controll(Processor_controll), .Address(Processor_address), .Write(Processor_write),
    .Read(Processor_read), .Data_Output(Processor_data_output), .Data_Input(or_1_out),
    .CLK_OUT(Processor_clk_out), .read_ram(Processor_read_ram), .write_ram(Processor_write_ram));
  RAM #(.addrWidth(16), .enables("line"), .\type ("nonvolatile")) ram_1 (
    .addr(Processor_address), .we(Processor_write_ram), .clk(Processor_clk_out), .din(Processor_data_output),
    .dout(ram_1_dout));
  assign or_1_out = pull_resistor_1_node | pull_resistor_4_node;  // OR_Gate or_1, 8 bits wide
  Pull_Resistor pull_resistor_1 (.node(pull_resistor_1_node));
  assign pull_resistor_1_node = Processor_read_ram ? ram_1_dout : 8'bz;  // Controlled_Buffer controlled_buffer_1
  Controlled_Buffer controlled_buffer_2 (.in(Processor_read), .en(comparator_1_eq));  // open: out
  assign controlled_buffer_3_out = comparator_1_eq ? Processor_write : 1'bz;  // Controlled_Buffer controlled_buffer_3
  Pull_Resistor pull_resistor_2 (.node(controlled_buffer_3_out));
  Comparator #(.mode("unsigned"), .width(4)) comparator_1 (
    .a(Processor_controll), .b(4'b0001), .eq(comparator_1_eq));  // open: gt, lt
  assign controlled_buffer_4_out = controlled_buffer_3_out ? Processor_data_output : 8'bz;  // Controlled_Buffer controlled_buffer_4
  Pull_Resistor pull_resistor_3 (.node(controlled_buffer_4_out));
  Pull_Resistor pull_resistor_4 (.node(pull_resistor_4_node));
  Pull_Resistor pull_resistor_5 (.node(pull_resistor_5_node));
  assign pull_resistor_4_node = controlled_buffer_6_out ? pull_resistor_5_node : 8'bz;  // Controlled_Buffer controlled_buffer_5
  assign controlled_buffer_6_out = comparator_2_eq ? Processor_read : 1'bz;  // Controlled_Buffer controlled_buffer_6
  Pull_Resistor pull_resistor_6 (.node(controlled_buffer_6_out));
  TTY tty_1 (
    .data(controlled_buffer_4_out[6:0]), .clk(Processor_clk_out), .we(controlled_buffer_3_out),
    .clr(button_1_out));
  Button button_1 (.out(button_1_out));
  Comparator #(.mode("unsigned"), .width(4)) comparator_2 (
    .a(Processor_controll), .b(4'b0001), .eq(comparator_2_eq));  // open: gt, lt
  Controlled_Buffer controlled_buffer_7 (.in(Processor_write), .en(comparator_2_eq));  // open: out
  Keyboard keyboard_1 (
    .clk(Processor_clk_out), .re(controlled_buffer_6_out), .clr(button_2_out), .avail(keyboard_1_avail),
    .data(pull_resistor_5_node[6:0]));
  Button button_2 (.out(button_2_out));

  // Notes on the sheet:
  //   Enable: initial=0x1
endmodule

module stepper (
  input  Enable,
  input  CLK,
  input  Reset_Manual,
  input  Reset_2,
  input  Reset,
  output out_6,
  output out_7,
  output out_8,
  output out_9,
  output out_10,
  output out_11,
  output out_12,
  output out_13,
  output out_14,
  output out_15,
  output out_16,
  output out_17,
  output out_18,
  output out_19,
  output out_20,
  output out_21
);

  wire nor_1_out, or_1_out, or_2_out;

  or or_1 (or_1_out, Reset_Manual, Reset_2, Reset);
  nor nor_1 (nor_1_out, out_20, out_18, out_17, out_21, out_16, out_15, out_14, out_13, out_12, out_11, out_10, out_9, out_8, out_7, out_6, out_19);
  or or_2 (or_2_out, out_21, nor_1_out);
  Shift_Register #(.length(16)) shift_register_1 (
    .shift(Enable), .in(or_2_out), .clk(CLK), .out(out_21), .clr(or_1_out), .q0(out_6), .q1(out_7),
    .q2(out_8), .q3(out_9), .q4(out_10), .q5(out_11), .q6(out_12), .q7(out_13), .q8(out_14), .q9(out_15),
    .q10(out_16), .q11(out_17), .q12(out_18), .q13(out_19), .q14(out_20));  // open: load, d0, d1, d2, d3, d4, d5, d6, d7, d8, d9, d10, d11, d12, d13, d14, d15, q15
endmodule

module oneOR (
  input  in_1,
  input  in_2,
  output out_3
);

  Pull_Resistor pull_resistor_1 (.node(out_3));
  or or_1 (out_3, in_1, in_2);
endmodule

module forORup (
  input  in_1,
  input  in_2,
  input  in_3,
  input  in_4,
  input  in_5,
  input  in_6,
  input  in_7,
  input  in_8,
  output out_9,
  output out_10,
  output out_11,
  output out_12
);

  Pull_Resistor pull_resistor_1 (.node(out_12));
  or or_1 (out_12, in_7, in_8);
  Pull_Resistor pull_resistor_2 (.node(out_11));
  or or_2 (out_11, in_5, in_6);
  Pull_Resistor pull_resistor_3 (.node(out_10));
  or or_3 (out_10, in_3, in_4);
  Pull_Resistor pull_resistor_4 (.node(out_9));
  or or_4 (out_9, in_1, in_2);
endmodule

module forORleft (
  input  in_1,
  input  in_2,
  input  in_3,
  input  in_4,
  input  in_5,
  input  in_6,
  input  in_7,
  input  in_8,
  output out_9,
  output out_10,
  output out_11,
  output out_12
);

  Pull_Resistor pull_resistor_1 (.node(out_12));
  or or_1 (out_12, in_7, in_8);
  Pull_Resistor pull_resistor_2 (.node(out_11));
  or or_2 (out_11, in_5, in_6);
  Pull_Resistor pull_resistor_3 (.node(out_10));
  or or_3 (out_10, in_3, in_4);
  Pull_Resistor pull_resistor_4 (.node(out_9));
  or or_4 (out_9, in_1, in_2);
endmodule

module load_store_imediate (
  input  [3:0] WRrIN,
  input  [3:0] WRacc_tmpIN,
  input  [3:0] RabcdIN,
  input  [3:0] WabcdIN,
  input  [12:0] stepsIN,
  input  resetIN,
  input  increnentRin,
  input  [7:0] opcode,
  output [3:0] WRrOUT,
  output [3:0] WRacc_tmpOUT,
  output [3:0] RabcdOUT,
  output RADD,
  output [3:0] WabcdOUT,
  output [12:0] stepsOUT,
  output SelectRADD_lh,
  output RSP,
  output resetOUT,
  output increnentRout,
  output load
);

  wire and_1_out, and_2_out, and_3_out, and_4_out, and_5_out, and_6_out, and_7_out, and_8_out, and_9_out,
       and_11_out, and_12_out, and_13_out, or_4_out, or_8_out, or_10_out, or_11_out, or_13_out, or_14_out,
       or_15_out, or_16_out, or_17_out, or_18_out, or_19_out, pull_resistor_3_node, pull_resistor_9_node;
  wire [3:0] demultiplexer_1_out3, demultiplexer_2_out3, pull_resistor_6_node, pull_resistor_15_node;

  or or_1 (resetOUT, and_1_out, and_13_out, resetIN);
  or or_2 (increnentRout, increnentRin, or_19_out, and_2_out);
  Pull_Resistor pull_resistor_1 (.node(resetIN));
  Pull_Resistor pull_resistor_2 (.node(increnentRin));
  and and_1 (and_1_out, stepsIN[11], or_4_out);
  and and_2 (and_2_out, stepsIN[12], or_4_out);
  or or_3 (pull_resistor_6_node[2], pull_resistor_3_node, or_11_out);
  or or_4 (or_4_out, or_8_out, and_3_out);
  Pull_Resistor pull_resistor_3 (.node(pull_resistor_3_node));
  assign pull_resistor_3_node = stepsIN[12] ? and_3_out : 1'bz;  // Controlled_Buffer controlled_buffer_1
  Demultiplexer #(.select(2)) demultiplexer_1 (
    .out0(demultiplexer_1_out3[3]), .out1(demultiplexer_1_out3[2]), .out2(demultiplexer_1_out3[1]),
    .out3(demultiplexer_1_out3[0]), .in(pull_resistor_3_node), .sel(opcode[1:0]));
  and and_3 (and_3_out, ~opcode[7], ~opcode[6], ~opcode[5], ~opcode[4], ~opcode[3], opcode[2]);  // AND_Gate
  Pull_Resistor pull_resistor_4 (.node(resetIN));
  Pull_Resistor pull_resistor_5 (.node(increnentRin));
  assign WRrOUT = WRrIN | pull_resistor_6_node;  // OR_Gate or_5, 4 bits wide
  Pull_Resistor pull_resistor_6 (.node(pull_resistor_6_node));
  Pull_Resistor pull_resistor_7 (.node(WRrIN));
  Pull_Resistor pull_resistor_8 (.node(WabcdIN));
  assign WabcdOUT = WabcdIN | demultiplexer_1_out3;  // OR_Gate or_6, 4 bits wide
  or or_7 (pull_resistor_6_node[3], pull_resistor_9_node, or_14_out, or_17_out);
  or or_8 (or_8_out, or_10_out, and_4_out);
  Pull_Resistor pull_resistor_9 (.node(pull_resistor_9_node));
  assign pull_resistor_9_node = stepsIN[12] ? and_4_out : 1'bz;  // Controlled_Buffer controlled_buffer_2
  Demultiplexer #(.select(2)) demultiplexer_2 (
    .out0(demultiplexer_2_out3[3]), .out1(demultiplexer_2_out3[2]), .out2(demultiplexer_2_out3[1]),
    .out3(demultiplexer_2_out3[0]), .in(pull_resistor_9_node), .sel(opcode[1:0]));
  and and_4 (and_4_out, opcode[7], ~opcode[6], ~opcode[5], ~opcode[4], ~opcode[3], opcode[2]);  // AND_Gate
  assign RabcdOUT = RabcdIN | demultiplexer_2_out3;  // OR_Gate or_9, 4 bits wide
  Pull_Resistor pull_resistor_10 (.node(RabcdIN));
  or or_10 (or_10_out, or_13_out, and_5_out);
  or or_11 (or_11_out, pull_resistor_15_node[1], pull_resistor_15_node[3]);
  Pull_Resistor pull_resistor_11 (.node(pull_resistor_15_node[3]));
  assign pull_resistor_15_node[3] = stepsIN[12] ? and_5_out : 1'bz;  // Controlled_Buffer controlled_buffer_3
  and and_5 (and_5_out, ~opcode[0], ~opcode[1], ~opcode[7], ~opcode[6], opcode[5], ~opcode[4], opcode[3], ~opcode[2]);  // AND_Gate
  assign WRacc_tmpOUT = WRacc_tmpIN | pull_resistor_15_node;  // OR_Gate or_12, 4 bits wide
  Pull_Resistor pull_resistor_12 (.node(WRacc_tmpIN));
  or or_13 (or_13_out, or_15_out, and_6_out);
  and and_6 (and_6_out, opcode[0], ~opcode[1], ~opcode[7], ~opcode[6], opcode[5], ~opcode[4], opcode[3], ~opcode[2]);  // AND_Gate
  or or_14 (or_14_out, pull_resistor_15_node[0], pull_resistor_15_node[2]);
  Pull_Resistor pull_resistor_13 (.node(pull_resistor_15_node[2]));
  assign pull_resistor_15_node[2] = stepsIN[12] ? and_6_out : 1'bz;  // Controlled_Buffer controlled_buffer_4
  or or_15 (or_15_out, or_16_out, and_7_out);
  Pull_Resistor pull_resistor_14 (.node(pull_resistor_15_node[1]));
  assign pull_resistor_15_node[1] = stepsIN[12] ? and_7_out : 1'bz;  // Controlled_Buffer controlled_buffer_5
  and and_7 (and_7_out, ~opcode[0], ~opcode[1], ~opcode[7], ~opcode[6], opcode[5], opcode[4], ~opcode[3], ~opcode[2]);  // AND_Gate
  or or_16 (or_16_out, and_9_out, and_8_out);
  Pull_Resistor pull_resistor_15 (.node(pull_resistor_15_node[0]));
  assign pull_resistor_15_node[0] = stepsIN[12] ? and_8_out : 1'bz;  // Controlled_Buffer controlled_buffer_6
  and and_8 (and_8_out, opcode[0], ~opcode[1], ~opcode[7], ~opcode[6], opcode[5], opcode[4], ~opcode[3], ~opcode[2]);  // AND_Gate
  or or_17 (or_17_out, RSP, or_18_out);
  Pull_Resistor pull_resistor_16 (.node(RSP));
  assign RSP = stepsIN[12] ? and_9_out : 1'bz;  // Controlled_Buffer controlled_buffer_7
  and and_9 (and_9_out, ~opcode[7], ~opcode[6], opcode[5], ~opcode[4], ~opcode[3], ~opcode[2], ~opcode[1], ~opcode[0]);  // AND_Gate
  or or_18 (or_18_out, and_12_out, SelectRADD_lh);
  or or_19 (or_19_out, and_12_out, SelectRADD_lh);
  and and_10 (SelectRADD_lh, and_11_out, stepsIN[12]);
  and and_11 (and_11_out, ~opcode[7], ~opcode[6], opcode[5], ~opcode[4], ~opcode[3], opcode[2], ~opcode[1], opcode[0]);  // AND_Gate
  or or_20 (RADD, SelectRADD_lh, and_12_out);
  and and_12 (and_12_out, stepsIN[11], and_11_out);
  and and_13 (and_13_out, stepsIN[10], and_11_out);
  or or_21 (load, and_11_out, or_4_out);

  assign stepsOUT = stepsIN;
endmodule

module transfers (
  input  [3:0] WRrIN,
  input  [3:0] WRacc_tmpIN,
  input  [3:0] RabcdIN,
  input  [3:0] WabcdIN,
  input  [12:0] stepsIN,
  input  resetIN,
  input  increnentRin,
  input  [7:0] in_8,
  output [3:0] WRrOUT,
  output [3:0] WRacc_tmpOUT,
  output [3:0] RabcdOUT,
  output [3:0] WabcdOUT,
  output [12:0] stepsOUT,
  output resetOUT,
  output increnentRout
);

  wire and_1_out, and_2_out, and_3_out, and_4_out, and_5_out, and_6_out, and_7_out, and_8_out, and_9_out,
       and_10_out, and_11_out, and_12_out, and_13_out, and_14_out, demultiplexer_1_out0,
       demultiplexer_1_out1, demultiplexer_1_out2, demultiplexer_1_out3, demultiplexer_2_out0,
       demultiplexer_2_out1, demultiplexer_2_out2, demultiplexer_2_out3, demultiplexer_3_out0,
       demultiplexer_3_out1, demultiplexer_3_out2, demultiplexer_3_out3, demultiplexer_4_out0,
       demultiplexer_4_out1, demultiplexer_4_out2, demultiplexer_4_out3, demultiplexer_5_out0,
       demultiplexer_5_out1, demultiplexer_5_out2, demultiplexer_5_out3, fororleft_3_out_9,
       fororleft_3_out_10, fororleft_3_out_11, fororleft_3_out_12, fororleft_4_out_9, fororleft_4_out_10,
       fororleft_4_out_11, fororleft_4_out_12, fororleft_5_out_9, fororleft_5_out_10, fororleft_5_out_11,
       fororleft_5_out_12, fororleft_6_out_9, fororleft_6_out_10, fororleft_6_out_11, fororleft_6_out_12,
       fororleft_7_out_9, fororleft_7_out_10, fororleft_7_out_11, fororleft_7_out_12, fororleft_8_out_9,
       fororleft_8_out_10, fororleft_8_out_11, fororleft_8_out_12, fororleft_9_out_9, fororleft_9_out_10,
       fororleft_9_out_11, fororleft_9_out_12, pull_resistor_7_node, pull_resistor_11_node,
       pull_resistor_13_node, pull_resistor_15_node, pull_resistor_17_node, pull_resistor_18_node,
       pull_resistor_20_node;
  wire [3:0] pull_resistor_6_node, pull_resistor_8_node, pull_resistor_10_node;

  Pull_Resistor pull_resistor_1 (.node(increnentRin));
  assign WRacc_tmpOUT = WRacc_tmpIN | pull_resistor_10_node;  // OR_Gate or_1, 4 bits wide
  assign RabcdOUT = RabcdIN | pull_resistor_8_node;  // OR_Gate or_2, 4 bits wide
  assign WabcdOUT = WabcdIN | pull_resistor_6_node;  // OR_Gate or_3, 4 bits wide
  Pull_Resistor pull_resistor_2 (.node(WRrIN));
  Pull_Resistor pull_resistor_3 (.node(WRacc_tmpIN));
  Pull_Resistor pull_resistor_4 (.node(RabcdIN));
  Pull_Resistor pull_resistor_5 (.node(WabcdIN));
  or or_4 (resetOUT, pull_resistor_7_node, and_1_out);
  Pull_Resistor pull_resistor_6 (.node(pull_resistor_6_node));
  Pull_Resistor pull_resistor_7 (.node(pull_resistor_7_node));
  Pull_Resistor pull_resistor_8 (.node(pull_resistor_8_node));
  and and_1 (and_1_out, stepsIN[11], and_2_out);
  Pull_Resistor pull_resistor_9 (.node(pull_resistor_8_node[3]));
  assign pull_resistor_8_node[3] = stepsIN[12] ? and_2_out : 1'bz;  // Controlled_Buffer controlled_buffer_1
  Demultiplexer #(.select(2)) demultiplexer_1 (
    .out0(demultiplexer_1_out0), .out1(demultiplexer_1_out1), .out2(demultiplexer_1_out2),
    .out3(demultiplexer_1_out3), .in(pull_resistor_8_node[3]), .sel(in_8[1:0]));
  and and_2 (and_2_out, in_8[2], in_8[3], ~in_8[4], ~in_8[5], ~in_8[6], ~in_8[7]);  // AND_Gate
  Pull_Resistor pull_resistor_10 (.node(pull_resistor_10_node));
  forORleft fororleft_1 (
    .out_9(pull_resistor_6_node[0]), .out_10(pull_resistor_6_node[1]), .out_11(pull_resistor_6_node[2]),
    .out_12(pull_resistor_6_node[3]), .in_6(demultiplexer_1_out1), .in_4(demultiplexer_1_out2),
    .in_2(demultiplexer_1_out3), .in_1(fororleft_4_out_9), .in_3(fororleft_4_out_10),
    .in_5(fororleft_4_out_11), .in_7(fororleft_4_out_12));  // open: in_8
  forORleft fororleft_2 (
    .out_9(pull_resistor_10_node[0]), .out_10(pull_resistor_10_node[1]), .out_11(pull_resistor_10_node[2]),
    .out_12(pull_resistor_10_node[3]), .in_8(demultiplexer_1_out0), .in_1(fororleft_3_out_9),
    .in_3(fororleft_3_out_10), .in_5(fororleft_3_out_11), .in_7(fororleft_3_out_12));  // open: in_6, in_4, in_2
  Pull_Resistor pull_resistor_11 (.node(pull_resistor_11_node));
  or or_5 (pull_resistor_7_node, pull_resistor_11_node, and_3_out);
  and and_3 (and_3_out, stepsIN[11], and_4_out);
  and and_4 (and_4_out, in_8[2], in_8[3], ~in_8[4], ~in_8[5], in_8[6], ~in_8[7]);  // AND_Gate
  Pull_Resistor pull_resistor_12 (.node(pull_resistor_8_node[2]));
  assign pull_resistor_8_node[2] = stepsIN[12] ? and_4_out : 1'bz;  // Controlled_Buffer controlled_buffer_2
  Demultiplexer #(.select(2)) demultiplexer_2 (
    .out0(demultiplexer_2_out0), .out1(demultiplexer_2_out1), .out2(demultiplexer_2_out2),
    .out3(demultiplexer_2_out3), .in(pull_resistor_8_node[2]), .sel(in_8[1:0]));
  forORleft fororleft_3 (
    .out_9(fororleft_3_out_9), .out_10(fororleft_3_out_10), .out_11(fororleft_3_out_11),
    .out_12(fororleft_3_out_12), .in_8(demultiplexer_2_out0), .in_1(fororleft_6_out_9),
    .in_3(fororleft_6_out_10), .in_5(fororleft_6_out_11), .in_7(fororleft_6_out_12));  // open: in_6, in_4, in_2
  forORleft fororleft_4 (
    .out_9(fororleft_4_out_9), .out_10(fororleft_4_out_10), .out_11(fororleft_4_out_11),
    .out_12(fororleft_4_out_12), .in_8(demultiplexer_2_out1), .in_4(demultiplexer_2_out2),
    .in_2(demultiplexer_2_out3), .in_1(fororleft_5_out_9), .in_3(fororleft_5_out_10),
    .in_5(fororleft_5_out_11), .in_7(fororleft_5_out_12));  // open: in_6
  or or_6 (pull_resistor_11_node, pull_resistor_13_node, and_5_out);
  Pull_Resistor pull_resistor_13 (.node(pull_resistor_13_node));
  and and_5 (and_5_out, stepsIN[11], and_6_out);
  Pull_Resistor pull_resistor_14 (.node(pull_resistor_8_node[1]));
  assign pull_resistor_8_node[1] = stepsIN[12] ? and_6_out : 1'bz;  // Controlled_Buffer controlled_buffer_3
  Demultiplexer #(.select(2)) demultiplexer_3 (
    .out0(demultiplexer_3_out0), .out1(demultiplexer_3_out1), .out2(demultiplexer_3_out2),
    .out3(demultiplexer_3_out3), .in(pull_resistor_8_node[1]), .sel(in_8[1:0]));
  and and_6 (and_6_out, in_8[2], in_8[3], ~in_8[4], ~in_8[5], ~in_8[6], in_8[7]);  // AND_Gate
  forORleft fororleft_5 (
    .out_9(fororleft_5_out_9), .out_10(fororleft_5_out_10), .out_11(fororleft_5_out_11),
    .out_12(fororleft_5_out_12), .in_8(demultiplexer_3_out1), .in_6(demultiplexer_3_out2),
    .in_2(demultiplexer_3_out3), .in_1(fororleft_7_out_9), .in_3(fororleft_7_out_10),
    .in_5(fororleft_7_out_11), .in_7(fororleft_7_out_12));  // open: in_4
  forORleft fororleft_6 (
    .out_9(fororleft_6_out_9), .out_10(fororleft_6_out_10), .out_11(fororleft_6_out_11),
    .out_12(fororleft_6_out_12), .in_8(demultiplexer_3_out0), .in_1(fororleft_8_out_9),
    .in_3(fororleft_8_out_10), .in_5(fororleft_8_out_11), .in_7(fororleft_8_out_12));  // open: in_6, in_4, in_2
  Pull_Resistor pull_resistor_15 (.node(pull_resistor_15_node));
  or or_7 (pull_resistor_13_node, pull_resistor_15_node, and_7_out);
  and and_7 (and_7_out, stepsIN[11], and_8_out);
  Pull_Resistor pull_resistor_16 (.node(pull_resistor_8_node[0]));
  assign pull_resistor_8_node[0] = stepsIN[12] ? and_8_out : 1'bz;  // Controlled_Buffer controlled_buffer_4
  Demultiplexer #(.select(2)) demultiplexer_4 (
    .out0(demultiplexer_4_out0), .out1(demultiplexer_4_out1), .out2(demultiplexer_4_out2),
    .out3(demultiplexer_4_out3), .in(pull_resistor_8_node[0]), .sel(in_8[1:0]));
  and and_8 (and_8_out, in_8[2], in_8[3], ~in_8[4], ~in_8[5], in_8[6], in_8[7]);  // AND_Gate
  forORleft fororleft_7 (
    .out_9(fororleft_7_out_9), .out_10(fororleft_7_out_10), .out_11(fororleft_7_out_11),
    .out_12(fororleft_7_out_12), .in_8(demultiplexer_4_out1), .in_6(demultiplexer_4_out2),
    .in_4(demultiplexer_4_out3), .in_1(demultiplexer_5_out3), .in_3(demultiplexer_5_out2),
    .in_5(demultiplexer_5_out1), .in_7(demultiplexer_5_out0));  // open: in_2
  forORleft fororleft_8 (
    .out_9(fororleft_8_out_9), .out_10(fororleft_8_out_10), .out_11(fororleft_8_out_11),
    .out_12(fororleft_8_out_12), .in_8(demultiplexer_4_out0), .in_1(fororleft_9_out_9),
    .in_3(fororleft_9_out_10), .in_5(fororleft_9_out_11), .in_7(fororleft_9_out_12));  // open: in_6, in_4, in_2
  Pull_Resistor pull_resistor_17 (.node(pull_resistor_17_node));
  or or_8 (pull_resistor_15_node, pull_resistor_17_node, and_9_out);
  and and_9 (and_9_out, stepsIN[11], and_10_out);
  and and_10 (and_10_out, in_8[2], in_8[3], ~in_8[4], in_8[5], ~in_8[6], ~in_8[7]);  // AND_Gate
  forORleft fororleft_9 (
    .out_9(fororleft_9_out_9), .out_10(fororleft_9_out_10), .out_11(fororleft_9_out_11),
    .out_12(fororleft_9_out_12), .in_6(pull_resistor_18_node), .in_1(and_14_out), .in_3(and_11_out),
    .in_5(and_11_out), .in_7(and_14_out));  // open: in_8, in_4, in_2
  Pull_Resistor pull_resistor_18 (.node(pull_resistor_18_node));
  assign pull_resistor_18_node = stepsIN[12] ? and_10_out : 1'bz;  // Controlled_Buffer controlled_buffer_5
  Demultiplexer #(.select(2)) demultiplexer_5 (
    .out0(demultiplexer_5_out0), .out1(demultiplexer_5_out1), .out2(demultiplexer_5_out2),
    .out3(demultiplexer_5_out3), .in(pull_resistor_18_node), .sel(in_8[1:0]));
  or or_9 (pull_resistor_17_node, resetIN, and_12_out);
  Pull_Resistor pull_resistor_19 (.node(resetIN));
  and and_11 (and_11_out, pull_resistor_20_node, ~in_8[0]);  // AND_Gate
  and and_12 (and_12_out, stepsIN[11], and_13_out);
  Pull_Resistor pull_resistor_20 (.node(pull_resistor_20_node));
  assign pull_resistor_20_node = stepsIN[12] ? and_13_out : 1'bz;  // Controlled_Buffer controlled_buffer_6
  and and_13 (and_13_out, ~in_8[1], in_8[2], in_8[3], ~in_8[4], in_8[5], ~in_8[6], in_8[7]);  // AND_Gate
  and and_14 (and_14_out, pull_resistor_20_node, in_8[0]);

  assign increnentRout = increnentRin;
  assign stepsOUT = stepsIN;
  assign WRrOUT = WRrIN;
endmodule

module jumps (
  input  [3:0] WRrIN,
  input  [3:0] WRacc_tmpIN,
  input  [3:0] RabcdIN,
  input  [3:0] WabcdIN,
  input  [12:0] stepsIN,
  input  resetIN,
  input  increnentRin,
  input  [7:0] ALUflags,
  input  interrupt,
  input  [7:0] in_10,
  output [3:0] WRrOUT,
  output [3:0] WRacc_tmpOUT,
  output [3:0] RabcdOUT,
  output [3:0] WabcdOUT,
  output [12:0] stepsOUT,
  output resetOUT,
  output increnentRout,
  output WADDhigh,
  output WADDlow,
  output jump
);

  wire and_1_out, and_2_out, and_3_out, and_4_out, and_5_out, and_6_out, and_7_out, and_8_out, and_9_out,
       and_10_out, and_11_out, and_12_out, and_13_out, jump_component_1_increment, jump_component_1_reset,
       not_1_out, not_2_out, not_3_out, or_5_out, or_7_out, or_8_out, or_9_out, or_10_out, or_11_out,
       or_12_out, or_13_out, or_14_out, or_15_out, or_16_out, or_17_out, or_18_out, or_19_out, or_20_out,
       or_21_out, or_22_out, or_23_out, or_24_out, or_25_out, or_26_out, or_27_out, or_28_out,
       pull_resistor_8_node, pull_resistor_9_node, pull_resistor_10_node, pull_resistor_11_node,
       pull_resistor_12_node, pull_resistor_13_node, pull_resistor_14_node, pull_resistor_15_node,
       pull_resistor_16_node, pull_resistor_17_node, pull_resistor_18_node, pull_resistor_19_node;
  wire [3:0] pull_resistor_5_node;

  assign WRrOUT = WRrIN | pull_resistor_5_node;  // OR_Gate or_1, 4 bits wide
  Pull_Resistor pull_resistor_1 (.node(WRrIN));
  Pull_Resistor pull_resistor_2 (.node(WRacc_tmpIN));
  Pull_Resistor pull_resistor_3 (.node(RabcdIN));
  Pull_Resistor pull_resistor_4 (.node(WabcdIN));
  Pull_Resistor pull_resistor_5 (.node(pull_resistor_5_node));
  or or_2 (resetOUT, jump_component_1_reset, resetIN);
  or or_3 (increnentRout, increnentRin, jump_component_1_increment);
  or or_4 (pull_resistor_5_node[2], WADDhigh, WADDlow);
  jump_component jump_component_1 (
    .reset(jump_component_1_reset), .increment(jump_component_1_increment), .WADDlow(WADDhigh),
    .WADDhigh(WADDlow), .in_1(stepsIN[12]), .in_2(stepsIN[11]), .in_3(stepsIN[9]), .condition(or_5_out),
    .\do (jump));
  Pull_Resistor pull_resistor_6 (.node(resetIN));
  Pull_Resistor pull_resistor_7 (.node(increnentRin));
  or or_5 (or_5_out, or_7_out, and_1_out);
  or or_6 (jump, or_8_out, and_1_out);
  and and_1 (and_1_out, ~in_10[7], ~in_10[6], ~in_10[5], in_10[4], ~in_10[3], ~in_10[2], ~in_10[1], ~in_10[0]);  // AND_Gate
  or or_7 (or_7_out, or_9_out, pull_resistor_8_node);
  or or_8 (or_8_out, or_10_out, and_2_out);
  and and_2 (and_2_out, ~in_10[7], ~in_10[6], ~in_10[5], in_10[4], ~in_10[3], ~in_10[2], ~in_10[1], in_10[0]);  // AND_Gate
  or or_9 (or_9_out, or_11_out, pull_resistor_9_node);
  or or_10 (or_10_out, or_12_out, and_3_out);
  Pull_Resistor pull_resistor_8 (.node(pull_resistor_8_node));
  assign pull_resistor_8_node = and_2_out ? ALUflags[0] : 1'bz;  // Controlled_Buffer controlled_buffer_1
  and and_3 (and_3_out, ~in_10[7], ~in_10[6], ~in_10[5], in_10[4], ~in_10[3], ~in_10[2], in_10[1], ~in_10[0]);  // AND_Gate
  or or_11 (or_11_out, or_13_out, pull_resistor_10_node);
  or or_12 (or_12_out, or_14_out, and_4_out);
  Pull_Resistor pull_resistor_9 (.node(pull_resistor_9_node));
  assign pull_resistor_9_node = and_3_out ? ALUflags[6] : 1'bz;  // Controlled_Buffer controlled_buffer_2
  Pull_Resistor pull_resistor_10 (.node(pull_resistor_10_node));
  assign pull_resistor_10_node = and_4_out ? ALUflags[1] : 1'bz;  // Controlled_Buffer controlled_buffer_3
  and and_4 (and_4_out, ~in_10[7], ~in_10[6], ~in_10[5], in_10[4], ~in_10[3], ~in_10[2], in_10[1], in_10[0]);  // AND_Gate
  or or_13 (or_13_out, or_15_out, pull_resistor_11_node);
  or or_14 (or_14_out, or_16_out, and_5_out);
  and and_5 (and_5_out, ~in_10[7], in_10[6], ~in_10[5], in_10[4], ~in_10[3], ~in_10[2], ~in_10[1], in_10[0]);  // AND_Gate
  or or_15 (or_15_out, or_17_out, pull_resistor_12_node);
  or or_16 (or_16_out, or_18_out, and_6_out);
  Pull_Resistor pull_resistor_11 (.node(pull_resistor_11_node));
  assign pull_resistor_11_node = and_5_out ? ALUflags[2] : 1'bz;  // Controlled_Buffer controlled_buffer_4
  Pull_Resistor pull_resistor_12 (.node(pull_resistor_12_node));
  assign pull_resistor_12_node = and_6_out ? ALUflags[3] : 1'bz;  // Controlled_Buffer controlled_buffer_5
  and and_6 (and_6_out, ~in_10[7], in_10[6], ~in_10[5], in_10[4], ~in_10[3], ~in_10[2], ~in_10[1], ~in_10[0]);  // AND_Gate
  or or_17 (or_17_out, or_20_out, pull_resistor_13_node);
  or or_18 (or_18_out, or_19_out, and_7_out);
  and and_7 (and_7_out, ~in_10[7], in_10[6], ~in_10[5], in_10[4], ~in_10[3], ~in_10[2], in_10[1], ~in_10[0]);  // AND_Gate
  or or_19 (or_19_out, or_22_out, and_8_out);
  Pull_Resistor pull_resistor_13 (.node(pull_resistor_13_node));
  assign pull_resistor_13_node = and_7_out ? not_1_out : 1'bz;  // Controlled_Buffer controlled_buffer_6
  not not_1 (not_1_out, ALUflags[5]);
  or or_20 (or_20_out, or_21_out, pull_resistor_14_node);
  and and_8 (and_8_out, ~in_10[7], in_10[6], ~in_10[5], in_10[4], ~in_10[3], ~in_10[2], in_10[1], in_10[0]);  // AND_Gate
  or or_21 (or_21_out, or_23_out, pull_resistor_15_node);
  or or_22 (or_22_out, or_24_out, and_9_out);
  Pull_Resistor pull_resistor_14 (.node(pull_resistor_14_node));
  assign pull_resistor_14_node = and_8_out ? ALUflags[5] : 1'bz;  // Controlled_Buffer controlled_buffer_7
  Pull_Resistor pull_resistor_15 (.node(pull_resistor_15_node));
  assign pull_resistor_15_node = and_9_out ? not_2_out : 1'bz;  // Controlled_Buffer controlled_buffer_8
  and and_9 (and_9_out, in_10[7], in_10[6], ~in_10[5], in_10[4], ~in_10[3], ~in_10[2], ~in_10[1], ~in_10[0]);  // AND_Gate
  not not_2 (not_2_out, ALUflags[4]);
  or or_23 (or_23_out, or_25_out, pull_resistor_16_node);
  or or_24 (or_24_out, or_26_out, and_10_out);
  and and_10 (and_10_out, in_10[7], in_10[6], ~in_10[5], in_10[4], ~in_10[3], ~in_10[2], ~in_10[1], in_10[0]);  // AND_Gate
  or or_25 (or_25_out, or_27_out, pull_resistor_17_node);
  or or_26 (or_26_out, or_28_out, and_11_out);
  Pull_Resistor pull_resistor_16 (.node(pull_resistor_16_node));
  assign pull_resistor_16_node = and_10_out ? ALUflags[4] : 1'bz;  // Controlled_Buffer controlled_buffer_9
  and and_11 (and_11_out, in_10[7], in_10[6], ~in_10[5], in_10[4], ~in_10[3], ~in_10[2], in_10[1], ~in_10[0]);  // AND_Gate
  or or_27 (or_27_out, pull_resistor_19_node, pull_resistor_18_node);
  or or_28 (or_28_out, and_13_out, and_12_out);
  Pull_Resistor pull_resistor_17 (.node(pull_resistor_17_node));
  assign pull_resistor_17_node = and_11_out ? ALUflags[7] : 1'bz;  // Controlled_Buffer controlled_buffer_10
  Pull_Resistor pull_resistor_18 (.node(pull_resistor_18_node));
  assign pull_resistor_18_node = and_12_out ? interrupt : 1'bz;  // Controlled_Buffer controlled_buffer_11
  and and_12 (and_12_out, in_10[7], in_10[6], ~in_10[5], in_10[4], ~in_10[3], ~in_10[2], in_10[1], in_10[0]);  // AND_Gate
  and and_13 (and_13_out, in_10[7], in_10[6], ~in_10[5], in_10[4], ~in_10[3], in_10[2], ~in_10[1], ~in_10[0]);  // AND_Gate
  Pull_Resistor pull_resistor_19 (.node(pull_resistor_19_node));
  assign pull_resistor_19_node = and_13_out ? not_3_out : 1'bz;  // Controlled_Buffer controlled_buffer_12
  not not_3 (not_3_out, ALUflags[2]);

  assign RabcdOUT = RabcdIN;
  assign stepsOUT = stepsIN;
  assign WabcdOUT = WabcdIN;
  assign WRacc_tmpOUT = WRacc_tmpIN;
endmodule

module operations (
  input  [3:0] WRrIN,
  input  [3:0] WRacc_tmpIN,
  input  [3:0] RabcdIN,
  input  [3:0] WabcdIN,
  input  [12:0] stepsIN,
  input  resetIN,
  input  increnentRin,
  input  [7:0] in_8,
  output [3:0] WRrOUT,
  output [3:0] WRacc_tmpOUT,
  output [3:0] RabcdOUT,
  output [3:0] WabcdOUT,
  output [12:0] stepsOUT,
  output ALUset,
  output ALUcarry,
  output [3:0] ALUopp,
  output resetOUT,
  output increnentRout
);

  wire and_1_out, and_4_out, and_5_out, and_6_out, and_7_out, and_8_out, and_9_out, and_10_out, and_11_out,
       and_12_out, or_3_out, or_5_out, or_7_out, or_9_out, or_11_out, or_13_out, or_15_out, or_17_out,
       or_19_out;
  wire [2:0] pull_resistor_6_node;
  wire [3:0] or_6_out, or_8_out, or_10_out, or_12_out, or_14_out, or_16_out, or_18_out, or_20_out,
       pull_resistor_8_node, pull_resistor_9_node, pull_resistor_10_node, pull_resistor_11_node,
       pull_resistor_12_node, pull_resistor_13_node, pull_resistor_14_node, pull_resistor_15_node,
       pull_resistor_16_node;

  Pull_Resistor pull_resistor_1 (.node(increnentRin));
  Pull_Resistor pull_resistor_2 (.node(WRrIN));
  Pull_Resistor pull_resistor_3 (.node(WRacc_tmpIN));
  assign WRacc_tmpOUT = WRacc_tmpIN | {ALUset, pull_resistor_6_node};  // OR_Gate or_1, 4 bits wide
  Pull_Resistor pull_resistor_4 (.node(RabcdIN));
  Pull_Resistor pull_resistor_5 (.node(WabcdIN));
  Pull_Resistor pull_resistor_6 (.node({ALUset, pull_resistor_6_node}));
  Pull_Resistor pull_resistor_7 (.node(resetIN));
  or or_2 (resetOUT, resetIN, and_1_out);
  and and_1 (and_1_out, stepsIN[11], or_3_out);
  and and_2 (ALUset, stepsIN[12], or_3_out);
  and and_3 (ALUcarry, and_4_out, in_8[0]);
  or or_3 (or_3_out, or_5_out, and_4_out);
  and and_4 (and_4_out, ~in_8[7], ~in_8[6], ~in_8[5], in_8[4], ~in_8[3], in_8[2], ~in_8[1]);  // AND_Gate
  assign ALUopp = pull_resistor_8_node | or_6_out;  // OR_Gate or_4, 4 bits wide
  or or_5 (or_5_out, or_7_out, and_5_out);
  Pull_Resistor pull_resistor_8 (.node(pull_resistor_8_node));
  assign pull_resistor_8_node = and_4_out ? 4'b0000 : 4'bz;  // Controlled_Buffer controlled_buffer_1
  and and_5 (and_5_out, ~in_8[7], ~in_8[6], ~in_8[5], in_8[4], ~in_8[3], in_8[2], in_8[1], ~in_8[0]);  // AND_Gate
  Pull_Resistor pull_resistor_9 (.node(pull_resistor_9_node));
  assign pull_resistor_9_node = and_5_out ? 4'b0001 : 4'bz;  // Controlled_Buffer controlled_buffer_2
  assign or_6_out = pull_resistor_9_node | or_8_out;  // OR_Gate or_6, 4 bits wide
  or or_7 (or_7_out, or_9_out, and_6_out);
  and and_6 (and_6_out, ~in_8[7], ~in_8[6], ~in_8[5], in_8[4], ~in_8[3], in_8[2], in_8[1], in_8[0]);  // AND_Gate
  assign or_8_out = pull_resistor_10_node | or_10_out;  // OR_Gate or_8, 4 bits wide
  or or_9 (or_9_out, or_11_out, and_7_out);
  Pull_Resistor pull_resistor_10 (.node(pull_resistor_10_node));
  assign pull_resistor_10_node = and_6_out ? 4'b0010 : 4'bz;  // Controlled_Buffer controlled_buffer_3
  and and_7 (and_7_out, ~in_8[7], in_8[6], ~in_8[5], in_8[4], ~in_8[3], in_8[2], ~in_8[1], ~in_8[0]);  // AND_Gate
  Pull_Resistor pull_resistor_11 (.node(pull_resistor_11_node));
  assign pull_resistor_11_node = and_7_out ? 4'b0011 : 4'bz;  // Controlled_Buffer controlled_buffer_4
  assign or_10_out = pull_resistor_11_node | or_12_out;  // OR_Gate or_10, 4 bits wide
  or or_11 (or_11_out, or_13_out, and_8_out);
  and and_8 (and_8_out, ~in_8[7], in_8[6], ~in_8[5], in_8[4], ~in_8[3], in_8[2], ~in_8[1], in_8[0]);  // AND_Gate
  Pull_Resistor pull_resistor_12 (.node(pull_resistor_12_node));
  assign pull_resistor_12_node = and_8_out ? 4'b0100 : 4'bz;  // Controlled_Buffer controlled_buffer_5
  assign or_12_out = pull_resistor_12_node | or_14_out;  // OR_Gate or_12, 4 bits wide
  or or_13 (or_13_out, or_15_out, and_9_out);
  and and_9 (and_9_out, ~in_8[7], in_8[6], ~in_8[5], in_8[4], ~in_8[3], in_8[2], in_8[1], in_8[0]);  // AND_Gate
  assign or_14_out = pull_resistor_13_node | or_16_out;  // OR_Gate or_14, 4 bits wide
  or or_15 (or_15_out, or_17_out, and_10_out);
  Pull_Resistor pull_resistor_13 (.node(pull_resistor_13_node));
  assign pull_resistor_13_node = and_9_out ? 4'b0101 : 4'bz;  // Controlled_Buffer controlled_buffer_6
  and and_10 (and_10_out, in_8[7], in_8[6], ~in_8[5], ~in_8[4], ~in_8[3], in_8[2], ~in_8[1], ~in_8[0]);  // AND_Gate
  Pull_Resistor pull_resistor_14 (.node(pull_resistor_14_node));
  assign pull_resistor_14_node = and_10_out ? 4'b0110 : 4'bz;  // Controlled_Buffer controlled_buffer_7
  assign or_16_out = pull_resistor_14_node | or_18_out;  // OR_Gate or_16, 4 bits wide
  or or_17 (or_17_out, or_19_out, and_11_out);
  and and_11 (and_11_out, in_8[7], in_8[6], ~in_8[5], ~in_8[4], ~in_8[3], in_8[2], ~in_8[1], in_8[0]);  // AND_Gate
  assign or_18_out = pull_resistor_15_node | or_20_out;  // OR_Gate or_18, 4 bits wide
  buf or_19 (or_19_out, and_12_out);  // OR_Gate
  Pull_Resistor pull_resistor_15 (.node(pull_resistor_15_node));
  assign pull_resistor_15_node = and_11_out ? 4'b0111 : 4'bz;  // Controlled_Buffer controlled_buffer_8
  and and_12 (and_12_out, in_8[7], in_8[6], ~in_8[5], ~in_8[4], ~in_8[3], in_8[2], in_8[1], ~in_8[0]);  // AND_Gate
  assign or_20_out = pull_resistor_16_node;  // OR_Gate or_20, 4 bits wide OR_Gate
  Pull_Resistor pull_resistor_16 (.node(pull_resistor_16_node));
  assign pull_resistor_16_node = and_12_out ? 4'b1000 : 4'bz;  // Controlled_Buffer controlled_buffer_9

  assign increnentRout = increnentRin;
  assign RabcdOUT = RabcdIN;
  assign stepsOUT = stepsIN;
  assign WabcdOUT = WabcdIN;
  assign WRrOUT = WRrIN;
endmodule

module binary_to_bcd (
  input  [7:0] in_1,
  input  [7:0] in_2
);
endmodule

module stepper2 (
  input  Enable,
  input  CLK,
  input  Reset_Manual,
  input  Reset_2,
  input  Reset,
  output out_6,
  output out_7,
  output out_8,
  output out_9,
  output out_10,
  output out_11,
  output out_12,
  output out_13,
  output out_14,
  output out_15
);

  wire nor_1_out, or_1_out, or_2_out;

  nor nor_1 (nor_1_out, out_15, out_14, out_13, out_12, out_6, out_11, out_10, out_9, out_8, out_7);
  or or_1 (or_1_out, out_15, nor_1_out);
  Shift_Register #(.length(10)) shift_register_1 (
    .shift(Enable), .in(or_1_out), .clk(CLK), .out(out_15), .clr(or_2_out), .q0(out_6), .q1(out_7),
    .q2(out_8), .q3(out_9), .q4(out_10), .q5(out_11), .q6(out_12), .q7(out_13), .q8(out_14));  // open: load, d0, d1, d2, d3, d4, d5, d6, d7, d8, d9, q9
  or or_2 (or_2_out, Reset_Manual, Reset_2, Reset);
endmodule

module ALU (
  input  [7:0] BUSin,
  input  ALUset,
  input  ALUcarry,
  input  [3:0] ALUopp,
  input  WACC,
  input  RACC,
  input  WTMP,
  input  RTMP,
  input  CLK,
  output [7:0] BUSout,
  output [7:0] ALUflags
);

  wire adder_1_cout, and_2_out, and_3_out, or_4_out;
  wire [6:1] register_1_q;
  wire [7:0] adder_1_out, and_1_out, controlled_buffer_2_out, controlled_buffer_3_out, multiplier_1_out,
       not_1_out, or_2_out, or_3_out, pull_resistor_1_node, pull_resistor_4_node, register_2_q,
       shifter_1_out, shifter_2_out, subtractor_1_out, xor_1_out;

  assign BUSout = controlled_buffer_2_out | controlled_buffer_3_out;  // OR_Gate or_1, 8 bits wide
  Pull_Resistor pull_resistor_1 (.node(pull_resistor_1_node));
  assign pull_resistor_1_node = ALUset ? pull_resistor_4_node : 8'bz;  // Controlled_Buffer controlled_buffer_1
  Register register_1 (.D(or_2_out), .en(WACC), .clk(CLK), .Q({ALUflags[5], register_1_q, ALUflags[4]}));  // open: clr
  assign or_2_out = BUSin | pull_resistor_1_node;  // OR_Gate or_2, 8 bits wide
  assign controlled_buffer_2_out = RACC ? {ALUflags[5], register_1_q, ALUflags[4]} : 8'bz;  // Controlled_Buffer controlled_buffer_2
  Pull_Resistor pull_resistor_2 (.node(controlled_buffer_2_out));
  nor nor_1 (ALUflags[6], ALUflags[5], ALUflags[5], register_1_q[6], register_1_q[5], register_1_q[4], register_1_q[3], register_1_q[2], register_1_q[1], ALUflags[4]);
  Adder adder_1 (
    .a({ALUflags[5], register_1_q, ALUflags[4]}), .b(register_2_q), .out(adder_1_out), .cin(ALUcarry),
    .cout(adder_1_cout));
  Subtractor subtractor_1 (
    .a({ALUflags[5], register_1_q, ALUflags[4]}), .b(register_2_q), .out(subtractor_1_out));  // open: bin, bout
  Multiplier #(.mode("twosComplement")) multiplier_1 (
    .a({ALUflags[5], register_1_q, ALUflags[4]}), .b(register_2_q), .out(multiplier_1_out));  // open: cin, cout
  Shifter #(.shift("lr")) shifter_1 (
    .in({ALUflags[5], register_1_q, ALUflags[4]}), .\dist (3'b001), .out(shifter_1_out));
  Shifter shifter_2 (.in({ALUflags[5], register_1_q, ALUflags[4]}), .\dist (3'b001), .out(shifter_2_out));
  assign not_1_out = ~{ALUflags[5], register_1_q, ALUflags[4]};  // NOT_Gate not_1, 8 bits wide
  assign and_1_out = {ALUflags[5], register_1_q, ALUflags[4]} & register_2_q;  // AND_Gate and_1, 8 bits wide
  assign or_3_out = {ALUflags[5], register_1_q, ALUflags[4]} | register_2_q;  // OR_Gate or_3, 8 bits wide
  assign xor_1_out = {ALUflags[5], register_1_q, ALUflags[4]} ^ register_2_q;  // XOR_Gate xor_1, 8 bits wide
  Comparator comparator_1 (
    .a({ALUflags[5], register_1_q, ALUflags[4]}), .b(register_2_q), .gt(ALUflags[1]), .eq(ALUflags[2]),
    .lt(ALUflags[3]));
  Register register_2 (.D(BUSin), .en(WTMP), .clk(CLK), .Q(register_2_q));  // open: clr
  and and_2 (and_2_out, ALUopp[0], ALUopp[1], ~ALUopp[2], ~ALUopp[3], ALUflags[4]);  // AND_Gate
  and and_3 (and_3_out, ~ALUopp[0], ~ALUopp[1], ALUopp[2], ~ALUopp[3], register_1_q[6]);  // AND_Gate
  assign controlled_buffer_3_out = RTMP ? register_2_q : 8'bz;  // Controlled_Buffer controlled_buffer_3
  Pull_Resistor pull_resistor_3 (.node(controlled_buffer_3_out));
  Pull_Resistor pull_resistor_4 (.node(pull_resistor_4_node));
  Multiplexer #(.select(4), .width(8)) multiplexer_1 (
    .in0(adder_1_out), .in1(subtractor_1_out), .in2(multiplier_1_out), .in3(shifter_1_out),
    .in4(shifter_2_out), .in5(not_1_out), .in6(and_1_out), .in7(or_3_out), .in8(xor_1_out),
    .out(pull_resistor_4_node), .sel(ALUopp));  // open: in9, in10, in11, in12, in13, in14, in15
  D_Flip_Flop d_ff_1 (.clk(ALUset), .D(adder_1_cout), .Q(ALUflags[0]));  // open: Qn, preset, reset
  D_Flip_Flop d_ff_2 (.clk(ALUset), .D(or_4_out), .Q(ALUflags[7]));  // open: Qn, preset, reset
  or or_4 (or_4_out, and_2_out, and_3_out);
endmodule

module compliment_to_bin (
  input  [7:0] in_1,
  output out_2,
  output [3:0] out_3,
  output [3:0] out_4
);

  wire not_1_out;
  wire [7:0] adder_1_out, not_2_out, pull_resistor_1_node, pull_resistor_2_node, pull_resistor_3_node;

  assign {out_3, out_4} = pull_resistor_1_node | pull_resistor_2_node;  // OR_Gate or_1, 8 bits wide
  Pull_Resistor pull_resistor_1 (.node(pull_resistor_1_node));
  assign pull_resistor_1_node = in_1[7] ? adder_1_out : 8'bz;  // Controlled_Buffer controlled_buffer_1
  Pull_Resistor pull_resistor_2 (.node(pull_resistor_2_node));
  assign pull_resistor_2_node = not_1_out ? in_1 : 8'bz;  // Controlled_Buffer controlled_buffer_2
  not not_1 (not_1_out, in_1[7]);
  Pull_Resistor pull_resistor_3 (.node(pull_resistor_3_node));
  assign not_2_out = ~in_1;  // NOT_Gate not_2, 8 bits wide
  Adder adder_1 (.a(not_2_out), .b(pull_resistor_3_node), .out(adder_1_out), .cin(in_1[7]));  // open: cout

  assign out_2 = in_1[7];
endmodule

module jump_component (
  input  in_1,
  input  in_2,
  input  in_3,
  input  condition,
  input  \do ,
  output reset,
  output increment,
  output WADDlow,
  output WADDhigh
);

  wire or_1_out;

  and and_1 (increment, \do , or_1_out);
  and and_2 (reset, in_3, \do );
  and and_3 (WADDlow, \do , in_1, condition);
  and and_4 (WADDhigh, \do , in_2, condition);
  or or_1 (or_1_out, in_1, in_2);
endmodule

module load_store_address (
  input  [3:0] WRrIN,
  input  [3:0] WRacc_tmpIN,
  input  [3:0] RabcdIN,
  input  [3:0] WabcdIN,
  input  [12:0] stepsIN,
  input  resetIN,
  input  incrementIN,
  input  [7:0] opcode,
  output [3:0] WRrOUT,
  output [3:0] WRacc_tmpOUT,
  output [3:0] RabcdOUT,
  output [3:0] WabcdOUT,
  output [12:0] stepsOUT,
  output ADDselect,
  output Write,
  output read,
  output RSP,
  output [1:0] RADD_lh,
  output saveADD,
  output loadADD,
  output WADDlow,
  output WADDhigh,
  output resetOUT,
  output increnentRout,
  output load_interrupt_address
);

  wire and_2_out, and_3_out, and_4_out, and_5_out, and_6_out, and_7_out, and_8_out, and_9_out, and_10_out,
       and_11_out, and_12_out, and_13_out, and_14_out, and_15_out, and_16_out, and_17_out, and_18_out,
       and_20_out, and_22_out, and_23_out, and_24_out, and_25_out, and_26_out, and_27_out,
       fororleft_1_out_11, fororleft_1_out_12, jump_component_1_increment, jump_component_1_waddhigh,
       jump_component_1_waddlow, or_3_out, or_7_out, or_8_out, or_9_out, or_10_out, or_15_out, or_16_out,
       or_17_out, or_18_out, or_19_out, or_20_out, or_21_out, or_22_out, or_23_out, or_24_out, or_25_out,
       or_26_out, or_27_out, or_28_out, or_29_out, or_30_out, or_31_out, or_32_out, or_33_out, or_34_out,
       or_36_out, or_37_out, or_38_out, pull_resistor_8_node, pull_resistor_12_node;
  wire [3:0] pull_resistor_7_node, pull_resistor_9_node, pull_resistor_10_node, pull_resistor_11_node;

  or or_1 (resetOUT, or_7_out, resetIN);
  Pull_Resistor pull_resistor_1 (.node(resetIN));
  or or_2 (increnentRout, or_3_out, and_11_out, incrementIN);
  Pull_Resistor pull_resistor_2 (.node(incrementIN));
  or or_3 (or_3_out, jump_component_1_increment, or_16_out);
  or or_4 (loadADD, and_6_out, or_9_out);
  or or_5 (WADDlow, and_23_out, jump_component_1_waddhigh);
  or or_6 (WADDhigh, and_22_out, jump_component_1_waddlow);
  or or_7 (or_7_out, and_8_out, and_4_out, and_3_out, and_5_out);
  and and_1 (saveADD, stepsIN[12], or_15_out);
  or or_8 (or_8_out, jump_component_1_waddhigh, jump_component_1_waddlow);
  or or_9 (or_9_out, and_7_out, and_2_out);
  and and_2 (and_2_out, ADDselect, stepsIN[8]);
  and and_3 (and_3_out, or_34_out, ~or_10_out, stepsIN[7]);  // AND_Gate
  and and_4 (and_4_out, ADDselect, stepsIN[5], ~and_25_out);  // AND_Gate
  or or_10 (or_10_out, and_25_out, ADDselect);
  and and_5 (and_5_out, stepsIN[1], and_25_out);
  and and_6 (and_6_out, and_25_out, stepsIN[5]);
  assign WRrOUT = WRrIN | pull_resistor_11_node;  // OR_Gate or_11, 4 bits wide
  assign WRacc_tmpOUT = WRacc_tmpIN | pull_resistor_10_node;  // OR_Gate or_12, 4 bits wide
  assign RabcdOUT = RabcdIN | pull_resistor_9_node;  // OR_Gate or_13, 4 bits wide
  assign WabcdOUT = WabcdIN | pull_resistor_7_node;  // OR_Gate or_14, 4 bits wide
  or or_15 (or_15_out, or_20_out, ADDselect);
  or or_16 (or_16_out, and_9_out, and_10_out, or_33_out);
  Pull_Resistor pull_resistor_3 (.node(WRrIN));
  Pull_Resistor pull_resistor_4 (.node(WRacc_tmpIN));
  Pull_Resistor pull_resistor_5 (.node(RabcdIN));
  Pull_Resistor pull_resistor_6 (.node(WabcdIN));
  jump_component jump_component_1 (
    .increment(jump_component_1_increment), .WADDlow(jump_component_1_waddlow),
    .WADDhigh(jump_component_1_waddhigh), .in_1(stepsIN[11]), .in_2(stepsIN[10]), .condition(1'b1),
    .\do (or_17_out));  // open: reset, in_3
  or or_17 (or_17_out, or_34_out, or_20_out);
  and and_7 (and_7_out, stepsIN[9], or_20_out);
  and and_8 (and_8_out, stepsIN[6], or_20_out);
  and and_9 (and_9_out, or_21_out, or_20_out);
  and and_10 (and_10_out, ADDselect, or_18_out);
  or or_18 (or_18_out, stepsIN[7], stepsIN[6]);
  or or_19 (or_19_out, stepsIN[2], stepsIN[4], stepsIN[3]);
  and and_11 (and_11_out, or_19_out, and_25_out);
  Pull_Resistor pull_resistor_7 (.node(pull_resistor_7_node));
  or or_20 (or_20_out, or_22_out, and_12_out);
  or or_21 (or_21_out, stepsIN[8], stepsIN[7]);
  Pull_Resistor pull_resistor_8 (.node(pull_resistor_8_node));
  assign pull_resistor_8_node = stepsIN[9] ? and_12_out : 1'bz;  // Controlled_Buffer controlled_buffer_1
  and and_12 (and_12_out, ~opcode[7], ~opcode[6], ~opcode[5], ~opcode[4], opcode[3], ~opcode[2]);  // AND_Gate
  Pull_Resistor pull_resistor_9 (.node(pull_resistor_9_node));
  Demultiplexer #(.select(2)) demultiplexer_1 (
    .out0(pull_resistor_7_node[3]), .out1(pull_resistor_7_node[2]), .out2(pull_resistor_7_node[1]),
    .out3(pull_resistor_7_node[0]), .in(pull_resistor_8_node), .sel(opcode[1:0]));
  Pull_Resistor pull_resistor_10 (.node(pull_resistor_10_node));
  or or_22 (or_22_out, or_26_out, and_13_out);
  and and_13 (and_13_out, opcode[7], ~opcode[6], ~opcode[5], ~opcode[4], opcode[3], ~opcode[2]);  // AND_Gate
  Pull_Resistor pull_resistor_11 (.node(pull_resistor_11_node));
  forORup fororup_1 (
    .out_12(pull_resistor_11_node[3]), .out_11(pull_resistor_11_node[2]), .out_10(pull_resistor_11_node[1]),
    .out_9(pull_resistor_11_node[0]), .in_8(or_24_out), .in_6(or_23_out), .in_5(or_25_out),
    .in_7(fororleft_1_out_12));  // open: in_4, in_2, in_1, in_3
  or or_23 (or_23_out, pull_resistor_8_node, or_36_out);
  or or_24 (or_24_out, pull_resistor_12_node, read, or_32_out);
  Pull_Resistor pull_resistor_12 (.node(pull_resistor_12_node));
  assign pull_resistor_12_node = stepsIN[9] ? and_13_out : 1'bz;  // Controlled_Buffer controlled_buffer_2
  Demultiplexer #(.select(2)) demultiplexer_2 (
    .out0(pull_resistor_9_node[3]), .out1(pull_resistor_9_node[2]), .out2(pull_resistor_9_node[1]),
    .out3(pull_resistor_9_node[0]), .in(pull_resistor_12_node), .sel(opcode[1:0]));
  or or_25 (or_25_out, or_8_out, fororleft_1_out_11);
  or or_26 (or_26_out, or_27_out, and_14_out);
  assign pull_resistor_10_node[3] = stepsIN[9] ? and_14_out : 1'bz;  // Controlled_Buffer controlled_buffer_3
  or or_27 (or_27_out, or_28_out, and_15_out);
  and and_14 (and_14_out, ~opcode[7], ~opcode[6], opcode[5], ~opcode[4], opcode[3], ~opcode[2], opcode[1], ~opcode[0]);  // AND_Gate
  forORleft fororleft_1 (
    .out_11(fororleft_1_out_11), .out_12(fororleft_1_out_12), .in_8(pull_resistor_10_node[2]),
    .in_6(pull_resistor_10_node[3]), .in_5(pull_resistor_10_node[1]), .in_7(or_29_out));  // open: out_9, out_10, in_4, in_2, in_1, in_3
  assign pull_resistor_10_node[2] = stepsIN[9] ? and_15_out : 1'bz;  // Controlled_Buffer controlled_buffer_4
  and and_15 (and_15_out, ~opcode[7], ~opcode[6], opcode[5], ~opcode[4], opcode[3], ~opcode[2], opcode[1], opcode[0]);  // AND_Gate
  assign pull_resistor_10_node[1] = stepsIN[9] ? and_16_out : 1'bz;  // Controlled_Buffer controlled_buffer_5
  or or_28 (or_28_out, or_30_out, and_16_out);
  and and_16 (and_16_out, ~opcode[7], ~opcode[6], opcode[5], opcode[4], ~opcode[3], ~opcode[2], opcode[1], ~opcode[0]);  // AND_Gate
  or or_29 (or_29_out, RSP, pull_resistor_10_node[0]);
  or or_30 (or_30_out, or_31_out, and_17_out);
  assign pull_resistor_10_node[0] = stepsIN[9] ? and_17_out : 1'bz;  // Controlled_Buffer controlled_buffer_6
  and and_17 (and_17_out, ~opcode[7], ~opcode[6], opcode[5], opcode[4], ~opcode[3], ~opcode[2], opcode[1], opcode[0]);  // AND_Gate
  or or_31 (or_31_out, or_38_out, and_18_out);
  Pull_Resistor pull_resistor_13 (.node(RSP));
  assign RSP = stepsIN[9] ? and_18_out : 1'bz;  // Controlled_Buffer controlled_buffer_7
  and and_18 (and_18_out, ~opcode[7], ~opcode[6], opcode[5], ~opcode[4], ~opcode[3], ~opcode[2], ~opcode[1], opcode[0]);  // AND_Gate
  or or_32 (or_32_out, and_20_out, RADD_lh[1]);
  or or_33 (or_33_out, or_32_out, and_22_out);
  or or_34 (or_34_out, or_37_out, ADDselect);
  or or_35 (RADD_lh[0], RADD_lh[1], and_20_out);
  and and_19 (RADD_lh[1], stepsIN[9], ADDselect);
  and and_20 (and_20_out, ADDselect, stepsIN[8]);
  and and_21 (ADDselect, ~opcode[7], ~opcode[6], opcode[5], ~opcode[4], ~opcode[3], opcode[2], opcode[1], opcode[0]);  // AND_Gate
  or or_36 (or_36_out, and_23_out, and_22_out);
  and and_22 (and_22_out, stepsIN[9], or_37_out);
  and and_23 (and_23_out, stepsIN[8], or_37_out);
  or or_37 (or_37_out, and_24_out, and_25_out);
  and and_24 (and_24_out, ~opcode[7], ~opcode[6], opcode[5], ~opcode[4], ~opcode[3], opcode[2], opcode[1], ~opcode[0]);  // AND_Gate
  and and_25 (and_25_out, opcode[7], opcode[6], ~opcode[5], ~opcode[4], ~opcode[3], opcode[2], opcode[1], opcode[0]);  // AND_Gate
  or or_38 (or_38_out, and_26_out, and_27_out);
  Pull_Resistor pull_resistor_14 (.node(load_interrupt_address));
  assign load_interrupt_address = and_23_out ? and_25_out : 1'bz;  // Controlled_Buffer controlled_buffer_8
  Pull_Resistor pull_resistor_15 (.node(Write));
  assign Write = stepsIN[9] ? and_26_out : 1'bz;  // Controlled_Buffer controlled_buffer_9
  and and_26 (and_26_out, opcode[7], opcode[6], opcode[5], ~opcode[4]);  // AND_Gate
  Pull_Resistor pull_resistor_16 (.node(read));
  assign read = stepsIN[9] ? and_27_out : 1'bz;  // Controlled_Buffer controlled_buffer_10
  and and_27 (and_27_out, opcode[7], opcode[6], ~opcode[5], ~opcode[4], ~opcode[3], ~opcode[2], opcode[1], ~opcode[0]);  // AND_Gate

  assign stepsOUT = stepsIN;
endmodule

module stackSTUFF (
  input  [3:0] WRrIN,
  input  [3:0] WRacc_tmpIN,
  input  [3:0] RabcdIN,
  input  [3:0] WabcdIN,
  input  [12:0] stepsIN,
  input  resetIN,
  input  incrementIN,
  input  [7:0] opcode,
  output [3:0] WRrOUT,
  output [3:0] WRacc_tmpOUT,
  output WADD_low,
  output [3:0] RabcdOUT,
  output [3:0] WabcdOUT,
  output [1:0] RADD_lh,
  output WADD_high,
  output toggleSTACK,
  output [12:0] stepsOUT,
  output incrementSTACK,
  output decrementSTACK,
  output resetOUT,
  output incrementOUT,
  output interrupt_address,
  output toggle_interrupt_signal
);

  wire and_1_out, and_2_out, and_4_out, and_5_out, and_6_out, and_7_out, and_8_out, and_9_out, and_10_out,
       and_11_out, and_12_out, and_13_out, and_14_out, and_16_out, and_17_out, and_18_out, and_19_out,
       and_20_out, and_22_out, and_23_out, and_24_out, and_25_out, and_27_out, and_28_out, and_29_out,
       and_30_out, and_31_out, and_32_out, and_33_out, and_34_out, and_36_out, and_37_out, and_43_out,
       and_44_out, and_51_out, and_52_out, and_54_out, controlled_buffer_6_out, or_5_out, or_6_out, or_7_out,
       or_8_out, or_10_out, or_15_out, or_16_out, or_19_out, or_20_out, or_24_out, or_26_out, or_27_out,
       or_28_out, or_30_out, or_31_out, or_33_out, or_35_out, or_38_out, or_39_out, or_41_out, or_42_out,
       or_43_out, or_44_out, pull_resistor_3_node, pull_resistor_4_node, pull_resistor_9_node,
       pull_resistor_11_node, pull_resistor_12_node;
  wire [1:0] or_34_out, or_40_out;
  wire [3:0] and_38_out, and_47_out, demultiplexer_1_out3, demultiplexer_2_out3, or_17_out, or_21_out,
       or_22_out, or_29_out, pull_resistor_10_node, pull_resistor_14_node;

  or or_1 (resetOUT, or_8_out, or_7_out, resetIN);
  buf or_2 (incrementOUT, incrementIN);  // OR_Gate
  Pull_Resistor pull_resistor_1 (.node(resetIN));
  Pull_Resistor pull_resistor_2 (.node(incrementIN));
  and and_1 (and_1_out, and_37_out, stepsIN[3]);
  or or_3 (toggleSTACK, and_1_out, pull_resistor_3_node, pull_resistor_4_node, or_42_out);
  or or_4 (incrementSTACK, or_5_out, or_28_out, or_26_out);
  or or_5 (or_5_out, or_6_out, and_5_out);
  or or_6 (or_6_out, controlled_buffer_6_out, or_10_out);
  or or_7 (or_7_out, and_8_out, and_54_out);
  buf or_8 (or_8_out, and_2_out);  // OR_Gate
  or or_9 (decrementSTACK, or_10_out, or_28_out);
  or or_10 (or_10_out, and_6_out, or_41_out);
  Pull_Resistor pull_resistor_3 (.node(pull_resistor_3_node));
  Pull_Resistor pull_resistor_4 (.node(pull_resistor_4_node));
  and and_2 (and_2_out, stepsIN[9], or_33_out);
  // AND_Gate and_3 has open pins: in0=stepsIN[10], in1=or_15_out, out=open
  and and_4 (and_4_out, stepsIN[11], and_9_out);
  and and_5 (and_5_out, stepsIN[11], and_9_out);
  and and_6 (and_6_out, stepsIN[12], and_10_out);
  and and_7 (and_7_out, stepsIN[10], and_10_out);
  assign pull_resistor_3_node = or_15_out ? stepsIN[12] : 1'bz;  // Controlled_Buffer controlled_buffer_1
  assign pull_resistor_4_node = or_15_out ? stepsIN[10] : 1'bz;  // Controlled_Buffer controlled_buffer_2
  and and_8 (and_8_out, stepsIN[2], and_37_out);
  Pull_Resistor pull_resistor_5 (.node(WRrIN));
  assign WRrOUT = WRrIN | pull_resistor_10_node;  // OR_Gate or_11, 4 bits wide
  Pull_Resistor pull_resistor_6 (.node(WRacc_tmpIN));
  assign WRacc_tmpOUT = WRacc_tmpIN | or_17_out;  // OR_Gate or_12, 4 bits wide
  Pull_Resistor pull_resistor_7 (.node(RabcdIN));
  assign RabcdOUT = RabcdIN | or_21_out;  // OR_Gate or_13, 4 bits wide
  Pull_Resistor pull_resistor_8 (.node(WabcdIN));
  assign WabcdOUT = WabcdIN | or_22_out;  // OR_Gate or_14, 4 bits wide
  or or_15 (or_15_out, or_27_out, or_16_out);
  or or_16 (or_16_out, and_9_out, and_10_out);
  assign or_17_out = pull_resistor_14_node | or_29_out;  // OR_Gate or_17, 4 bits wide
  Pull_Resistor pull_resistor_9 (.node(pull_resistor_9_node));
  assign pull_resistor_9_node = stepsIN[11] ? and_9_out : 1'bz;  // Controlled_Buffer controlled_buffer_3
  Demultiplexer #(.select(2)) demultiplexer_1 (
    .out0(demultiplexer_1_out3[3]), .out1(demultiplexer_1_out3[2]), .out2(demultiplexer_1_out3[1]),
    .out3(demultiplexer_1_out3[0]), .in(pull_resistor_9_node), .sel(opcode[1:0]));
  and and_9 (and_9_out, ~opcode[7], ~opcode[6], ~opcode[5], opcode[4], opcode[3], ~opcode[2]);  // AND_Gate
  Pull_Resistor pull_resistor_10 (.node(pull_resistor_10_node));
  or or_18 (pull_resistor_10_node[3], or_19_out, or_34_out[0]);
  or or_19 (or_19_out, and_4_out, or_20_out);
  or or_20 (or_20_out, and_11_out, controlled_buffer_6_out, and_17_out);
  assign or_21_out = demultiplexer_1_out3 | and_38_out;  // OR_Gate or_21, 4 bits wide
  assign or_22_out = and_47_out | demultiplexer_2_out3;  // OR_Gate or_22, 4 bits wide
  or or_23 (pull_resistor_10_node[2], and_7_out, or_44_out, or_24_out);
  or or_24 (or_24_out, or_29_out[1], or_38_out, or_29_out[3]);
  and and_10 (and_10_out, opcode[7], ~opcode[6], ~opcode[5], opcode[4], opcode[3], ~opcode[2]);  // AND_Gate
  Pull_Resistor pull_resistor_11 (.node(pull_resistor_11_node));
  assign pull_resistor_11_node = stepsIN[10] ? and_10_out : 1'bz;  // Controlled_Buffer controlled_buffer_4
  Demultiplexer #(.select(2)) demultiplexer_2 (
    .out0(demultiplexer_2_out3[3]), .out1(demultiplexer_2_out3[2]), .out2(demultiplexer_2_out3[1]),
    .out3(demultiplexer_2_out3[0]), .in(pull_resistor_11_node), .sel(opcode[1:0]));
  or or_25 (or_29_out[2], and_11_out, and_33_out);
  or or_26 (or_26_out, and_18_out, or_30_out, and_12_out);
  and and_11 (and_11_out, stepsIN[11], and_13_out);
  and and_12 (and_12_out, stepsIN[11], and_13_out);
  or or_27 (or_27_out, or_31_out, and_22_out, and_19_out, and_16_out, and_13_out);
  or or_28 (or_28_out, and_20_out, or_35_out, and_14_out);
  and and_13 (and_13_out, opcode[7], ~opcode[6], opcode[5], ~opcode[4], opcode[3], ~opcode[2], ~opcode[1], ~opcode[0]);  // AND_Gate
  and and_14 (and_14_out, stepsIN[12], and_16_out);
  and and_15 (or_29_out[3], stepsIN[11], and_16_out);
  and and_16 (and_16_out, opcode[7], ~opcode[6], opcode[5], ~opcode[4], opcode[3], ~opcode[2], ~opcode[1], opcode[0]);  // AND_Gate
  or or_29 (or_29_out[0], and_17_out, and_34_out);
  and and_17 (and_17_out, stepsIN[11], and_19_out);
  and and_18 (and_18_out, stepsIN[11], and_19_out);
  and and_19 (and_19_out, ~opcode[7], ~opcode[6], opcode[5], opcode[4], ~opcode[3], opcode[2], ~opcode[1], ~opcode[0]);  // AND_Gate
  and and_20 (and_20_out, stepsIN[12], and_22_out);
  and and_21 (or_29_out[1], stepsIN[11], and_22_out);
  and and_22 (and_22_out, ~opcode[7], ~opcode[6], opcode[5], opcode[4], ~opcode[3], opcode[2], ~opcode[1], opcode[0]);  // AND_Gate
  or or_30 (or_30_out, and_24_out, and_23_out);
  and and_23 (and_23_out, stepsIN[11], and_27_out);
  or or_31 (or_31_out, pull_resistor_12_node, and_30_out, and_27_out);
  assign RADD_lh = or_34_out | or_40_out;  // OR_Gate or_32, 2 bits wide
  or or_33 (or_33_out, and_30_out, and_27_out);
  or or_34 (or_34_out[0], and_25_out, or_34_out[1]);
  and and_24 (and_24_out, stepsIN[10], and_27_out);
  and and_25 (and_25_out, stepsIN[11], and_27_out);
  and and_26 (or_34_out[1], stepsIN[10], and_27_out);
  and and_27 (and_27_out, ~opcode[7], ~opcode[6], ~opcode[5], opcode[4], opcode[3], opcode[2], ~opcode[1], ~opcode[0]);  // AND_Gate
  or or_35 (or_35_out, and_28_out, and_29_out);
  and and_28 (and_28_out, and_30_out, stepsIN[12]);
  and and_29 (and_29_out, and_30_out, stepsIN[11]);
  and and_30 (and_30_out, ~opcode[7], ~opcode[6], ~opcode[5], opcode[4], opcode[3], opcode[2], opcode[1], opcode[0]);  // AND_Gate
  or or_36 (WADD_low, and_31_out, and_52_out);
  or or_37 (WADD_high, and_32_out, and_51_out);
  or or_38 (or_38_out, and_31_out, and_32_out);
  and and_31 (and_31_out, and_30_out, stepsIN[11]);
  and and_32 (and_32_out, and_30_out, stepsIN[10]);
  Pull_Resistor pull_resistor_12 (.node(pull_resistor_12_node));
  assign pull_resistor_12_node = stepsIN[12] ? and_37_out : 1'bz;  // Controlled_Buffer controlled_buffer_5
  and and_33 (and_33_out, stepsIN[5], and_37_out);
  and and_34 (and_34_out, stepsIN[4], and_37_out);
  or or_39 (or_39_out, stepsIN[5], stepsIN[11], stepsIN[10], stepsIN[4], stepsIN[9], stepsIN[8], stepsIN[7], stepsIN[6]);
  assign controlled_buffer_6_out = and_37_out ? or_39_out : 1'bz;  // Controlled_Buffer controlled_buffer_6
  Pull_Resistor pull_resistor_13 (.node(controlled_buffer_6_out));
  or or_40 (or_40_out[0], or_40_out[1], and_36_out);
  and and_35 (or_40_out[1], stepsIN[11], and_37_out);
  and and_36 (and_36_out, stepsIN[10], and_37_out);
  and and_37 (and_37_out, opcode[7], opcode[6], ~opcode[5], ~opcode[4], ~opcode[3], ~opcode[2], ~opcode[1], ~opcode[0]);  // AND_Gate
  and and_38 (and_38_out[0], stepsIN[6], and_37_out);
  and and_39 (and_38_out[1], stepsIN[7], and_37_out);
  and and_40 (and_38_out[2], stepsIN[8], and_37_out);
  and and_41 (and_38_out[3], stepsIN[9], and_37_out);
  and and_42 (interrupt_address, stepsIN[3], and_37_out);
  or or_41 (or_41_out, and_43_out, or_43_out);
  or or_42 (or_42_out, and_43_out, toggle_interrupt_signal);
  and and_43 (and_43_out, stepsIN[12], and_44_out);
  and and_44 (and_44_out, opcode[7], opcode[6], ~opcode[5], ~opcode[4], opcode[3], ~opcode[2], ~opcode[1], ~opcode[0]);  // AND_Gate
  and and_45 (pull_resistor_14_node[1], stepsIN[11], and_44_out);
  and and_46 (pull_resistor_14_node[3], stepsIN[10], and_44_out);
  and and_47 (and_47_out[0], stepsIN[9], and_44_out);
  and and_48 (and_47_out[1], stepsIN[8], and_44_out);
  and and_49 (and_47_out[2], stepsIN[7], and_44_out);
  and and_50 (and_47_out[3], stepsIN[6], and_44_out);
  and and_51 (and_51_out, stepsIN[5], and_44_out);
  and and_52 (and_52_out, stepsIN[4], and_44_out);
  and and_53 (toggle_interrupt_signal, stepsIN[3], and_44_out);
  and and_54 (and_54_out, and_44_out, stepsIN[2]);
  or or_43 (or_43_out, and_51_out, and_47_out[3], and_47_out[2], and_47_out[1], and_47_out[0], pull_resistor_14_node[3], pull_resistor_14_node[1]);
  or or_44 (or_44_out, and_52_out, or_43_out);
  Pull_Resistor pull_resistor_14 (.node(pull_resistor_14_node));

  assign stepsOUT = stepsIN;
endmodule

module CPU (
  input  Enable,
  input  CLK_IN,
  input  Interrupt,
  input  [3:0] Interrupt_port,
  input  [7:0] Data_Input,
  output [3:0] controll,
  output [15:0] Address,
  output Write,
  output Read,
  output [7:0] Data_Output,
  output CLK_OUT,
  output read_ram,
  output write_ram
);

  wire ADDselect, ALUcarry, ALUset, and_1_out, and_2_out, and_3_out, and_4_out, and_5_out, and_6_out,
       and_7_out, and_8_out, and_9_out, button_1_out, comparator_1_eq, comparator_1_gt, comparator_1_lt,
       decrementSTACK, incrementSTACK, interrupt_address, interrupt_stuff_1_incrementout,
       interrupt_stuff_1_load_add_high, interrupt_stuff_1_load_add_low,
       interrupt_stuff_1_load_interrupt_address, interrupt_stuff_1_read, interrupt_stuff_1_resetout,
       jumps_1_increnentrout, jumps_1_resetout, jumps_1_waddhigh, jumps_1_waddlow, load_interrupt_address,
       load_store_address_1_increnentrout, load_store_address_1_load_interrupt_address,
       load_store_address_1_read, load_store_address_1_resetout, load_store_address_1_rsp,
       load_store_address_1_waddhigh, load_store_address_1_waddlow, load_store_address_1_write,
       load_store_imediate_1_increnentrout, load_store_imediate_1_resetout, load_store_imediate_1_rsp,
       loadADD, nor_1_out, not_1_out, not_2_out, not_3_out, operations_1_increnentrout,
       operations_1_resetout, or_1_out, or_2_out, or_5_out, or_10_out, pull_resistor_1_node,
       pull_resistor_8_node, RA, RACC, RB, RC, RD, RR, RSP, RTMP, stackstuff_1_incrementout,
       stackstuff_1_resetout, stackstuff_1_toggle_interrupt_signal, stackstuff_1_wadd_high,
       stackstuff_1_wadd_low, stepper_1_out_6, stepper_1_out_7, storeADD, t_ff_1_qn, t_ff_2_qn, toggleSTACK,
       transfers_1_increnentrout, transfers_1_resetout, WA, WACC, WADDhigh, WADDlow, WB, WC, WD, WTMP;
  wire [1:0] load_store_address_1_radd_lh, load_store_imediate_1_radd, or_15_out, RADD_lh,
       stackstuff_1_radd_lh;
  wire [2:0] load_store_imediate_1_wrrout;
  wire [3:0] ALUopp, interrupt_stuff_1_rabcdout, interrupt_stuff_1_wabcdout, interrupt_stuff_1_wracc_tmpout,
       interrupt_stuff_1_wrrout, IR_q, IR_q_2, jumps_1_rabcdout, jumps_1_wabcdout, jumps_1_wracc_tmpout,
       jumps_1_wrrout, load_store_address_1_rabcdout, load_store_address_1_wabcdout,
       load_store_address_1_wracc_tmpout, load_store_address_1_wrrout, operations_1_rabcdout,
       operations_1_wabcdout, operations_1_wracc_tmpout, operations_1_wrrout, register_4_q,
       stackstuff_1_rabcdout, stackstuff_1_wabcdout, stackstuff_1_wracc_tmpout, stackstuff_1_wrrout,
       transfers_1_rabcdout, transfers_1_wabcdout, transfers_1_wracc_tmpout, transfers_1_wrrout;
  wire [7:0] A_q, ALUflags, B_q, C_q, controlled_buffer_5_out, counter_1_q, D_q, multiplexer_3_out,
       multiplexer_4_out, or_4_out, or_6_out, pull_resistor_6_node, pull_resistor_7_node,
       pull_resistor_10_node, pull_resistor_11_node, pull_resistor_12_node, pull_resistor_13_node,
       pull_resistor_14_node, pull_resistor_15_node, pull_resistor_16_node, register_1_q;
  wire [12:0] jumps_1_stepsout, load_store_address_1_stepsout, load_store_imediate_1_stepsout,
       operations_1_stepsout, stackstuff_1_stepsout, stepper_1_out_20, transfers_1_stepsout;
  wire [15:0] counter_2_q, multiplexer_2_out, or_3_out, pull_resistor_2_node, pull_resistor_3_node,
       pull_resistor_4_node, register_2_q, register_3_q;

  Register register_1 (.D(or_4_out), .en(WADDhigh), .clk(CLK_IN), .Q(register_1_q));  // open: clr
  Register #(.width(16)) register_2 (.D(counter_2_q), .en(storeADD), .clk(CLK_IN), .Q(register_2_q));  // open: clr
  Register #(.width(16)) register_3 (
    .D({register_1_q, or_4_out}), .en(load_interrupt_address), .clk(CLK_IN), .Q(register_3_q));  // open: clr
  or or_1 (or_1_out, stepper_1_out_7, load_store_imediate_1_increnentrout);
  and and_1 (and_1_out, or_1_out, not_2_out);
  Pull_Resistor pull_resistor_1 (.node(pull_resistor_1_node));
  or or_2 (or_2_out, loadADD, WADDlow, interrupt_address);
  assign pull_resistor_1_node = not_1_out ? or_2_out : 1'bz;  // Controlled_Buffer controlled_buffer_1
  not not_1 (not_1_out, load_interrupt_address);
  Pull_Resistor pull_resistor_2 (.node(pull_resistor_2_node));
  assign pull_resistor_2_node = loadADD ? register_2_q : 16'bz;  // Controlled_Buffer controlled_buffer_2
  Pull_Resistor pull_resistor_3 (.node(pull_resistor_3_node));
  assign pull_resistor_3_node = WADDlow ? {register_1_q, or_4_out} : 16'bz;  // Controlled_Buffer controlled_buffer_3
  not not_2 (not_2_out, comparator_1_eq);
  not not_3 (not_3_out, decrementSTACK);
  Counter #(.ongoal("stay")) counter_1 (
    .count(incrementSTACK), .Q(counter_1_q), .up(not_3_out), .clk(CLK_IN));  // open: load, D, carry, clr
  Counter #(.max('hffff), .width(16)) counter_2 (
    .load(pull_resistor_1_node), .D(or_3_out), .count(and_1_out), .Q(counter_2_q), .clk(CLK_IN));  // open: carry, up, clr
  assign or_3_out = pull_resistor_2_node | pull_resistor_4_node | pull_resistor_3_node;  // OR_Gate or_3, 16 bits wide
  Pull_Resistor pull_resistor_4 (.node(pull_resistor_4_node));
  assign pull_resistor_4_node = interrupt_address ? register_3_q : 16'bz;  // Controlled_Buffer controlled_buffer_4
  T_Flip_Flop t_ff_1 (.T(toggleSTACK), .clk(CLK_IN), .Qn(t_ff_1_qn));  // open: Q, reset, preset
  Multiplexer #(.width(16)) multiplexer_1 (
    .in0({{8{1'b0}}, counter_1_q}), .in1(counter_2_q), .out(Address), .sel(t_ff_1_qn));
  Multiplexer #(.width(16)) multiplexer_2 (
    .in0(counter_2_q), .in1(register_2_q), .out(multiplexer_2_out), .sel(ADDselect));
  Multiplexer #(.width(8)) multiplexer_3 (
    .in0(multiplexer_2_out[7:0]), .in1(multiplexer_2_out[15:8]), .out(multiplexer_3_out), .sel(RADD_lh[1]));
  assign controlled_buffer_5_out = RSP ? counter_1_q : 8'bz;  // Controlled_Buffer controlled_buffer_5
  Pull_Resistor pull_resistor_5 (.node(controlled_buffer_5_out));
  Pull_Resistor pull_resistor_6 (.node(pull_resistor_6_node));
  assign pull_resistor_6_node = RADD_lh[0] ? multiplexer_3_out : 8'bz;  // Controlled_Buffer controlled_buffer_6
  assign or_4_out = Data_Output | pull_resistor_7_node;  // OR_Gate or_4, 8 bits wide
  Button button_1 (.out(button_1_out));
  or or_5 (or_5_out, and_2_out, load_store_imediate_1_resetout);
  and and_2 (and_2_out, CLK_IN, nor_1_out, stepper_1_out_20[12]);
  Register IR (.D(multiplexer_4_out), .en(stepper_1_out_6), .clk(CLK_IN), .Q({IR_q_2, IR_q}));  // open: clr
  assign or_6_out = controlled_buffer_5_out | pull_resistor_6_node | pull_resistor_7_node | Data_Input;  // OR_Gate or_6, 8 bits wide
  Pull_Resistor pull_resistor_7 (.node(pull_resistor_7_node));
  Pull_Resistor pull_resistor_8 (.node(pull_resistor_8_node));
  stepper stepper_1 (
    .CLK(CLK_IN), .Reset_Manual(button_1_out), .Enable(Enable), .Reset(or_5_out), .out_6(stepper_1_out_6),
    .out_7(stepper_1_out_7), .out_8(stepper_1_out_20[12]), .out_9(stepper_1_out_20[11]),
    .out_10(stepper_1_out_20[10]), .out_11(stepper_1_out_20[9]), .out_12(stepper_1_out_20[8]),
    .out_13(stepper_1_out_20[7]), .out_14(stepper_1_out_20[6]), .out_15(stepper_1_out_20[5]),
    .out_16(stepper_1_out_20[4]), .out_17(stepper_1_out_20[3]), .out_18(stepper_1_out_20[2]),
    .out_19(stepper_1_out_20[1]), .out_20(stepper_1_out_20[0]), .Reset_2(pull_resistor_8_node));  // open: out_21
  nor nor_1 (nor_1_out, IR_q_2[3], IR_q_2[2], IR_q_2[1], IR_q_2[0], IR_q[3], IR_q[2], IR_q[1], IR_q[0]);
  or or_7 (read_ram, stepper_1_out_6, RR);
  or or_8 (RR, load_store_imediate_1_wrrout[2], Write);
  Multiplexer #(.width(8)) multiplexer_4 (.in0(or_6_out), .in1(8'hc0), .out(multiplexer_4_out), .sel(and_4_out));
  or or_9 (RSP, load_store_imediate_1_rsp, load_store_address_1_rsp);
  load_store_imediate load_store_imediate_1 (
    .WRrOUT({write_ram, load_store_imediate_1_wrrout}), .WRacc_tmpOUT({WACC, RACC, WTMP, RTMP}),
    .RabcdOUT({RA, RB, RC, RD}), .WabcdOUT({WA, WB, WC, WD}), .stepsIN(stepper_1_out_20),
    .resetOUT(load_store_imediate_1_resetout), .increnentRout(load_store_imediate_1_increnentrout),
    .RSP(load_store_imediate_1_rsp), .SelectRADD_lh(load_store_imediate_1_radd[1]),
    .RADD(load_store_imediate_1_radd[0]), .opcode({IR_q_2, IR_q}), .WRrIN(transfers_1_wrrout),
    .WRacc_tmpIN(transfers_1_wracc_tmpout), .RabcdIN(transfers_1_rabcdout), .WabcdIN(transfers_1_wabcdout),
    .stepsOUT(load_store_imediate_1_stepsout), .resetIN(transfers_1_resetout),
    .increnentRin(transfers_1_increnentrout));  // open: load
  transfers transfers_1 (
    .WRrOUT(transfers_1_wrrout), .WRacc_tmpOUT(transfers_1_wracc_tmpout), .RabcdOUT(transfers_1_rabcdout),
    .WabcdOUT(transfers_1_wabcdout), .stepsIN(load_store_imediate_1_stepsout),
    .resetOUT(transfers_1_resetout), .increnentRout(transfers_1_increnentrout), .in_8({IR_q_2, IR_q}),
    .WRrIN(jumps_1_wrrout), .WRacc_tmpIN(jumps_1_wracc_tmpout), .RabcdIN(jumps_1_rabcdout),
    .WabcdIN(jumps_1_wabcdout), .stepsOUT(transfers_1_stepsout), .resetIN(jumps_1_resetout),
    .increnentRin(jumps_1_increnentrout));
  or or_10 (or_10_out, comparator_1_gt, comparator_1_lt);
  Comparator comparator_1 (
    .a({IR_q_2, IR_q}), .b(8'hc0), .gt(comparator_1_gt), .eq(comparator_1_eq), .lt(comparator_1_lt));
  T_Flip_Flop t_ff_2 (
    .T(and_3_out), .clk(CLK_IN), .Qn(t_ff_2_qn), .reset(stackstuff_1_toggle_interrupt_signal));  // open: Q, preset
  and and_3 (and_3_out, comparator_1_eq, Interrupt);
  assign Data_Output = or_6_out | pull_resistor_7_node;  // OR_Gate or_11, 8 bits wide
  or or_12 (WADDlow, load_store_address_1_waddlow, stackstuff_1_wadd_high, jumps_1_waddlow, interrupt_stuff_1_load_add_low);
  or or_13 (WADDhigh, stackstuff_1_wadd_low, load_store_address_1_waddhigh, jumps_1_waddhigh, interrupt_stuff_1_load_add_high);
  and and_4 (and_4_out, or_10_out, Interrupt, t_ff_2_qn);
  Pull_Resistor pull_resistor_9 (.node(Data_Output));
  Register A (.D(Data_Output), .en(WA), .clk(CLK_IN), .Q(A_q));  // open: clr
  Pull_Resistor pull_resistor_10 (.node(pull_resistor_10_node));
  Pull_Resistor pull_resistor_11 (.node(pull_resistor_11_node));
  Pull_Resistor pull_resistor_12 (.node(pull_resistor_12_node));
  Pull_Resistor pull_resistor_13 (.node(pull_resistor_13_node));
  assign pull_resistor_7_node = pull_resistor_10_node | pull_resistor_11_node | pull_resistor_12_node | pull_resistor_13_node | pull_resistor_14_node | pull_resistor_15_node | pull_resistor_16_node;  // OR_Gate or_14, 8 bits wide
  Pull_Resistor pull_resistor_14 (.node(pull_resistor_14_node));
  Pull_Resistor pull_resistor_15 (.node(pull_resistor_15_node));
  Pull_Resistor pull_resistor_16 (.node(pull_resistor_16_node));
  jumps jumps_1 (
    .WRrOUT(jumps_1_wrrout), .WRacc_tmpOUT(jumps_1_wracc_tmpout), .RabcdOUT(jumps_1_rabcdout),
    .WabcdOUT(jumps_1_wabcdout), .stepsIN(transfers_1_stepsout), .resetOUT(jumps_1_resetout),
    .increnentRout(jumps_1_increnentrout), .ALUflags(ALUflags), .WADDhigh(jumps_1_waddhigh),
    .WADDlow(jumps_1_waddlow), .in_10({IR_q_2, IR_q}), .interrupt(Interrupt), .WRrIN(operations_1_wrrout),
    .WRacc_tmpIN(operations_1_wracc_tmpout), .RabcdIN(operations_1_rabcdout),
    .WabcdIN(operations_1_wabcdout), .stepsOUT(jumps_1_stepsout), .resetIN(operations_1_resetout),
    .increnentRin(operations_1_increnentrout));  // open: jump
  assign pull_resistor_10_node = RA ? A_q : 8'bz;  // Controlled_Buffer controlled_buffer_7
  operations operations_1 (
    .WRrOUT(operations_1_wrrout), .WRacc_tmpOUT(operations_1_wracc_tmpout), .RabcdOUT(operations_1_rabcdout),
    .WabcdOUT(operations_1_wabcdout), .stepsIN(jumps_1_stepsout), .resetOUT(operations_1_resetout),
    .increnentRout(operations_1_increnentrout), .ALUset(ALUset), .ALUcarry(ALUcarry), .ALUopp(ALUopp),
    .in_8({IR_q_2, IR_q}), .WRrIN(load_store_address_1_wrrout),
    .WRacc_tmpIN(load_store_address_1_wracc_tmpout), .RabcdIN(load_store_address_1_rabcdout),
    .WabcdIN(load_store_address_1_wabcdout), .stepsOUT(operations_1_stepsout),
    .resetIN(load_store_address_1_resetout), .increnentRin(load_store_address_1_increnentrout));
  Register B (.D(Data_Output), .en(WB), .clk(CLK_IN), .Q(B_q));  // open: clr
  assign pull_resistor_11_node = RB ? B_q : 8'bz;  // Controlled_Buffer controlled_buffer_8
  Register C (.D(Data_Output), .en(WC), .clk(CLK_IN), .Q(C_q));  // open: clr
  assign or_15_out = load_store_address_1_radd_lh | load_store_imediate_1_radd;  // OR_Gate or_15, 2 bits wide
  load_store_address load_store_address_1 (
    .WRrOUT(load_store_address_1_wrrout), .WRacc_tmpOUT(load_store_address_1_wracc_tmpout),
    .RabcdOUT(load_store_address_1_rabcdout), .WabcdOUT(load_store_address_1_wabcdout),
    .stepsIN(operations_1_stepsout), .resetOUT(load_store_address_1_resetout),
    .increnentRout(load_store_address_1_increnentrout), .saveADD(storeADD), .loadADD(loadADD),
    .WADDlow(load_store_address_1_waddlow), .WADDhigh(load_store_address_1_waddhigh),
    .RSP(load_store_address_1_rsp), .RADD_lh(load_store_address_1_radd_lh), .ADDselect(ADDselect),
    .Write(load_store_address_1_write), .read(load_store_address_1_read),
    .load_interrupt_address(load_store_address_1_load_interrupt_address), .opcode({IR_q_2, IR_q}),
    .WRrIN(stackstuff_1_wrrout), .WRacc_tmpIN(stackstuff_1_wracc_tmpout), .RabcdIN(stackstuff_1_rabcdout),
    .WabcdIN(stackstuff_1_wabcdout), .stepsOUT(load_store_address_1_stepsout),
    .resetIN(stackstuff_1_resetout), .incrementIN(stackstuff_1_incrementout));
  or or_16 (Write, load_store_address_1_write, and_6_out);
  assign pull_resistor_12_node = RC ? C_q : 8'bz;  // Controlled_Buffer controlled_buffer_9
  Register D (.D(Data_Output), .en(WD), .clk(CLK_IN), .Q(D_q));  // open: clr
  assign pull_resistor_13_node = RD ? D_q : 8'bz;  // Controlled_Buffer controlled_buffer_10
  assign RADD_lh = or_15_out | stackstuff_1_radd_lh;  // OR_Gate or_17, 2 bits wide
  or or_18 (Read, load_store_address_1_read, interrupt_stuff_1_read);
  or or_19 (load_interrupt_address, interrupt_stuff_1_load_interrupt_address, load_store_address_1_load_interrupt_address);
  stackSTUFF stackstuff_1 (
    .WRrOUT(stackstuff_1_wrrout), .WRacc_tmpOUT(stackstuff_1_wracc_tmpout), .RabcdOUT(stackstuff_1_rabcdout),
    .WabcdOUT(stackstuff_1_wabcdout), .stepsIN(load_store_address_1_stepsout),
    .resetOUT(stackstuff_1_resetout), .incrementOUT(stackstuff_1_incrementout), .toggleSTACK(toggleSTACK),
    .incrementSTACK(incrementSTACK), .decrementSTACK(decrementSTACK), .RADD_lh(stackstuff_1_radd_lh),
    .WADD_low(stackstuff_1_wadd_low), .WADD_high(stackstuff_1_wadd_high),
    .interrupt_address(interrupt_address), .opcode({IR_q_2, IR_q}),
    .toggle_interrupt_signal(stackstuff_1_toggle_interrupt_signal), .WRrIN(interrupt_stuff_1_wrrout),
    .WRacc_tmpIN(interrupt_stuff_1_wracc_tmpout), .RabcdIN(interrupt_stuff_1_rabcdout),
    .WabcdIN(interrupt_stuff_1_wabcdout), .stepsOUT(stackstuff_1_stepsout),
    .resetIN(interrupt_stuff_1_resetout), .incrementIN(interrupt_stuff_1_incrementout));
  ALU alu_1 (
    .CLK(CLK_IN), .BUSout(pull_resistor_14_node), .BUSin(Data_Output), .ALUset(ALUset), .ALUcarry(ALUcarry),
    .ALUopp(ALUopp), .WACC(WACC), .RACC(RACC), .WTMP(WTMP), .RTMP(RTMP), .ALUflags(ALUflags));
  interrupt_stuff interrupt_stuff_1 (
    .WRrOUT(interrupt_stuff_1_wrrout), .WRacc_tmpOUT(interrupt_stuff_1_wracc_tmpout),
    .RabcdOUT(interrupt_stuff_1_rabcdout), .WabcdOUT(interrupt_stuff_1_wabcdout),
    .stepsIN(stackstuff_1_stepsout), .resetOUT(interrupt_stuff_1_resetout),
    .incrementOUT(interrupt_stuff_1_incrementout), .load_add_low(interrupt_stuff_1_load_add_low),
    .load_add_high(interrupt_stuff_1_load_add_high),
    .load_interrupt_address(interrupt_stuff_1_load_interrupt_address), .read(interrupt_stuff_1_read),
    .in_8({IR_q_2, IR_q}), .resetIN(and_7_out), .incrementIN(and_6_out));  // open: WRrIN, WRacc_tmpIN, RabcdIN, WabcdIN, stepsOUT
  and and_5 (and_5_out, IR_q_2[3], IR_q_2[2], IR_q_2[1], IR_q_2[0]);
  Register #(.width(4)) register_4 (.D(Interrupt_port), .en(Interrupt), .clk(CLK_IN), .Q(register_4_q));  // open: clr
  and and_6 (and_6_out, and_5_out, stepper_1_out_20[12]);
  and and_7 (and_7_out, and_5_out, stepper_1_out_20[11]);
  Multiplexer #(.width(4)) multiplexer_5 (.in0(IR_q), .in1(register_4_q), .out(controll), .sel(and_8_out));
  and and_8 (and_8_out, Read, ~and_9_out);  // AND_Gate
  and and_9 (and_9_out, IR_q_2[3], ~IR_q_2[2], IR_q_2[1], IR_q_2[0]);  // AND_Gate

  assign CLK_OUT = CLK_IN;

  // Other names for the same wires on the sheet: WR = write_ram

  // Notes on the sheet:
  //   Enable: initial=0x1
endmodule

module interrupt_stuff (
  input  [3:0] WRrIN,
  input  [3:0] WRacc_tmpIN,
  input  [3:0] RabcdIN,
  input  [3:0] WabcdIN,
  input  [12:0] stepsIN,
  input  resetIN,
  input  incrementIN,
  input  [7:0] in_8,
  output [3:0] WRrOUT,
  output [3:0] WRacc_tmpOUT,
  output [3:0] RabcdOUT,
  output [3:0] WabcdOUT,
  output load_add_low,
  output [12:0] stepsOUT,
  output load_interrupt_address,
  output load_add_high,
  output read,
  output resetOUT,
  output incrementOUT
);

  wire and_1_out, and_4_out, and_5_out, and_7_out, and_8_out, or_7_out, or_9_out, or_12_out, or_13_out,
       or_14_out;
  wire [3:0] pull_resistor_7_node;

  or or_1 (resetOUT, or_7_out, resetIN);
  Pull_Resistor pull_resistor_1 (.node(resetIN));
  or or_2 (incrementOUT, incrementIN, or_9_out);
  Pull_Resistor pull_resistor_2 (.node(incrementIN));
  assign WRrOUT = WRrIN | pull_resistor_7_node;  // OR_Gate or_3, 4 bits wide
  assign WRacc_tmpOUT = WRacc_tmpIN;  // OR_Gate or_4, 4 bits wide OR_Gate
  assign RabcdOUT = RabcdIN;  // OR_Gate or_5, 4 bits wide OR_Gate
  assign WabcdOUT = WabcdIN;  // OR_Gate or_6, 4 bits wide OR_Gate
  Pull_Resistor pull_resistor_3 (.node(WRrIN));
  Pull_Resistor pull_resistor_4 (.node(WRacc_tmpIN));
  Pull_Resistor pull_resistor_5 (.node(RabcdIN));
  Pull_Resistor pull_resistor_6 (.node(WabcdIN));
  or or_7 (or_7_out, or_12_out, and_1_out);
  Pull_Resistor pull_resistor_7 (.node(pull_resistor_7_node));
  and and_1 (and_1_out, stepsIN[10], and_4_out);
  or or_8 (pull_resistor_7_node[2], load_add_low, load_add_high);
  or or_9 (or_9_out, or_13_out, load_add_high, load_add_low);
  and and_2 (load_add_low, stepsIN[11], and_4_out);
  and and_3 (load_add_high, stepsIN[12], and_4_out);
  and and_4 (and_4_out, in_8[7], in_8[6], ~in_8[5], ~in_8[4], ~in_8[3], ~in_8[2], in_8[1], in_8[0]);  // AND_Gate
  buf or_10 (load_interrupt_address, load_add_low);  // OR_Gate
  buf or_11 (pull_resistor_7_node[3], read);  // OR_Gate
  and and_5 (and_5_out, stepsIN[11], read);
  buf or_12 (or_12_out, and_5_out);  // OR_Gate
  buf or_13 (or_13_out, read);  // OR_Gate
  and and_6 (read, stepsIN[12], or_14_out);
  or or_14 (or_14_out, and_7_out, and_8_out);
  and and_7 (and_7_out, in_8[7], in_8[6], ~in_8[5], ~in_8[4], ~in_8[3], ~in_8[2], ~in_8[1], in_8[0]);  // AND_Gate
  and and_8 (and_8_out, in_8[7], ~in_8[6], in_8[5], in_8[4]);  // AND_Gate

  assign stepsOUT = stepsIN;
endmodule
