// Logisim project G116B.circ as structural Verilog: 5 circuits, main circuit main
module main (
  output [6:0] out_1
);

  wire basic_terminal_1_read_out, basic_terminal_1_read_term, basic_terminal_1_term_sel,
       basic_terminal_1_write_out, basic_terminal_1_write_term, clock_1_out, clock_2_out, clock_3_out,
       clock_4_out, clock_5_out, CPU_0_read, CPU_0_write, Interrupt_out, keyboard_1_avail,
       Maskable_Interrupt_out, not_1_out, or_1_out, reset_keyboard_out, reset_TTY_out, t_ff_1_qn, xor_1_out;
  wire [6:0] bit_extender_1_out;
  wire [7:0] CPU_0_data_out, CPU_0_data_out_2, multiplexer_1_out;
  wire [15:0] basic_terminal_1_address_out, basic_terminal_1_data_out, basic_terminal_1_term_data_out,
       CPU_0_address, multiplexer_2_out, RAM_0_dout;

  Button Interrupt (.out(Interrupt_out));
  Clock clock_1 (.out(clock_1_out));
  or or_1 (or_1_out, keyboard_1_avail, Maskable_Interrupt_out);
  Button Maskable_Interrupt (.out(Maskable_Interrupt_out));
  Clock clock_2 (.out(clock_2_out));
  not not_1 (not_1_out, clock_2_out);
  T_Flip_Flop t_ff_1 (.T(basic_terminal_1_write_term), .clk(xor_1_out), .Qn(t_ff_1_qn));  // open: Q, reset, preset
  xor xor_1 (xor_1_out, clock_2_out, not_1_out);
  Multiplexer #(.width(8)) multiplexer_1 (
    .in0(CPU_0_data_out), .in1(CPU_0_data_out_2), .out(multiplexer_1_out), .sel(t_ff_1_qn));
  G116B CPU_0 (
    .CLK_in(clock_1_out), .DATA_in(multiplexer_2_out), .INT(Interrupt_out), .INT_maskable(or_1_out),
    .Address(CPU_0_address), .write(CPU_0_write), .read(CPU_0_read),
    .DATA_out({CPU_0_data_out_2, CPU_0_data_out}));  // open: ENABLE_not
  Bit_Extender #(.out_width(7), .\type ("zero")) bit_extender_1 (.in(multiplexer_1_out), .out(bit_extender_1_out));
  TTY tty_1 (.data(bit_extender_1_out), .clk(xor_1_out), .we(basic_terminal_1_write_term), .clr(reset_TTY_out));
  Clock clock_3 (.out(clock_3_out));
  Clock clock_4 (.out(clock_4_out));
  Keyboard keyboard_1 (
    .clk(clock_3_out), .re(basic_terminal_1_read_term), .clr(reset_keyboard_out), .avail(keyboard_1_avail),
    .data(out_1));
  Button reset_keyboard (.out(reset_keyboard_out));
  Multiplexer #(.width(16)) multiplexer_2 (
    .in0(RAM_0_dout), .in1(basic_terminal_1_term_data_out), .out(multiplexer_2_out),
    .sel(basic_terminal_1_term_sel));
  BASIC_TERMINAL basic_terminal_1 (
    .CLK_in(clock_4_out), .ADDRESS_in(CPU_0_address), .write_in(CPU_0_write), .read_in(CPU_0_read),
    .DATA_in({CPU_0_data_out_2, CPU_0_data_out}), .SEL_ADDRESS_in({16{1'b1}}), .KEYBOARD_in(out_1),
    .TERM_DATA_out(basic_terminal_1_term_data_out), .ADDRESS_out(basic_terminal_1_address_out),
    .write_out(basic_terminal_1_write_out), .read_out(basic_terminal_1_read_out),
    .DATA_out(basic_terminal_1_data_out), .TERM_SEL(basic_terminal_1_term_sel),
    .read_term(basic_terminal_1_read_term), .write_term(basic_terminal_1_write_term));
  Button reset_TTY (.out(reset_TTY_out));
  RAM #(.addrWidth(16), .asyncread("true"), .dataWidth(16), .\type ("nonvolatile")) RAM_0 (
    .addr(basic_terminal_1_address_out), .we(basic_terminal_1_write_out), .oe(basic_terminal_1_read_out),
    .clk(clock_5_out), .din(basic_terminal_1_data_out), .dout(RAM_0_dout));
  Clock clock_5 (.out(clock_5_out));
endmodule

module G116B (
  input  ENABLE_not,
  input  CLK_in,
  input  [15:0] DATA_in,
  input  INT,
  input  INT_maskable,
  output [15:0] Address,
  output write,
  output read,
  output [15:0] DATA_out
);

  wire access_INT, addr_hold_wr, addr_sel_en, alt_alt_data, alt_data, and_1_out, and_3_out, and_4_out,
       and_5_out, and_6_out, and_7_out, and_8_out, and_9_out, and_10_out, and_11_out, and_12_out, and_13_out,
       and_14_out, and_15_out, and_16_out, and_17_out, and_18_out, and_19_out, and_22_out, and_23_out,
       and_24_out, and_25_out, and_27_out, and_29_out, and_30_out, and_31_out, and_32_out, and_33_out,
       and_34_out, and_35_out, and_36_out, and_37_out, and_38_out, and_39_out, CLK, comparator_1_eq,
       comparator_2_eq, comparator_3_eq, comparator_4_eq, comparator_5_eq, comparator_6_eq, comparator_7_eq,
       comparator_8_eq, comparator_9_eq, comparator_9_gt, comparator_9_lt, comparator_10_gt,
       comparator_10_lt, comparator_11_eq, comparator_12_eq, comparator_13_eq, D4, d_ff_1_qn, Data_in_NOTen,
       delay_in, delay_out, demultiplexer_1_out0, demultiplexer_1_out1, demultiplexer_1_out2,
       demultiplexer_1_out3, demultiplexer_1_out4, demultiplexer_1_out5, demultiplexer_1_out6,
       demultiplexer_1_out7, demultiplexer_1_out8, demultiplexer_1_out9, demultiplexer_1_out10,
       demultiplexer_1_out11, demultiplexer_1_out12, demultiplexer_1_out13, demultiplexer_1_out14,
       demultiplexer_1_out15, demultiplexer_2_out0, demultiplexer_2_out1, demultiplexer_2_out2,
       demultiplexer_2_out3, demultiplexer_2_out4, demultiplexer_2_out5, demultiplexer_2_out6,
       demultiplexer_2_out7, demultiplexer_2_out8, demultiplexer_2_out9, demultiplexer_2_out10,
       demultiplexer_2_out11, demultiplexer_2_out12, demultiplexer_2_out13, demultiplexer_2_out14,
       demultiplexer_2_out15, G0_only, G1_use, G10, G11, G12, G13, halt, halt_INT_control,
       halt_maskINT_control, INT_mask, INT_t, interrupt, IR_wr, load, load_PC, mask, multiplexer_5_out,
       nor_1_out, nor_2_out, not_1_out, not_2_out, not_5_out, not_6_out, or_1_out, or_2_out, or_4_out,
       or_5_out, or_6_out, or_7_out, or_10_out, or_11_out, or_12_out, or_13_out, priviledged,
       pull_resistor_6_node, pull_resistor_7_node, pull_resistor_13_node, pull_resistor_16_node,
       pull_resistor_22_node, pull_resistor_36_node, pull_resistor_46_node, s_r_ff_4_qn, SOFT_INT, soft_mask,
       stack_EN, stack_inc, stack_SyEN, store_status, T0_INT, T0_mask, T1_INT, T1_mask;
  wire [1:0] G, G1;
  wire [1:1] pull_resistor_37_node;
  wire [2:0] addr_sel;
  wire [3:0] D0, D1, D1v, pull_resistor_11_node, pull_resistor_38_node, pull_resistor_39_node;
  wire [7:0] multiplexer_10_out, or_14_out;
  wire [7:1] and_40_out;
  wire [14:12] IR;
  wire [15:0] adder_1_out, address_t, alt_alt_datadata, and_20_out, Data_in_t, INT_Vector_q,
       multiplexer_1_out, multiplexer_2_out, multiplexer_8_out, multiplexer_9_out, multiplexer_11_out,
       multiplexer_12_out, negator_1_out, not_4_out, or_8_out, PC_q, pull_resistor_9_node,
       pull_resistor_12_node, R0_q, R1, R15_q, register_2_q, register_3_q, register_4_q, register_5_q,
       register_6_q, register_7_q, register_8_q, register_9_q, register_10_q, register_11_q, register_12_q,
       register_13_q, register_14_q, register_15_q, register_16_q, register_17_q, register_18_q,
       register_19_q, register_20_q, register_21_q, register_22_q, register_23_q, shifter_1_out,
       shifter_2_out, shifter_3_out, shifter_4_out, SP_q, Status_q, subtractor_1_out, SySP_q, T0_q, T1_q,
       xor_1_out;
  wire [15:4] Control_q;

  Comparator #(.width(16)) comparator_1 (
    .a({D4, IR, G1, G, D1, D0}), .b(16'hb943), .eq(comparator_1_eq));  // open: gt, lt
  nor nor_1 (nor_1_out, halt_maskINT_control, ~halt);  // NOR_Gate
  Pull_Resistor pull_resistor_1 (.node(CLK_in));
  Pull_Resistor pull_resistor_2 (.node(DATA_in));
  nor nor_2 (nor_2_out, ~halt, halt_INT_control);  // NOR_Gate
  Pull_Resistor pull_resistor_3 (.node(INT_maskable));
  or or_1 (or_1_out, comparator_1_eq, nor_1_out);
  Pull_Resistor pull_resistor_4 (.node(ENABLE_not));
  Pull_Resistor pull_resistor_5 (.node(INT));
  Pull_Resistor pull_resistor_6 (.node(pull_resistor_6_node));
  or or_2 (or_2_out, nor_2_out, comparator_1_eq);
  and and_1 (and_1_out, INT_mask, INT_maskable);
  Pull_Resistor pull_resistor_7 (.node(pull_resistor_7_node));
  and and_2 (CLK, ~ENABLE_not, CLK_in, halt);  // AND_Gate
  Multiplexer #(.width(16)) multiplexer_1 (.in0(DATA_in), .in1(16'hb943), .out(multiplexer_1_out), .sel(interrupt));
  Multiplexer #(.width(16)) multiplexer_2 (.in0(DATA_in), .in1(R1), .out(multiplexer_2_out), .sel(alt_data));
  Pull_Resistor pull_resistor_8 (.node(alt_data));
  S_R_Flip_Flop #(.trigger("falling")) s_r_ff_1 (
    .S(pull_resistor_6_node), .R(or_2_out), .clk(CLK), .Q(INT_t), .preset(INT));  // open: reset, Qn
  S_R_Flip_Flop #(.trigger("falling")) s_r_ff_2 (
    .S(pull_resistor_7_node), .R(or_1_out), .clk(CLK), .Q(INT_mask), .preset(and_1_out));  // open: reset, Qn
  and and_3 (and_3_out, halt, halt_INT_control);
  and and_4 (and_4_out, INT_mask, and_5_out);
  and and_5 (and_5_out, halt, halt_maskINT_control);
  Pull_Resistor pull_resistor_9 (.node(pull_resistor_9_node));
  not not_1 (not_1_out, Data_in_NOTen);
  Register #(.width(16)) u_IR (
    .D(pull_resistor_9_node), .en(not_2_out), .clk(CLK_in), .Q({D4, IR, G1, G, D1, D0}));  // open: clr
  assign pull_resistor_9_node = not_1_out ? multiplexer_1_out : 16'bz;  // Controlled_Buffer controlled_buffer_1
  not not_2 (not_2_out, IR_wr);
  Multiplexer #(.width(16)) multiplexer_3 (
    .in0(multiplexer_2_out), .in1(alt_alt_datadata), .out(Data_in_t), .sel(alt_alt_data));
  and and_6 (and_6_out, and_3_out, INT_t);
  or or_3 (interrupt, and_6_out, and_4_out, access_INT);
  T_Flip_Flop delay (.T(delay_in), .clk(CLK), .Q(delay_out));  // open: Qn, reset, preset
  Register #(.width(16)) register_1 (.D(Data_in_t), .en(addr_hold_wr), .clk(CLK), .Q(address_t));  // open: clr
  Pull_Resistor pull_resistor_10 (.node(addr_sel));
  Comparator #(.mode("unsigned"), .width(3)) comparator_2 (.a(IR), .b(3'b011), .eq(comparator_2_eq));  // open: gt, lt
  Comparator #(.mode("unsigned"), .width(3)) comparator_3 (.a(IR), .b(3'b011), .eq(comparator_3_eq));  // open: gt, lt
  Comparator #(.mode("unsigned"), .width(3)) comparator_4 (.a(IR), .b(3'b100), .eq(comparator_4_eq));  // open: gt, lt
  Comparator #(.mode("unsigned"), .width(3)) comparator_5 (.a(IR), .b(3'b011), .eq(comparator_5_eq));  // open: gt, lt
  Comparator #(.mode("unsigned"), .width(3)) comparator_6 (.a(IR), .b(3'b000), .eq(comparator_6_eq));  // open: gt, lt
  Comparator #(.mode("unsigned"), .width(3)) comparator_7 (.a(IR), .b(3'b001), .eq(comparator_7_eq));  // open: gt, lt
  Comparator #(.mode("unsigned"), .width(3)) comparator_8 (.a(IR), .b(3'b010), .eq(comparator_8_eq));  // open: gt, lt
  and and_7 (and_7_out, comparator_3_eq, D4, G1[1], ~G1[0]);  // AND_Gate
  and and_8 (and_8_out, comparator_4_eq, D4);
  and and_9 (and_9_out, comparator_5_eq, D4, G1[1], ~G1[0]);  // AND_Gate
  and and_10 (and_10_out, comparator_6_eq, ~G1[0], ~G1[1]);  // AND_Gate
  and and_11 (and_11_out, comparator_7_eq, D4);
  and and_12 (and_12_out, comparator_8_eq, D4);
  Decoder #(.disabled("Z"), .select(2)) decoder_1 (
    .out0(G10), .out1(G11), .out2(G12), .out3(G13), .sel(G), .en(and_12_out));
  and and_13 (and_13_out, comparator_2_eq, D4, ~G1[1]);  // AND_Gate
  and and_14 (and_14_out, G1[1], comparator_2_eq, D4);
  Pull_Resistor pull_resistor_11 (.node(pull_resistor_11_node));
  assign pull_resistor_11_node = and_18_out ? D1 : 4'bz;  // Controlled_Buffer controlled_buffer_2
  and and_15 (and_15_out, and_7_out, ~D1[0], ~D1[1], D1[2], ~D1[3]);  // AND_Gate
  Comparator #(.width(16)) comparator_9 (
    .a(DATA_out), .b(R1), .gt(comparator_9_gt), .eq(comparator_9_eq), .lt(comparator_9_lt));
  Comparator #(.mode("unsigned"), .width(16)) comparator_10 (
    .a(DATA_out), .b(R1), .gt(comparator_10_gt), .lt(comparator_10_lt));  // open: eq
  Comparator #(.mode("unsigned"), .width(16)) comparator_11 (
    .a(DATA_out), .b(pull_resistor_12_node), .eq(comparator_11_eq));  // open: gt, lt
  Pull_Resistor pull_resistor_12 (.node(pull_resistor_12_node));
  and and_16 (and_16_out, D1[0], ~D1[1], D1[2], ~D1[3], and_9_out);  // AND_Gate
  or or_4 (or_4_out, G1[0], G1[1]);
  or or_5 (or_5_out, or_4_out, or_6_out);
  or or_6 (or_6_out, G[0], G[1]);
  and and_17 (and_17_out, and_10_out, D4);
  Decoder #(.disabled("Z"), .select(2)) decoder_2 (
    .out0(G10), .out1(G11), .out2(G12), .out3(G13), .sel(G1), .en(and_11_out));
  and and_18 (and_18_out, and_14_out, ~D1[2], ~D1[3]);  // AND_Gate
  assign stack_inc = pull_resistor_11_node[1] ? pull_resistor_11_node[1] : 1'bz;  // Controlled_Buffer controlled_buffer_3
  assign write = pull_resistor_11_node[1] ? pull_resistor_11_node[1] : 1'bz;  // Controlled_Buffer controlled_buffer_4
  Pull_Resistor pull_resistor_13 (.node(pull_resistor_13_node));
  Pull_Resistor pull_resistor_14 (.node(stack_inc));
  assign stack_inc = and_15_out ? and_15_out : 1'bz;  // Controlled_Buffer controlled_buffer_5
  assign write = and_15_out ? and_15_out : 1'bz;  // Controlled_Buffer controlled_buffer_6
  assign load = and_15_out ? and_15_out : 1'bz;  // Controlled_Buffer controlled_buffer_7
  assign addr_sel = and_15_out ? 3'b011 : 3'bz;  // Controlled_Buffer controlled_buffer_8
  assign alt_data = and_15_out ? and_15_out : 1'bz;  // Controlled_Buffer controlled_buffer_9
  assign G11 = and_15_out ? and_15_out : 1'bz;  // Controlled_Buffer controlled_buffer_10
  Pull_Resistor pull_resistor_15 (.node(stack_SyEN));
  assign stack_SyEN = and_15_out ? and_15_out : 1'bz;  // Controlled_Buffer controlled_buffer_11
  Multiplexer #(.width(4)) multiplexer_4 (.in0(D1), .in1(4'b0010), .out(D1v), .sel(and_15_out));
  S_R_Flip_Flop s_r_ff_3 (
    .S(pull_resistor_16_node), .R(or_7_out), .clk(CLK_in), .Qn(halt), .preset(and_16_out));  // open: Q, reset
  Pull_Resistor pull_resistor_16 (.node(pull_resistor_16_node));
  or or_7 (or_7_out, INT_t, INT_mask);
  and and_19 (and_19_out, or_5_out, G1_use);
  Pull_Resistor pull_resistor_17 (.node(write));
  not not_3 (read, write);
  Pull_Resistor pull_resistor_18 (.node(DATA_out));
  Pull_Resistor pull_resistor_19 (.node(G1_use));
  assign G1_use = and_11_out ? and_11_out : 1'bz;  // Controlled_Buffer controlled_buffer_12
  assign load = and_11_out ? and_11_out : 1'bz;  // Controlled_Buffer controlled_buffer_13
  assign alt_data = and_11_out ? and_11_out : 1'bz;  // Controlled_Buffer controlled_buffer_14
  Pull_Resistor pull_resistor_20 (.node(G13));
  Pull_Resistor pull_resistor_21 (.node(G12));
  assign and_20_out = DATA_out & R1;  // AND_Gate and_20, 16 bits wide
  assign or_8_out = DATA_out | R1;  // OR_Gate or_8, 16 bits wide
  assign xor_1_out = DATA_out ^ R1;  // XOR_Gate xor_1, 16 bits wide
  assign not_4_out = ~DATA_out;  // NOT_Gate not_4, 16 bits wide
  Adder #(.width(16)) adder_1 (.a(DATA_out), .b(R1), .out(adder_1_out));  // open: cin, cout
  Subtractor #(.width(16)) subtractor_1 (.a(DATA_out), .b(R1), .out(subtractor_1_out));  // open: bin, bout
  Negator #(.width(16)) negator_1 (.in(DATA_out), .out(negator_1_out));
  Shifter #(.width(16)) shifter_1 (.in(DATA_out), .\dist (4'b0001), .out(shifter_1_out));
  Shifter #(.shift("lr"), .width(16)) shifter_2 (.in(DATA_out), .\dist (4'b0001), .out(shifter_2_out));
  Shifter #(.shift("rl"), .width(16)) shifter_3 (.in(DATA_out), .\dist (4'b0001), .out(shifter_3_out));
  Shifter #(.shift("rr"), .width(16)) shifter_4 (.in(DATA_out), .\dist (4'b0001), .out(shifter_4_out));
  S_R_Flip_Flop s_r_ff_4 (
    .S(pull_resistor_13_node), .R(and_15_out), .clk(CLK), .Qn(s_r_ff_4_qn), .preset(interrupt));  // open: Q, reset
  Pull_Resistor #(.pull(1)) pull_resistor_22 (.node(pull_resistor_22_node));
  Multiplexer #(.enable("true"), .select(4)) multiplexer_5 (
    .in0(pull_resistor_22_node), .in1(comparator_9_gt), .in2(comparator_9_eq), .in3(comparator_9_lt),
    .in4(comparator_10_gt), .in5(comparator_10_lt), .in6(comparator_11_eq), .in7(DATA_out[0]),
    .in8(DATA_out[15]), .out(multiplexer_5_out), .sel({G1, G}), .en(and_8_out));  // open: in9, in10, in11, in12, in13, in14, in15
  and and_21 (access_INT, priviledged, and_19_out);
  and and_22 (and_22_out, and_17_out, ~D1[2], ~D1[3]);  // AND_Gate
  and and_23 (and_23_out, and_17_out, D1[2], ~D1[3]);  // AND_Gate
  and and_24 (and_24_out, and_17_out, ~D1[2], D1[3]);  // AND_Gate
  and and_25 (and_25_out, and_17_out, D1[2], D1[3]);
  Pull_Resistor pull_resistor_23 (.node(G11));
  and and_26 (SOFT_INT, s_r_ff_4_qn, and_15_out);
  assign Data_in_NOTen = and_8_out ? and_8_out : 1'bz;  // Controlled_Buffer controlled_buffer_15
  assign G10 = and_8_out ? and_8_out : 1'bz;  // Controlled_Buffer controlled_buffer_16
  assign G0_only = and_8_out ? and_8_out : 1'bz;  // Controlled_Buffer controlled_buffer_17
  Pull_Resistor pull_resistor_24 (.node(G0_only));
  Pull_Resistor pull_resistor_25 (.node(load_PC));
  assign load_PC = multiplexer_5_out ? multiplexer_5_out : 1'bz;  // Controlled_Buffer controlled_buffer_18
  assign G1_use = and_17_out ? and_17_out : 1'bz;  // Controlled_Buffer controlled_buffer_19
  Pull_Resistor pull_resistor_26 (.node(load));
  assign load = and_22_out ? and_22_out : 1'bz;  // Controlled_Buffer controlled_buffer_20
  Pull_Resistor pull_resistor_27 (.node(Data_in_NOTen));
  assign Data_in_NOTen = and_22_out ? and_22_out : 1'bz;  // Controlled_Buffer controlled_buffer_21
  Pull_Resistor pull_resistor_28 (.node(Data_in_NOTen));
  assign Data_in_NOTen = and_24_out ? and_24_out : 1'bz;  // Controlled_Buffer controlled_buffer_22
  assign write = and_24_out ? and_24_out : 1'bz;  // Controlled_Buffer controlled_buffer_23
  Pull_Resistor pull_resistor_29 (.node(write));
  and and_27 (and_27_out, and_25_out, delay_out);
  Pull_Resistor pull_resistor_30 (.node(G10));
  Multiplexer #(.disabled("Z"), .enable("true"), .select(2), .width(16)) multiplexer_6 (
    .in0(and_20_out), .in1(or_8_out), .in2(xor_1_out), .in3(not_4_out), .out(alt_alt_datadata), .sel(G1),
    .en(and_12_out));
  Multiplexer #(.disabled("Z"), .enable("true"), .select(3), .width(16)) multiplexer_7 (
    .in0(adder_1_out), .in1(subtractor_1_out), .in2(negator_1_out), .in3(shifter_1_out), .in4(shifter_2_out),
    .in5(shifter_3_out), .in6(shifter_4_out), .out(alt_alt_datadata), .sel({G1[0], G}), .en(and_13_out));  // open: in7
  assign G1_use = and_18_out ? and_18_out : 1'bz;  // Controlled_Buffer controlled_buffer_24
  assign addr_sel_en = and_18_out ? and_18_out : 1'bz;  // Controlled_Buffer controlled_buffer_25
  assign addr_sel = stack_EN ? 3'b010 : 3'bz;  // Controlled_Buffer controlled_buffer_26
  and and_28 (stack_EN, ~pull_resistor_11_node[0], and_18_out);  // AND_Gate
  and and_29 (and_29_out, pull_resistor_11_node[0], and_18_out);
  assign stack_SyEN = and_29_out ? and_29_out : 1'bz;  // Controlled_Buffer controlled_buffer_27
  assign addr_sel = and_29_out ? 3'b011 : 3'bz;  // Controlled_Buffer controlled_buffer_28
  and and_30 (and_30_out, ~pull_resistor_11_node[1], and_18_out);  // AND_Gate
  assign addr_sel = and_31_out ? 3'b001 : 3'bz;  // Controlled_Buffer controlled_buffer_29
  assign delay_in = and_23_out ? and_23_out : 1'bz;  // Controlled_Buffer controlled_buffer_30
  Pull_Resistor pull_resistor_31 (.node(addr_sel_en));
  and and_31 (and_31_out, and_23_out, delay_out);
  assign addr_sel_en = and_31_out ? and_31_out : 1'bz;  // Controlled_Buffer controlled_buffer_31
  assign load = and_31_out ? and_31_out : 1'bz;  // Controlled_Buffer controlled_buffer_32
  assign Data_in_NOTen = and_31_out ? and_31_out : 1'bz;  // Controlled_Buffer controlled_buffer_33
  and and_32 (and_32_out, and_23_out, ~delay_out);  // AND_Gate
  assign addr_hold_wr = and_32_out ? and_32_out : 1'bz;  // Controlled_Buffer controlled_buffer_34
  Pull_Resistor pull_resistor_32 (.node(IR_wr));
  assign IR_wr = and_32_out ? and_32_out : 1'bz;  // Controlled_Buffer controlled_buffer_35
  Pull_Resistor pull_resistor_33 (.node(delay_in));
  assign delay_in = and_25_out ? and_25_out : 1'bz;  // Controlled_Buffer controlled_buffer_36
  Pull_Resistor pull_resistor_34 (.node(addr_hold_wr));
  and and_33 (and_33_out, and_25_out, ~delay_out);  // AND_Gate
  assign addr_hold_wr = and_33_out ? and_33_out : 1'bz;  // Controlled_Buffer controlled_buffer_37
  assign IR_wr = and_33_out ? and_33_out : 1'bz;  // Controlled_Buffer controlled_buffer_38
  assign addr_sel_en = and_27_out ? and_27_out : 1'bz;  // Controlled_Buffer controlled_buffer_39
  assign write = and_27_out ? and_27_out : 1'bz;  // Controlled_Buffer controlled_buffer_40
  assign Data_in_NOTen = and_27_out ? and_27_out : 1'bz;  // Controlled_Buffer controlled_buffer_41
  assign addr_sel = and_27_out ? 3'b001 : 3'bz;  // Controlled_Buffer controlled_buffer_42
  assign G1_use = and_12_out ? and_12_out : 1'bz;  // Controlled_Buffer controlled_buffer_43
  assign load = and_12_out ? and_12_out : 1'bz;  // Controlled_Buffer controlled_buffer_44
  assign alt_alt_data = and_12_out ? and_12_out : 1'bz;  // Controlled_Buffer controlled_buffer_45
  Pull_Resistor pull_resistor_35 (.node(alt_alt_data));
  assign delay_in = and_30_out ? and_30_out : 1'bz;  // Controlled_Buffer controlled_buffer_46
  and and_34 (and_34_out, and_30_out, delay_out);
  assign load = and_34_out ? and_34_out : 1'bz;  // Controlled_Buffer controlled_buffer_47
  and and_35 (and_35_out, and_30_out, ~delay_out);  // AND_Gate
  assign IR_wr = and_35_out ? and_35_out : 1'bz;  // Controlled_Buffer controlled_buffer_48
  assign G10 = and_13_out ? and_13_out : 1'bz;  // Controlled_Buffer controlled_buffer_49
  assign alt_alt_data = and_13_out ? and_13_out : 1'bz;  // Controlled_Buffer controlled_buffer_50
  assign load = and_13_out ? and_13_out : 1'bz;  // Controlled_Buffer controlled_buffer_51
  assign G0_only = and_13_out ? and_13_out : 1'bz;  // Controlled_Buffer controlled_buffer_52
  Demultiplexer #(.enable("true"), .select(4)) demultiplexer_1 (
    .out0(demultiplexer_1_out0), .out1(demultiplexer_1_out1), .out2(demultiplexer_1_out2),
    .out3(demultiplexer_1_out3), .out4(demultiplexer_1_out4), .out5(demultiplexer_1_out5),
    .out6(demultiplexer_1_out6), .out7(demultiplexer_1_out7), .out8(demultiplexer_1_out8),
    .out9(demultiplexer_1_out9), .out10(demultiplexer_1_out10), .out11(demultiplexer_1_out11),
    .out12(demultiplexer_1_out12), .out13(demultiplexer_1_out13), .out14(demultiplexer_1_out14),
    .out15(demultiplexer_1_out15), .in(load), .sel(D0), .en(pull_resistor_36_node));
  Comparator #(.mode("unsigned"), .width(2)) comparator_12 (.a(G), .b(2'b00), .eq(comparator_12_eq));  // open: gt, lt
  Pull_Resistor pull_resistor_36 (.node(pull_resistor_36_node));
  or or_9 (pull_resistor_36_node, comparator_12_eq, G0_only);
  Register #(.width(16)) R0 (.D(Data_in_t), .en(demultiplexer_1_out0), .clk(and_36_out), .Q(R0_q));  // open: clr
  Register #(.width(16)) register_2 (
    .D(Data_in_t), .en(demultiplexer_1_out1), .clk(and_36_out), .Q(register_2_q));  // open: clr
  Register #(.width(16)) register_3 (
    .D(Data_in_t), .en(demultiplexer_1_out2), .clk(and_36_out), .Q(register_3_q));  // open: clr
  Register #(.width(16)) register_4 (
    .D(Data_in_t), .en(demultiplexer_1_out3), .clk(and_36_out), .Q(register_4_q));  // open: clr
  Register #(.width(16)) register_5 (
    .D(Data_in_t), .en(demultiplexer_1_out4), .clk(and_36_out), .Q(register_5_q));  // open: clr
  Register #(.width(16)) register_6 (
    .D(Data_in_t), .en(demultiplexer_1_out5), .clk(and_36_out), .Q(register_6_q));  // open: clr
  Register #(.width(16)) register_7 (
    .D(Data_in_t), .en(demultiplexer_1_out6), .clk(and_36_out), .Q(register_7_q));  // open: clr
  Register #(.width(16)) register_8 (
    .D(Data_in_t), .en(demultiplexer_1_out7), .clk(and_36_out), .Q(register_8_q));  // open: clr
  Register #(.width(16)) register_9 (
    .D(Data_in_t), .en(demultiplexer_1_out8), .clk(and_36_out), .Q(register_9_q));  // open: clr
  Register #(.width(16)) register_10 (
    .D(Data_in_t), .en(demultiplexer_1_out9), .clk(and_36_out), .Q(register_10_q));  // open: clr
  Register #(.width(16)) register_11 (
    .D(Data_in_t), .en(demultiplexer_1_out10), .clk(and_36_out), .Q(register_11_q));  // open: clr
  Register #(.width(16)) register_12 (.D(Data_in_t), .en(demultiplexer_1_out11), .Q(register_12_q));  // open: clk, clr
  Register #(.width(16)) register_13 (
    .D(Data_in_t), .en(demultiplexer_1_out12), .clk(and_36_out), .Q(register_13_q));  // open: clr
  Register #(.width(16)) register_14 (
    .D(Data_in_t), .en(demultiplexer_1_out13), .clk(and_36_out), .Q(register_14_q));  // open: clr
  Register #(.width(16)) register_15 (
    .D(Data_in_t), .en(demultiplexer_1_out14), .clk(and_36_out), .Q(register_15_q));  // open: clr
  Register #(.width(16)) R15 (.D(Data_in_t), .en(demultiplexer_1_out15), .clk(and_36_out), .Q(R15_q));  // open: clr
  and and_36 (and_36_out, pull_resistor_36_node, CLK);
  assign DATA_out = pull_resistor_36_node ? multiplexer_8_out : 16'bz;  // Controlled_Buffer controlled_buffer_53
  Multiplexer #(.select(4), .width(16)) multiplexer_8 (
    .in0(R0_q), .in1(register_2_q), .in2(register_3_q), .in3(register_4_q), .in4(register_5_q),
    .in5(register_6_q), .in6(register_7_q), .in7(register_8_q), .in8(register_9_q), .in9(register_10_q),
    .in10(register_11_q), .in11(register_12_q), .in12(register_13_q), .in13(register_14_q),
    .in14(register_15_q), .in15(R15_q), .out(multiplexer_8_out), .sel(D0));
  Multiplexer #(.enable("true"), .select(4), .width(16)) multiplexer_9 (
    .in0(R0_q), .in1(register_2_q), .in2(register_3_q), .in3(register_4_q), .in4(register_5_q),
    .in5(register_6_q), .in6(register_7_q), .in7(register_8_q), .in8(register_9_q), .in9(register_10_q),
    .in10(register_11_q), .in11(register_12_q), .in12(register_13_q), .in13(register_14_q),
    .in14(register_15_q), .in15(R15_q), .out(multiplexer_9_out), .sel(D1), .en(G10));
  assign R1 = G10 ? multiplexer_9_out : 16'bz;  // Controlled_Buffer controlled_buffer_54
  D_Flip_Flop d_ff_1 (.Qn(d_ff_1_qn), .preset(CLK));  // open: D, clk, Q, reset
  and and_37 (and_37_out, d_ff_1_qn, CLK);
  Multiplexer #(.width(8)) multiplexer_10 (
    .in0(Data_in_t[15:8]), .in1(or_14_out), .out(multiplexer_10_out), .sel(or_11_out));
  or or_10 (or_10_out, store_status, d_ff_1_qn, demultiplexer_2_out0);
  or or_11 (or_11_out, store_status, d_ff_1_qn);
  Demultiplexer #(.enable("true"), .select(4)) demultiplexer_2 (
    .out0(demultiplexer_2_out0), .out1(demultiplexer_2_out1), .out2(demultiplexer_2_out2),
    .out3(demultiplexer_2_out3), .out4(demultiplexer_2_out4), .out5(demultiplexer_2_out5),
    .out6(demultiplexer_2_out6), .out7(demultiplexer_2_out7), .out8(demultiplexer_2_out8),
    .out9(demultiplexer_2_out9), .out10(demultiplexer_2_out10), .out11(demultiplexer_2_out11),
    .out12(demultiplexer_2_out12), .out13(demultiplexer_2_out13), .out14(demultiplexer_2_out14),
    .out15(demultiplexer_2_out15), .in(load), .sel(D0), .en(and_38_out));
  Pull_Resistor pull_resistor_37 (.node(pull_resistor_37_node[1]));
  Pull_Resistor pull_resistor_38 (.node(pull_resistor_38_node));
  assign pull_resistor_38_node = not_5_out ? Data_in_t[3:0] : 4'bz;  // Controlled_Buffer controlled_buffer_55
  Pull_Resistor pull_resistor_39 (.node(pull_resistor_39_node));
  not not_5 (not_5_out, d_ff_1_qn);
  or or_12 (or_12_out, load_PC, demultiplexer_2_out3);
  not not_6 (not_6_out, addr_sel_en);
  Comparator #(.mode("unsigned"), .width(2)) comparator_13 (.a(G), .b(2'b01), .eq(comparator_13_eq));  // open: gt, lt
  and and_38 (and_38_out, comparator_13_eq, ~G0_only);  // AND_Gate
  Register #(.width(16)) Status (
    .D({multiplexer_10_out, pull_resistor_39_node, pull_resistor_38_node[3:2], {2{pull_resistor_37_node[1]}}}),
    .en(or_10_out), .clk(or_13_out), .Q({Status_q[15:3], priviledged, Status_q[1:0]}));  // open: clr
  or or_13 (or_13_out, and_37_out, and_39_out);
  Register #(.width(16)) Control (
    .D(Data_in_t), .en(demultiplexer_2_out1), .clk(and_39_out),
    .Q({Control_q[15:10], halt_maskINT_control, halt_INT_control, Control_q[7:4], T1_mask, T0_mask, soft_mask, mask}));  // open: clr
  Register #(.width(16)) INT_Vector (
    .D(Data_in_t), .en(demultiplexer_2_out2), .clk(and_39_out), .Q(INT_Vector_q));  // open: clr
  Register #(.width(16)) register_16 (
    .D(Data_in_t), .en(demultiplexer_2_out8), .clk(and_39_out), .Q(register_16_q));  // open: clr
  Register #(.width(16)) register_17 (
    .D(Data_in_t), .en(demultiplexer_2_out9), .clk(and_39_out), .Q(register_17_q));  // open: clr
  Register #(.width(16)) register_18 (
    .D(Data_in_t), .en(demultiplexer_2_out10), .clk(and_39_out), .Q(register_18_q));  // open: clr
  Register #(.width(16)) register_19 (.D(Data_in_t), .en(demultiplexer_2_out11), .Q(register_19_q));  // open: clk, clr
  Register #(.width(16)) register_20 (
    .D(Data_in_t), .en(demultiplexer_2_out12), .clk(and_39_out), .Q(register_20_q));  // open: clr
  Register #(.width(16)) register_21 (
    .D(Data_in_t), .en(demultiplexer_2_out13), .clk(and_39_out), .Q(register_21_q));  // open: clr
  Register #(.width(16)) register_22 (
    .D(Data_in_t), .en(demultiplexer_2_out14), .clk(and_39_out), .Q(register_22_q));  // open: clr
  Register #(.width(16)) register_23 (
    .D(Data_in_t), .en(demultiplexer_2_out15), .clk(and_39_out), .Q(register_23_q));  // open: clr
  and and_39 (and_39_out, and_38_out, CLK);
  Pull_Resistor pull_resistor_40 (.node(and_38_out));
  Counter #(.max('hffff), .width(16)) PC (
    .load(or_12_out), .D(Data_in_t), .count(not_6_out), .Q(PC_q), .clk(CLK));  // open: carry, up, clr
  Counter #(.max('hffff), .width(16)) SP (
    .load(demultiplexer_2_out4), .D(Data_in_t), .count(stack_EN), .Q(SP_q), .up(stack_inc), .clk(CLK));  // open: carry, clr
  Counter #(.max('hffff), .width(16)) SySP (
    .load(demultiplexer_2_out5), .D(Data_in_t), .count(stack_SyEN), .Q(SySP_q), .up(stack_inc), .clk(CLK));  // open: carry, clr
  Counter #(.max('hffff), .width(16)) T0 (
    .load(demultiplexer_2_out6), .D(Data_in_t), .Q(T0_q), .carry(T0_INT), .clk(and_39_out));  // open: count, up, clr
  Counter #(.max('hffff), .width(16)) T1 (
    .load(demultiplexer_2_out7), .D(Data_in_t), .Q(T1_q), .carry(T1_INT), .clk(and_39_out));  // open: count, up, clr
  assign or_14_out = Status_q[15:8] | {{2{and_40_out[7]}}, access_INT, and_40_out[4:1], INT_t};  // OR_Gate or_14, 8 bits wide
  Multiplexer #(.select(4), .width(16)) multiplexer_11 (
    .in0({Status_q[15:3], priviledged, Status_q[1:0]}),
    .in1({Control_q[15:10], halt_maskINT_control, halt_INT_control, Control_q[7:4], T1_mask, T0_mask, soft_mask, mask}),
    .in2(INT_Vector_q), .in3(PC_q), .in4(SP_q), .in5(SySP_q), .in6(T0_q), .in7(T1_q), .in8(register_16_q),
    .in9(register_17_q), .in10(register_18_q), .in11(register_19_q), .in12(register_20_q),
    .in13(register_21_q), .in14(register_22_q), .in15(register_23_q), .out(multiplexer_11_out), .sel(D0));
  Multiplexer #(.enable("true"), .select(4), .width(16)) multiplexer_12 (
    .in0({Status_q[15:3], priviledged, Status_q[1:0]}),
    .in1({Control_q[15:10], halt_maskINT_control, halt_INT_control, Control_q[7:4], T1_mask, T0_mask, soft_mask, mask}),
    .in2(INT_Vector_q), .in3(PC_q), .in4(SP_q), .in5(SySP_q), .in6(T0_q), .in7(T1_q), .in8(register_16_q),
    .in9(register_17_q), .in10(register_18_q), .in11(register_19_q), .in12(register_20_q),
    .in13(register_21_q), .in14(register_22_q), .in15(register_23_q), .out(multiplexer_12_out), .sel(D1v),
    .en(G11));
  assign DATA_out = and_38_out ? multiplexer_11_out : 16'bz;  // Controlled_Buffer controlled_buffer_56
  Pull_Resistor pull_resistor_41 (.node(DATA_out));
  Pull_Resistor pull_resistor_42 (.node(and_40_out[7]));
  Pull_Resistor pull_resistor_43 (.node(addr_sel));
  assign R1 = G11 ? multiplexer_12_out : 16'bz;  // Controlled_Buffer controlled_buffer_57
  Pull_Resistor pull_resistor_44 (.node(R1));
  Pull_Resistor pull_resistor_45 (.node(Address));
  Multiplexer #(.select(3), .width(16)) multiplexer_13 (
    .in0(PC_q), .in1(address_t), .in2(SP_q), .in3(SySP_q), .in4(T0_q), .in5(T1_q), .out(Address),
    .sel(addr_sel));  // open: in6, in7
  and and_40 (and_40_out[1], INT_mask, mask);
  and and_41 (and_40_out[2], SOFT_INT, soft_mask);
  and and_42 (and_40_out[3], T0_INT, T0_mask);
  and and_43 (and_40_out[4], T1_INT, T1_mask);
  or or_15 (store_status, INT_t, INT_mask, SOFT_INT, T0_INT, T1_INT, access_INT, pull_resistor_46_node, pull_resistor_46_node);
  Pull_Resistor pull_resistor_46 (.node(pull_resistor_46_node));

  // Other names for the same wires on the sheet: IR (some bits) = {D4, G1, G, D1, D0}; CLK_cut = CLK_in;
  //   dissable_addr_inc = addr_sel_en; R0[15:0] = DATA_out

  // Notes on the sheet:
  //   ARITHMETIC
  //   SOFT_INT
  //   JUMP/BRANCH
  //   HALT
  //   TRANSFER
  //   LOGIC
  //   STACK
  //   LOAD/STORE
endmodule

module BASIC_DMA (
  input  MAIN_CLK,
  input  [15:0] ADDRESS_in,
  input  cpu_write,
  input  cpu_read,
  input  [15:0] cpu_DATA_in,
  input  [15:0] dev_0_ADDRESS,
  input  [15:0] dev_0_DATA_in,
  input  dev_0_write,
  input  dev_0_read,
  output cpu_enable,
  output cpu_clk,
  output [15:0] ADDRESS_out,
  output write,
  output read,
  output RAM_clk,
  output [15:0] DATA_out,
  output dev_clk_0
);

  Multiplexer #(.width(16)) multiplexer_1 (.in0(ADDRESS_in), .in1(dev_0_ADDRESS), .out(ADDRESS_out), .sel(cpu_enable));
  Multiplexer #(.width(16)) multiplexer_2 (.in0(cpu_DATA_in), .in1(dev_0_DATA_in), .out(DATA_out), .sel(cpu_enable));
  Pull_Resistor pull_resistor_1 (.node(cpu_enable));
  Multiplexer multiplexer_3 (.in0(cpu_write), .in1(dev_0_write), .out(write), .sel(cpu_enable));
  Multiplexer multiplexer_4 (.in0(cpu_read), .in1(dev_0_read), .out(read), .sel(cpu_enable));
  not not_1 (cpu_enable, MAIN_CLK);

  assign cpu_clk = MAIN_CLK;
  assign dev_clk_0 = cpu_enable;

  // Notes on the sheet:
  //   THIS IS MY FIRST ONE SO DONT EXPECT MUCH
  //   NOT A LOT OF FEATURES SINCE I DIDNT HAVE THE TIME
endmodule

module BASIC_DMA_TERMINAL (
  input  clk_in,
  input  [15:0] DATA_in,
  input  [6:0] keyboard_in,
  input  [15:0] ADDRESS_in,
  input  [15:0] select_address,
  output [15:0] DATA_out,
  output [15:0] ADDRESS_out,
  output write,
  output read,
  output read_keyboard
);

  wire and_1_out, comparator_1_eq, comparator_2_eq, comparator_3_eq, or_1_out, t_ff_1_q;
  wire [6:0] bit_extender_1_out, controlled_buffer_1_out, multiplexer_3_out;
  wire [7:0] multiplexer_1_out, multiplexer_2_out, pull_resistor_2_node, register_1_q, register_2_q;
  wire [15:0] register_3_q;

  Register register_1 (.D(DATA_in[7:0]), .en(read), .clk(clk_in), .Q(register_1_q));  // open: clr
  Register register_2 (.D(DATA_in[15:8]), .en(read), .clk(clk_in), .Q(register_2_q));  // open: clr
  T_Flip_Flop t_ff_1 (.T(read), .clk(clk_in), .Q(t_ff_1_q));  // open: Qn, reset, preset
  Comparator #(.width(16)) comparator_1 (.a(ADDRESS_in), .b(select_address), .eq(comparator_1_eq));  // open: gt, lt
  Register #(.trigger("falling"), .width(16)) register_3 (
    .D(DATA_in), .en(comparator_1_eq), .clk(clk_in), .Q(register_3_q));  // open: clr
  Multiplexer #(.width(8)) multiplexer_1 (
    .in0(register_1_q), .in1(register_2_q), .out(multiplexer_1_out), .sel(t_ff_1_q));
  Bit_Extender #(.out_width(7), .\type ("input")) bit_extender_1 (
    .in(multiplexer_2_out), .out(bit_extender_1_out));  // open: extend
  Multiplexer #(.width(8)) multiplexer_2 (
    .in0(multiplexer_1_out), .in1(register_3_q[7:0]), .out(multiplexer_2_out), .sel(comparator_2_eq));
  assign controlled_buffer_1_out = or_1_out ? multiplexer_3_out : 7'bz;  // Controlled_Buffer controlled_buffer_1
  Multiplexer #(.width(7)) multiplexer_3 (
    .in0(bit_extender_1_out), .in1(keyboard_in), .out(multiplexer_3_out), .sel(and_1_out));
  and and_1 (and_1_out, comparator_2_eq, read_keyboard);
  or or_1 (or_1_out, comparator_2_eq, read, read_keyboard);
  Comparator comparator_2 (.a(register_3_q[15:8]), .b(8'h1), .eq(comparator_2_eq));  // open: gt, lt
  Comparator comparator_3 (.a(register_3_q[15:8]), .b(8'h2), .eq(comparator_3_eq));  // open: gt, lt
  Pull_Resistor pull_resistor_1 (.node(controlled_buffer_1_out));
  TTY tty_1 (.data(controlled_buffer_1_out), .clk(clk_in), .we(or_1_out));  // open: clr
  D_Flip_Flop d_ff_1 (.D(comparator_3_eq), .clk(clk_in), .Q(read), .Qn(read_keyboard));  // open: preset, reset
  Pull_Resistor pull_resistor_2 (.node(pull_resistor_2_node));
  Counter #(.max('hffff), .width(16)) counter_1 (
    .D({register_3_q[7:0], pull_resistor_2_node}), .count(read), .Q(ADDRESS_out), .clk(clk_in));  // open: load, carry, up, clr
  assign DATA_out = {{9{1'b0}}, keyboard_in};  // Bit_Extender bit_extender_2
endmodule

module BASIC_TERMINAL (
  input  CLK_in,
  input  [15:0] ADDRESS_in,
  input  write_in,
  input  read_in,
  input  [15:0] DATA_in,
  input  [15:0] SEL_ADDRESS_in,
  input  [6:0] KEYBOARD_in,
  output [15:0] TERM_DATA_out,
  output [15:0] ADDRESS_out,
  output write_out,
  output read_out,
  output [15:0] DATA_out,
  output TERM_SEL,
  output read_term,
  output write_term
);

  wire comparator_1_eq, t_ff_1_q, undriven;

  Comparator #(.width(16)) comparator_1 (.a(ADDRESS_in), .b(SEL_ADDRESS_in), .eq(comparator_1_eq));  // open: gt, lt
  assign TERM_DATA_out = {{9{1'b0}}, KEYBOARD_in};  // Bit_Extender bit_extender_1
  and and_1 (write_out, write_in, ~comparator_1_eq);  // AND_Gate
  and and_2 (read_out, read_in, ~comparator_1_eq);  // AND_Gate
  and and_3 (read_term, read_in, comparator_1_eq);
  and and_4 (write_term, write_in, comparator_1_eq);
  T_Flip_Flop t_ff_1 (.T(undriven), .clk(undriven), .Q(t_ff_1_q));  // open: Qn, reset, preset

  assign ADDRESS_out = ADDRESS_in;
  assign DATA_out = DATA_in;
  assign TERM_SEL = read_term;
endmodule
