// Logisim project cpu32_again.circ as structural Verilog: 10 circuits, main circuit main
module main (
  input  in_1,
  input  in_2,
  input  in_3
);

  wire clock_1_out, clock_2_out, le_cpu_again_but_planned_1_write_mem, not_1_out;
  wire [23:0] bit_extender_1_out;
  wire [31:0] le_cpu_again_but_planned_1_address_out, le_cpu_again_but_planned_1_data_out, ram_1_dout;

  Clock clock_1 (.out(clock_1_out));
  le_cpu_again_but_planned le_cpu_again_but_planned_1 (
    .not_enable(in_1), .clk_in(clock_1_out), .data_in(ram_1_dout), .interrupt_unmaskable(in_2),
    .interrupt_maskable(in_3), .address_out(le_cpu_again_but_planned_1_address_out),
    .data_out(le_cpu_again_but_planned_1_data_out), .write_mem(le_cpu_again_but_planned_1_write_mem));
  Bit_Extender #(.in_width(32), .out_width(24), .\type ("zero")) bit_extender_1 (
    .in(le_cpu_again_but_planned_1_address_out), .out(bit_extender_1_out));
  not not_1 (not_1_out, le_cpu_again_but_planned_1_write_mem);
  Clock clock_2 (.out(clock_2_out));
  RAM #(.addrWidth(24), .asyncread("true"), .dataWidth(32), .\type ("nonvolatile")) ram_1 (
    .addr(bit_extender_1_out), .we(le_cpu_again_but_planned_1_write_mem), .oe(not_1_out), .clk(clock_2_out),
    .din(le_cpu_again_but_planned_1_data_out), .dout(ram_1_dout));

  // Notes on the sheet:
  //   alu 1
  //   mem 1
  //   mem 2
  //   doesnt do [mem 2] in this case
endmodule

module reg_file_v1 (
  input  clk_in,
  input  [9:0] condition_address,
  input  [31:0] data_in,
  input  [9:0] address1,
  input  [9:0] address2,
  input  enable_PC,
  input  write,
  input  [9:0] write_address,
  input  dec_sp,
  input  inc_sp,
  input  inc_ISP,
  input  interrupt,
  input  unmask,
  input  mask,
  output [31:0] PC,
  output [31:0] condition_data_out,
  output [31:0] data_out,
  output [31:0] data_out2,
  output [31:0] control_out,
  output [31:0] status_out,
  output [31:0] SP,
  output [31:0] ISP,
  output int_mask,
  output soft_int_mask
);

  wire and_1_out, and_2_out, and_3_out, and_4_out, and_5_out, and_6_out, and_7_out, and_11_out, and_12_out,
       and_13_out, and_14_out, and_15_out, comparator_1_eq, comparator_2_eq, comparator_3_eq,
       comparator_4_eq, comparator_5_eq, comparator_6_eq, comparator_7_eq, comparator_8_eq, comparator_9_gt,
       comparator_9_lt, demultiplexer_1_out0, demultiplexer_1_out1, demultiplexer_1_out2,
       demultiplexer_1_out3, demultiplexer_2_out0, demultiplexer_2_out1, demultiplexer_2_out2,
       demultiplexer_2_out3, demultiplexer_4_out0, demultiplexer_4_out1, demultiplexer_4_out2,
       demultiplexer_4_out3, demultiplexer_4_out4, demultiplexer_4_out5, demultiplexer_4_out6,
       demultiplexer_4_out7, demultiplexer_4_out8, demultiplexer_4_out9, demultiplexer_4_out10,
       demultiplexer_4_out11, demultiplexer_4_out12, demultiplexer_4_out13, demultiplexer_4_out14,
       demultiplexer_4_out15, demultiplexer_4_out16, demultiplexer_4_out17, demultiplexer_4_out18,
       demultiplexer_4_out19, demultiplexer_4_out20, demultiplexer_4_out21, demultiplexer_4_out22,
       demultiplexer_4_out23, demultiplexer_4_out24, demultiplexer_4_out25, demultiplexer_4_out26,
       demultiplexer_4_out27, demultiplexer_4_out28, demultiplexer_4_out29, demultiplexer_4_out30,
       demultiplexer_4_out31, nor_1_out, not_1_out, not_2_out, or_1_out, or_2_out, or_3_out, or_4_out,
       or_5_out, xor_1_out, xor_2_out;
  wire [1:0] STACK_CONTROL_q, STACK_CONTROL_q_3;
  wire [2:0] and_8_out;
  wire [4:0] bit_extender_1_out, bit_extender_2_out, bit_extender_3_out, bit_extender_4_out;
  wire [31:0] controlled_buffer_1_out, counter_1_q, counter_2_q, counter_3_q, counter_4_q, data,
       multiplexer_2_out, pull_resistor_8_node, register_1_q, register_2_q, register_3_q, register_5_q,
       register_6_q, register_7_q, register_8_q, register_9_q, register_10_q, register_11_q, register_12_q,
       register_13_q, register_14_q, register_15_q, register_16_q, register_17_q, register_18_q,
       register_19_q, register_20_q, register_21_q, register_22_q, register_23_q, register_24_q,
       register_25_q, register_26_q, register_27_q, register_28_q, register_29_q, register_30_q,
       register_31_q, register_32_q, register_33_q, register_34_q, register_35_q;
  wire [31:2] STACK_CONTROL_q_2;

  and and_1 (and_1_out, dec_sp, STACK_CONTROL_q_2[16]);
  Pull_Resistor pull_resistor_1 (.node(dec_sp));
  Pull_Resistor pull_resistor_2 (.node(inc_sp));
  or or_1 (or_1_out, and_1_out, inc_sp);
  Pull_Resistor pull_resistor_3 (.node(inc_ISP));
  Demultiplexer #(.select(2)) demultiplexer_1 (
    .out0(demultiplexer_1_out0), .out1(demultiplexer_1_out1), .out2(demultiplexer_1_out2),
    .out3(demultiplexer_1_out3), .in(and_15_out), .sel(STACK_CONTROL_q));
  or or_2 (or_2_out, and_15_out, dec_sp, inc_sp, inc_ISP);
  Demultiplexer #(.disabled("Z"), .enable("true"), .select(2), .tristate("true")) demultiplexer_2 (
    .out0(demultiplexer_2_out0), .out1(demultiplexer_2_out1), .out2(demultiplexer_2_out2),
    .out3(demultiplexer_2_out3), .in(or_2_out), .sel(STACK_CONTROL_q), .en(not_1_out));
  Demultiplexer #(.disabled("Z"), .enable("true"), .select(2), .tristate("true")) demultiplexer_3 (
    .out0(demultiplexer_2_out0), .out1(demultiplexer_2_out1), .out2(demultiplexer_2_out2),
    .out3(demultiplexer_2_out3), .in(or_2_out), .sel(STACK_CONTROL_q_3), .en(inc_ISP));
  not not_1 (not_1_out, inc_ISP);
  Comparator #(.mode("unsigned"), .width(10)) comparator_1 (
    .a(write_address), .b(10'h300), .eq(comparator_1_eq));  // open: gt, lt
  Comparator #(.mode("unsigned"), .width(10)) comparator_2 (
    .a(write_address), .b(10'h301), .eq(comparator_2_eq));  // open: gt, lt
  Comparator #(.mode("unsigned"), .width(10)) comparator_3 (
    .a(write_address), .b(10'h302), .eq(comparator_3_eq));  // open: gt, lt
  Comparator #(.mode("unsigned"), .width(10)) comparator_4 (
    .a(write_address), .b(10'h303), .eq(comparator_4_eq));  // open: gt, lt
  Pull_Resistor pull_resistor_4 (.node(demultiplexer_2_out0));
  Register #(.width(32)) register_1 (.D(data), .en(and_2_out), .clk(clk_in), .Q(register_1_q));  // open: clr
  and and_2 (and_2_out, and_11_out, comparator_1_eq);
  Register #(.width(32)) register_2 (.D(data), .en(and_3_out), .clk(clk_in), .Q(register_2_q));  // open: clr
  and and_3 (and_3_out, and_11_out, comparator_2_eq);
  Register #(.width(32)) register_3 (.D(data), .en(and_4_out), .clk(clk_in), .Q(register_3_q));  // open: clr
  and and_4 (and_4_out, and_11_out, comparator_3_eq);
  Register #(.width(32)) register_4 (.D(data), .en(and_5_out), .clk(clk_in));  // open: Q, clr
  and and_5 (and_5_out, and_11_out, comparator_4_eq);
  Pull_Resistor pull_resistor_5 (.node(demultiplexer_2_out1));
  Pull_Resistor pull_resistor_6 (.node(demultiplexer_2_out2));
  Pull_Resistor pull_resistor_7 (.node(demultiplexer_2_out3));
  or or_3 (or_3_out, and_6_out, and_7_out);
  and and_6 (and_6_out, or_1_out, xor_1_out);
  xor xor_1 (xor_1_out, inc_sp, STACK_CONTROL_q_2[16]);
  and and_7 (and_7_out, xor_2_out, inc_ISP);
  xor xor_2 (xor_2_out, inc_ISP, STACK_CONTROL_q_2[17]);
  assign controlled_buffer_1_out = and_8_out[0] ? register_1_q : 32'bz;  // Controlled_Buffer controlled_buffer_1
  assign controlled_buffer_1_out = and_8_out[1] ? register_2_q : 32'bz;  // Controlled_Buffer controlled_buffer_2
  and and_8 (and_8_out[0], unmask, interrupt);
  and and_9 (and_8_out[1], mask, ~unmask, interrupt);  // AND_Gate
  and and_10 (and_8_out[2], nor_1_out, interrupt);
  nor nor_1 (nor_1_out, mask, unmask);
  Counter #(.max('hffffffff), .width(32)) counter_1 (
    .load(demultiplexer_1_out0), .D(data), .count(demultiplexer_2_out0), .Q(counter_1_q), .up(or_3_out),
    .clk(clk_in));  // open: carry, clr
  Counter #(.max('hffffffff), .width(32)) counter_2 (
    .load(demultiplexer_1_out1), .D(data), .count(demultiplexer_2_out1), .Q(counter_2_q), .up(or_3_out),
    .clk(clk_in));  // open: carry, clr
  Counter #(.max('hffffffff), .width(32)) counter_3 (
    .load(demultiplexer_1_out2), .D(data), .count(demultiplexer_2_out2), .Q(counter_3_q), .up(or_3_out),
    .clk(clk_in));  // open: carry, clr
  Counter #(.max('hffffffff), .width(32)) counter_4 (
    .load(demultiplexer_1_out3), .D(data), .count(demultiplexer_2_out3), .Q(counter_4_q), .up(or_3_out),
    .clk(clk_in));  // open: carry, clr
  assign controlled_buffer_1_out = and_8_out[2] ? register_3_q : 32'bz;  // Controlled_Buffer controlled_buffer_3
  Pull_Resistor pull_resistor_8 (.node(pull_resistor_8_node));
  Pull_Resistor pull_resistor_9 (.node(enable_PC));
  Pull_Resistor pull_resistor_10 (.node(clk_in));
  Pull_Resistor pull_resistor_11 (.node(data_in));
  Multiplexer #(.width(32)) multiplexer_1 (.in0(data_in), .in1(controlled_buffer_1_out), .out(data), .sel(interrupt));
  not not_2 (not_2_out, enable_PC);
  Multiplexer #(.width(32)) multiplexer_2 (
    .in0(data), .in1({pull_resistor_8_node[31:3], and_8_out}), .out(multiplexer_2_out), .sel(interrupt));
  Multiplexer #(.select(2), .width(32)) multiplexer_3 (
    .in0(counter_1_q), .in1(counter_2_q), .in2(counter_3_q), .in3(counter_4_q), .out(SP),
    .sel(STACK_CONTROL_q));
  Multiplexer #(.select(2), .width(32)) multiplexer_4 (
    .in0(counter_1_q), .in1(counter_2_q), .in2(counter_3_q), .in3(counter_4_q), .out(ISP),
    .sel(STACK_CONTROL_q_3));
  Pull_Resistor pull_resistor_12 (.node(condition_address));
  Pull_Resistor pull_resistor_13 (.node(address1));
  Pull_Resistor pull_resistor_14 (.node(address2));
  Pull_Resistor pull_resistor_15 (.node(write));
  Pull_Resistor pull_resistor_16 (.node(write_address));
  and and_11 (and_11_out, write, comparator_9_gt);
  Comparator #(.mode("unsigned"), .width(10)) comparator_5 (
    .a(write_address), .b(10'h100), .eq(comparator_5_eq));  // open: gt, lt
  Comparator #(.mode("unsigned"), .width(10)) comparator_6 (
    .a(write_address), .b(10'h101), .eq(comparator_6_eq));  // open: gt, lt
  Comparator #(.mode("unsigned"), .width(10)) comparator_7 (
    .a(write_address), .b(10'h103), .eq(comparator_7_eq));  // open: gt, lt
  Comparator #(.mode("unsigned"), .width(10)) comparator_8 (
    .a(write_address), .b(10'h104), .eq(comparator_8_eq));  // open: gt, lt
  Register #(.width(32)) CONTROL (.D(data), .en(and_12_out), .clk(clk_in), .Q(control_out));  // open: clr
  and and_12 (and_12_out, and_11_out, comparator_5_eq);
  or or_4 (or_4_out, interrupt, and_13_out);
  Register #(.width(32)) STATUS (.D(multiplexer_2_out), .en(or_4_out), .clk(clk_in), .Q(status_out));  // open: clr
  and and_13 (and_13_out, and_11_out, comparator_6_eq);
  Register #(.width(32)) STACK_CONTROL (
    .D(data), .en(and_14_out), .clk(clk_in),
    .Q({STACK_CONTROL_q_2[31:10], STACK_CONTROL_q_3, STACK_CONTROL_q_2[7:2], STACK_CONTROL_q}));  // open: clr
  and and_14 (and_14_out, and_11_out, comparator_7_eq);
  and and_15 (and_15_out, and_11_out, comparator_8_eq);
  Bit_Extender #(.in_width(10), .out_width(5), .\type ("zero")) bit_extender_1 (
    .in(write_address), .out(bit_extender_1_out));
  Comparator #(.mode("unsigned"), .width(10)) comparator_9 (
    .a(write_address), .b(10'h20), .gt(comparator_9_gt), .lt(comparator_9_lt));  // open: eq
  Demultiplexer #(.enable("true"), .select(5)) demultiplexer_4 (
    .out0(demultiplexer_4_out0), .out1(demultiplexer_4_out1), .out2(demultiplexer_4_out2),
    .out3(demultiplexer_4_out3), .out4(demultiplexer_4_out4), .out5(demultiplexer_4_out5),
    .out6(demultiplexer_4_out6), .out7(demultiplexer_4_out7), .out8(demultiplexer_4_out8),
    .out9(demultiplexer_4_out9), .out10(demultiplexer_4_out10), .out11(demultiplexer_4_out11),
    .out12(demultiplexer_4_out12), .out13(demultiplexer_4_out13), .out14(demultiplexer_4_out14),
    .out15(demultiplexer_4_out15), .out16(demultiplexer_4_out16), .out17(demultiplexer_4_out17),
    .out18(demultiplexer_4_out18), .out19(demultiplexer_4_out19), .out20(demultiplexer_4_out20),
    .out21(demultiplexer_4_out21), .out22(demultiplexer_4_out22), .out23(demultiplexer_4_out23),
    .out24(demultiplexer_4_out24), .out25(demultiplexer_4_out25), .out26(demultiplexer_4_out26),
    .out27(demultiplexer_4_out27), .out28(demultiplexer_4_out28), .out29(demultiplexer_4_out29),
    .out30(demultiplexer_4_out30), .out31(demultiplexer_4_out31), .in(comparator_9_lt),
    .sel(bit_extender_1_out), .en(write));
  Bit_Extender #(.in_width(10), .out_width(5), .\type ("zero")) bit_extender_2 (
    .in(condition_address), .out(bit_extender_2_out));
  Bit_Extender #(.in_width(10), .out_width(5), .\type ("zero")) bit_extender_3 (
    .in(address1), .out(bit_extender_3_out));
  Bit_Extender #(.in_width(10), .out_width(5), .\type ("zero")) bit_extender_4 (
    .in(address2), .out(bit_extender_4_out));
  or or_5 (or_5_out, interrupt, demultiplexer_4_out0);
  Register #(.width(32)) register_5 (.D(data), .en(demultiplexer_4_out1), .clk(clk_in), .Q(register_5_q));  // open: clr
  Register #(.width(32)) register_6 (.D(data), .en(demultiplexer_4_out2), .clk(clk_in), .Q(register_6_q));  // open: clr
  Register #(.width(32)) register_7 (.D(data), .en(demultiplexer_4_out3), .clk(clk_in), .Q(register_7_q));  // open: clr
  Register #(.width(32)) register_8 (.D(data), .en(demultiplexer_4_out4), .clk(clk_in), .Q(register_8_q));  // open: clr
  Register #(.width(32)) register_9 (.D(data), .en(demultiplexer_4_out5), .clk(clk_in), .Q(register_9_q));  // open: clr
  Register #(.width(32)) register_10 (
    .D(data), .en(demultiplexer_4_out6), .clk(clk_in), .Q(register_10_q));  // open: clr
  Register #(.width(32)) register_11 (
    .D(data), .en(demultiplexer_4_out7), .clk(clk_in), .Q(register_11_q));  // open: clr
  Register #(.width(32)) register_12 (
    .D(data), .en(demultiplexer_4_out8), .clk(clk_in), .Q(register_12_q));  // open: clr
  Register #(.width(32)) register_13 (
    .D(data), .en(demultiplexer_4_out9), .clk(clk_in), .Q(register_13_q));  // open: clr
  Register #(.width(32)) register_14 (
    .D(data), .en(demultiplexer_4_out10), .clk(clk_in), .Q(register_14_q));  // open: clr
  Register #(.width(32)) register_15 (
    .D(data), .en(demultiplexer_4_out11), .clk(clk_in), .Q(register_15_q));  // open: clr
  Register #(.width(32)) register_16 (
    .D(data), .en(demultiplexer_4_out12), .clk(clk_in), .Q(register_16_q));  // open: clr
  Register #(.width(32)) register_17 (
    .D(data), .en(demultiplexer_4_out13), .clk(clk_in), .Q(register_17_q));  // open: clr
  Register #(.width(32)) register_18 (
    .D(data), .en(demultiplexer_4_out14), .clk(clk_in), .Q(register_18_q));  // open: clr
  Register #(.width(32)) register_19 (
    .D(data), .en(demultiplexer_4_out15), .clk(clk_in), .Q(register_19_q));  // open: clr
  Register #(.width(32)) register_20 (
    .D(data), .en(demultiplexer_4_out16), .clk(clk_in), .Q(register_20_q));  // open: clr
  Register #(.width(32)) register_21 (
    .D(data), .en(demultiplexer_4_out17), .clk(clk_in), .Q(register_21_q));  // open: clr
  Register #(.width(32)) register_22 (
    .D(data), .en(demultiplexer_4_out18), .clk(clk_in), .Q(register_22_q));  // open: clr
  Register #(.width(32)) register_23 (
    .D(data), .en(demultiplexer_4_out19), .clk(clk_in), .Q(register_23_q));  // open: clr
  Register #(.width(32)) register_24 (
    .D(data), .en(demultiplexer_4_out20), .clk(clk_in), .Q(register_24_q));  // open: clr
  Register #(.width(32)) register_25 (
    .D(data), .en(demultiplexer_4_out21), .clk(clk_in), .Q(register_25_q));  // open: clr
  Register #(.width(32)) register_26 (
    .D(data), .en(demultiplexer_4_out22), .clk(clk_in), .Q(register_26_q));  // open: clr
  Register #(.width(32)) register_27 (
    .D(data), .en(demultiplexer_4_out23), .clk(clk_in), .Q(register_27_q));  // open: clr
  Register #(.width(32)) register_28 (
    .D(data), .en(demultiplexer_4_out24), .clk(clk_in), .Q(register_28_q));  // open: clr
  Register #(.width(32)) register_29 (
    .D(data), .en(demultiplexer_4_out25), .clk(clk_in), .Q(register_29_q));  // open: clr
  Register #(.width(32)) register_30 (
    .D(data), .en(demultiplexer_4_out26), .clk(clk_in), .Q(register_30_q));  // open: clr
  Register #(.width(32)) register_31 (
    .D(data), .en(demultiplexer_4_out27), .clk(clk_in), .Q(register_31_q));  // open: clr
  Register #(.width(32)) register_32 (
    .D(data), .en(demultiplexer_4_out28), .clk(clk_in), .Q(register_32_q));  // open: clr
  Register #(.width(32)) register_33 (
    .D(data), .en(demultiplexer_4_out29), .clk(clk_in), .Q(register_33_q));  // open: clr
  Register #(.width(32)) register_34 (
    .D(data), .en(demultiplexer_4_out30), .clk(clk_in), .Q(register_34_q));  // open: clr
  Register #(.width(32)) register_35 (
    .D(data), .en(demultiplexer_4_out31), .clk(clk_in), .Q(register_35_q));  // open: clr
  Counter #(.max('hffffffff), .width(32)) counter_5 (
    .load(or_5_out), .D(data), .count(not_2_out), .Q(PC), .clk(clk_in));  // open: carry, up, clr
  Multiplexer #(.select(5), .width(32)) multiplexer_5 (
    .in0(PC), .in1(register_5_q), .in2(register_6_q), .in3(register_7_q), .in4(register_8_q),
    .in5(register_9_q), .in6(register_10_q), .in7(register_11_q), .in8(register_12_q), .in9(register_13_q),
    .in10(register_14_q), .in11(register_15_q), .in12(register_16_q), .in13(register_17_q),
    .in14(register_18_q), .in15(register_19_q), .in16(register_20_q), .in17(register_21_q),
    .in18(register_22_q), .in19(register_23_q), .in20(register_24_q), .in21(register_25_q),
    .in22(register_26_q), .in23(register_27_q), .in24(register_28_q), .in25(register_29_q),
    .in26(register_30_q), .in27(register_31_q), .in28(register_32_q), .in29(register_33_q),
    .in30(register_34_q), .in31(register_35_q), .out(condition_data_out), .sel(bit_extender_2_out));
  Multiplexer #(.select(5), .width(32)) multiplexer_6 (
    .in0(PC), .in1(register_5_q), .in2(register_6_q), .in3(register_7_q), .in4(register_8_q),
    .in5(register_9_q), .in6(register_10_q), .in7(register_11_q), .in8(register_12_q), .in9(register_13_q),
    .in10(register_14_q), .in11(register_15_q), .in12(register_16_q), .in13(register_17_q),
    .in14(register_18_q), .in15(register_19_q), .in16(register_20_q), .in17(register_21_q),
    .in18(register_22_q), .in19(register_23_q), .in20(register_24_q), .in21(register_25_q),
    .in22(register_26_q), .in23(register_27_q), .in24(register_28_q), .in25(register_29_q),
    .in26(register_30_q), .in27(register_31_q), .in28(register_32_q), .in29(register_33_q),
    .in30(register_34_q), .in31(register_35_q), .out(data_out), .sel(bit_extender_3_out));
  Multiplexer #(.select(5), .width(32)) multiplexer_7 (
    .in0(PC), .in1(register_5_q), .in2(register_6_q), .in3(register_7_q), .in4(register_8_q),
    .in5(register_9_q), .in6(register_10_q), .in7(register_11_q), .in8(register_12_q), .in9(register_13_q),
    .in10(register_14_q), .in11(register_15_q), .in12(register_16_q), .in13(register_17_q),
    .in14(register_18_q), .in15(register_19_q), .in16(register_20_q), .in17(register_21_q),
    .in18(register_22_q), .in19(register_23_q), .in20(register_24_q), .in21(register_25_q),
    .in22(register_26_q), .in23(register_27_q), .in24(register_28_q), .in25(register_29_q),
    .in26(register_30_q), .in27(register_31_q), .in28(register_32_q), .in29(register_33_q),
    .in30(register_34_q), .in31(register_35_q), .out(data_out2), .sel(bit_extender_4_out));

  assign int_mask = control_out[0];
  assign soft_int_mask = control_out[1];

  // Other names for the same wires on the sheet: clk = clk_in

  // Notes on the sheet:
  //   interrupt stack pointer
endmodule

module le_cpu_again_but_planned (
  input  not_enable,
  input  clk_in,
  input  [31:0] data_in,
  input  interrupt_unmaskable,
  input  interrupt_maskable,
  output [31:0] address_out,
  output [31:0] data_out,
  output write_mem
);

  wire allow_alu, alt_data, alu_1_alu_busy, alu_1_reg_request, and_1_out, and_3_out, and_4_out, and_5_out,
       clk, condition_check_1_condition_busy, condition_check_1_write_alu, condition_check_1_write_mem,
       dec_sp, decode_1_alu, decode_1_write_mem, halt_PC, inc_ISP, inc_sp, \int , mem_handler_1_alt_address,
       mem_handler_1_mem_busy, not_1_out, or_1_out, pull_resistor_1_node, reg_file_v1_1_int_mask, s_r_ff_1_q,
       soft_mask, t_ff_1_q, t_ff_1_qn, t_ff_2_q, write_reg;
  wire [1:0] condition_check_1_reg_address, decode_1_reg_addrs;
  wire [3:0] decode_1_cond_out;
  wire [4:0] condition_check_1_signals_out, condition_check_1_source2_out, decode_1_signals, decode_1_src2;
  wire [9:0] cond, condition_check_1_source1_out, decode_1_dest, decode_1_src1, rd_mem, rd_mem2, wr_mem;
  wire [31:0] address, cond_data, condition_check_1_data_out, control, decode_1_data_out, ISP,
       mem_handler_1_address_out, multiplexer_1_out, multiplexer_2_out, pull_resistor_2_node, reg_data,
       reg_file_v1_1_data_out, reg_file_v1_1_data_out2, SP, status;

  and and_1 (and_1_out, interrupt_maskable, reg_file_v1_1_int_mask);
  and and_2 (clk, ~not_enable, clk_in);  // AND_Gate
  or or_1 (or_1_out, interrupt_unmaskable, and_1_out);
  T_Flip_Flop t_ff_1 (.T(t_ff_2_q), .clk(clk), .Q(t_ff_1_q), .Qn(t_ff_1_qn));  // open: reset, preset
  T_Flip_Flop t_ff_2 (.T(s_r_ff_1_q), .clk(clk), .Q(t_ff_2_q));  // open: Qn, reset, preset
  and and_3 (and_3_out, t_ff_1_q, t_ff_2_q);
  and and_4 (and_4_out, or_1_out, not_1_out);
  not not_1 (not_1_out, or_1_out);
  S_R_Flip_Flop s_r_ff_1 (
    .S(pull_resistor_1_node), .R(and_3_out), .clk(clk), .Q(s_r_ff_1_q), .preset(and_4_out));  // open: reset, Qn
  Pull_Resistor pull_resistor_1 (.node(pull_resistor_1_node));
  Pull_Resistor pull_resistor_2 (.node(pull_resistor_2_node));
  assign pull_resistor_2_node = and_5_out ? 32'h8000001 : 32'bz;  // Controlled_Buffer controlled_buffer_1
  and and_5 (and_5_out, t_ff_1_qn, t_ff_2_q);
  Multiplexer #(.width(32)) multiplexer_1 (
    .in0(data_in), .in1(pull_resistor_2_node), .out(multiplexer_1_out), .sel(s_r_ff_1_q));
  or or_2 (halt_PC, s_r_ff_1_q, condition_check_1_condition_busy);
  decode decode_1 (
    .clk_in(clk), .data_in(multiplexer_1_out), .not_stall(condition_check_1_condition_busy), .PC_in(address),
    .cond_out(decode_1_cond_out), .write_mem(decode_1_write_mem), .signals(decode_1_signals),
    .reg_addrs(decode_1_reg_addrs), .src2(decode_1_src2), .dest(decode_1_dest), .src1(decode_1_src1),
    .alu(decode_1_alu), .data_out(decode_1_data_out));
  Multiplexer #(.width(32)) multiplexer_2 (.in0(reg_data), .in1(data_in), .out(multiplexer_2_out), .sel(alt_data));
  reg_file_v1 reg_file_v1_1 (
    .clk_in(clk), .condition_address(cond), .data_in(multiplexer_2_out), .address1(rd_mem),
    .address2(rd_mem2), .enable_PC(halt_PC), .write(write_reg), .write_address(wr_mem), .dec_sp(dec_sp),
    .inc_sp(inc_sp), .inc_ISP(inc_ISP), .interrupt(\int ), .unmask(interrupt_unmaskable), .mask(and_1_out),
    .PC(address), .condition_data_out(cond_data), .data_out(reg_file_v1_1_data_out),
    .data_out2(reg_file_v1_1_data_out2), .control_out(control), .status_out(status), .SP(SP), .ISP(ISP),
    .int_mask(reg_file_v1_1_int_mask), .soft_int_mask(soft_mask));
  condition_check condition_check_1 (
    .clk(clk), .mem_busy(mem_handler_1_mem_busy), .alu_busy(alu_1_alu_busy), .reg_data(cond_data),
    .condition(decode_1_cond_out), .wr_mem(decode_1_write_mem), .signals(decode_1_signals),
    .reg_addrs(decode_1_reg_addrs), .source2(decode_1_src2), .destination(decode_1_dest),
    .source1(decode_1_src1), .wr_alu(decode_1_alu), .data_in(decode_1_data_out),
    .write_mem(condition_check_1_write_mem), .destination_out(cond),
    .source1_out(condition_check_1_source1_out), .signals_out(condition_check_1_signals_out),
    .reg_address(condition_check_1_reg_address), .source2_out(condition_check_1_source2_out),
    .write_alu(condition_check_1_write_alu), .data_out(condition_check_1_data_out),
    .condition_busy(condition_check_1_condition_busy));
  mem_handler mem_handler_1 (
    .clk(clk), .data_in(data_in), .new_command(condition_check_1_write_mem), .destination(cond),
    .source1(condition_check_1_source1_out), .signals(condition_check_1_signals_out),
    .reg_addrs(condition_check_1_reg_address), .reg_data_in_1(reg_file_v1_1_data_out),
    .reg_data_in_2(reg_file_v1_1_data_out2), .alu_reg_request(alu_1_reg_request), .SP(SP),
    .imm_data_in(condition_check_1_data_out), .ISP(ISP), .mem_busy(mem_handler_1_mem_busy),
    .alt_address(mem_handler_1_alt_address), .address_out(mem_handler_1_address_out), .data_out(reg_data),
    .write_mem(write_mem), .write_reg(write_reg), .wr_select_reg(wr_mem), .rd_select_reg(rd_mem),
    .rd_select_reg_2(rd_mem2), .allow_alu(allow_alu), .halt_PC(halt_PC), .alt_data(alt_data),
    .inc_sp(inc_sp), .dec_sp(dec_sp), .inc_ISP(inc_ISP), .interrupt(\int ));  // open: soft_int_mask, halt_decoder
  alu alu_1 (
    .clk(clk), .destination(cond), .source1(condition_check_1_source1_out),
    .source2(condition_check_1_source2_out), .signals(condition_check_1_signals_out),
    .new_command(condition_check_1_write_alu), .reg_data_in_1(reg_file_v1_1_data_out),
    .reg_data_in_2(reg_file_v1_1_data_out2), .reg_request_granted(allow_alu),
    .reg_request(alu_1_reg_request), .data_out(reg_data), .write_reg(write_reg), .wr_select_reg(wr_mem),
    .rd_select_reg(rd_mem), .rd_select_reg_2(rd_mem2), .alu_busy(alu_1_alu_busy));
  Multiplexer #(.width(32)) multiplexer_3 (
    .in0(address), .in1(mem_handler_1_address_out), .out(address_out), .sel(mem_handler_1_alt_address));
  assign data_out = mem_handler_1_alt_address ? reg_data : 32'bz;  // Controlled_Buffer controlled_buffer_2
endmodule

module decode (
  input  clk_in,
  input  [31:0] data_in,
  input  not_stall,
  input  [31:0] PC_in,
  output [3:0] cond_out,
  output write_mem,
  output [4:0] signals,
  output [1:0] reg_addrs,
  output [4:0] src2,
  output [9:0] dest,
  output [9:0] src1,
  output alu,
  output [31:0] data_out
);

  wire alu_t, and_3_out, and_4_out, and_5_out, and_6_out, and_7_out, and_8_out, and_9_out, and_10_out,
       and_11_out, and_12_out, and_13_out, and_14_out, and_15_out, and_16_out, and_17_out, and_18_out,
       and_19_out, and_20_out, and_21_out, and_22_out, and_23_out, and_24_out, and_25_out, and_26_out,
       and_27_out, and_28_out, and_29_out, clk, comparator_1_eq, comparator_2_eq, comparator_3_eq,
       comparator_4_eq, comparator_5_eq, comparator_6_eq, comparator_7_eq, comparator_8_eq, comparator_9_eq,
       comparator_10_eq, comparator_11_eq, imm_data, mem, nor_1_out, nor_2_out, nor_3_out, nor_4_out,
       nor_5_out, nor_6_out, nor_7_out, nor_8_out, nor_9_out, nor_10_out, nor_11_out, nor_12_out, nor_13_out,
       nor_14_out, nor_15_out, nor_16_out, nor_17_out, nor_18_out, not_1_out, pull_resistor_4_node, ten_dest,
       ten_src, valid;
  wire [1:0] IR_q_3, reg_address;
  wire [1:1] pull_resistor_5_node;
  wire [3:0] conditin, IR_q_2;
  wire [4:0] signals_t;
  wire [9:0] bit_extender_1_out, bit_extender_3_out, multiplexer_2_out;
  wire [27:0] IR_q;
  wire [31:0] bit_extender_2_out;

  not not_1 (not_1_out, not_stall);
  and and_1 (clk, clk_in, not_1_out);
  Register #(.width(32)) IR (
    .D(data_in), .en(not_1_out), .clk(clk),
    .Q({conditin, IR_q[27:22], IR_q_2[0], IR_q_2[1], IR_q_2[2], IR_q_2[3], src2[0], src2[1], src2[2], src2[3], src2[4], IR_q[12:8], IR_q_3, IR_q[5:3], imm_data, IR_q[1:0]}));  // open: clr
  Pull_Resistor pull_resistor_1 (.node(data_in));
  and and_2 (valid, IR_q[0], ~IR_q[1]);  // AND_Gate
  nor nor_1 (nor_1_out, ~IR_q[27], IR_q[26], IR_q[25], IR_q[24]);  // NOR_Gate
  assign bit_extender_1_out = {{5{1'b0}}, {IR_q[23], IR_q[24], IR_q[25], IR_q[26], IR_q[27]}};  // Bit_Extender bit_extender_1
  Multiplexer #(.width(10)) multiplexer_1 (
    .in0(bit_extender_1_out), .in1({IR_q_2, IR_q[22], IR_q[23], IR_q[24], IR_q[25], IR_q[26], IR_q[27]}),
    .out(dest), .sel(ten_dest));
  assign bit_extender_2_out = {{12{1'b0}}, {IR_q[22], IR_q_2[0], IR_q_2[1], IR_q_2[2], IR_q_2[3], src2[0], src2[1], src2[2], src2[3], src2[4], IR_q[12:8], IR_q_3, IR_q[5:3]}};  // Bit_Extender bit_extender_2
  assign bit_extender_3_out = {{5{1'b0}}, {IR_q_2, IR_q[22]}};  // Bit_Extender bit_extender_3
  Multiplexer #(.width(10)) multiplexer_2 (
    .in0({src2, IR_q_2, IR_q[22]}), .in1({IR_q[8], IR_q[9], IR_q[10], IR_q[11], IR_q[12], src2}),
    .out(multiplexer_2_out), .sel(ten_dest));
  Pull_Resistor pull_resistor_2 (.node(ten_src));
  Multiplexer #(.width(10)) multiplexer_3 (
    .in0(bit_extender_3_out), .in1(multiplexer_2_out), .out(src1), .sel(ten_src));
  Multiplexer #(.width(32)) multiplexer_4 (.in0(PC_in), .in1(bit_extender_2_out), .out(data_out), .sel(imm_data));
  Pull_Resistor pull_resistor_3 (.node(ten_dest));
  nor nor_2 (nor_2_out, IR_q[23], IR_q[22], IR_q_2[0], IR_q_2[1], IR_q_2[2], IR_q_2[3], src2[0], src2[1], src2[2], src2[3]);
  nor nor_3 (nor_3_out, src2[0], src2[1], src2[2], src2[3], src2[4], IR_q[12], IR_q[11], IR_q[10]);
  nor nor_4 (nor_4_out, src2[4], IR_q[12], IR_q[11], IR_q[10]);
  nor nor_5 (nor_5_out, src2[1], src2[2], ~src2[3]);  // NOR_Gate
  nor nor_6 (nor_6_out, ~src2[4], IR_q[12], IR_q[11], IR_q[10]);  // NOR_Gate
  nor nor_7 (nor_7_out, IR_q[9], IR_q[8], IR_q_3[1], IR_q_3[0]);
  nor nor_8 (nor_8_out, IR_q[9], ~IR_q[8], IR_q_3[1], IR_q_3[0]);  // NOR_Gate
  and and_3 (and_3_out, IR_q[12], IR_q[11], IR_q[10]);
  nor nor_9 (nor_9_out, IR_q[12], ~IR_q[11], ~IR_q[10]);  // NOR_Gate
  nor nor_10 (nor_10_out, ~IR_q[12], IR_q[11], ~IR_q[10]);  // NOR_Gate
  nor nor_11 (nor_11_out, IR_q[12], IR_q[11], ~IR_q[10]);  // NOR_Gate
  nor nor_12 (nor_12_out, ~IR_q[12], ~IR_q[11], IR_q[10]);  // NOR_Gate
  nor nor_13 (nor_13_out, IR_q[12], ~IR_q[11], IR_q[10]);  // NOR_Gate
  nor nor_14 (nor_14_out, ~IR_q[12], IR_q[11], IR_q[10]);  // NOR_Gate
  nor nor_15 (nor_15_out, IR_q[12], IR_q[11], IR_q[10]);
  nor nor_16 (nor_16_out, ~IR_q[9], IR_q[8], IR_q_3[1], IR_q_3[0]);  // NOR_Gate
  and and_4 (and_4_out, nor_15_out, nor_8_out);
  assign signals_t = imm_data ? 5'b00111 : 5'bz;  // Controlled_Buffer controlled_buffer_1
  assign mem = imm_data ? 1'b1 : 1'bz;  // Controlled_Buffer controlled_buffer_2
  nor nor_17 (nor_17_out, imm_data, IR_q[3], IR_q[4], IR_q[5]);
  nor nor_18 (nor_18_out, imm_data, IR_q[3], IR_q[4], ~IR_q[5]);  // NOR_Gate
  and and_5 (and_5_out, nor_17_out, nor_16_out, nor_15_out);
  and and_6 (and_6_out, nor_17_out, nor_16_out, nor_14_out);
  and and_7 (and_7_out, nor_17_out, nor_16_out, nor_13_out);
  and and_8 (and_8_out, nor_17_out, nor_16_out, nor_12_out);
  and and_9 (and_9_out, nor_17_out, nor_16_out, nor_11_out);
  and and_10 (and_10_out, nor_17_out, nor_16_out, nor_10_out);
  and and_11 (and_11_out, nor_17_out, nor_16_out, nor_9_out);
  and and_12 (and_12_out, nor_17_out, nor_16_out, and_3_out);
  and and_13 (and_13_out, nor_17_out, nor_16_out, and_4_out);
  and and_14 (and_14_out, nor_17_out, nor_7_out, nor_6_out, src2[3], src2[2]);
  and and_15 (and_15_out, nor_17_out, nor_7_out, nor_6_out);
  assign reg_address = nor_18_out ? IR_q_3 : 2'bz;  // Controlled_Buffer controlled_buffer_3
  assign alu_t = and_5_out ? 1'b1 : 1'bz;  // Controlled_Buffer controlled_buffer_4
  assign signals_t = and_5_out ? {5{1'b0}} : 5'bz;  // Controlled_Buffer controlled_buffer_5
  assign alu_t = and_6_out ? 1'b1 : 1'bz;  // Controlled_Buffer controlled_buffer_6
  assign signals_t = and_6_out ? 5'b00001 : 5'bz;  // Controlled_Buffer controlled_buffer_7
  assign alu_t = and_7_out ? 1'b1 : 1'bz;  // Controlled_Buffer controlled_buffer_8
  assign signals_t = and_7_out ? 5'b00010 : 5'bz;  // Controlled_Buffer controlled_buffer_9
  assign alu_t = and_8_out ? 1'b1 : 1'bz;  // Controlled_Buffer controlled_buffer_10
  assign signals_t = and_8_out ? 5'b00011 : 5'bz;  // Controlled_Buffer controlled_buffer_11
  assign alu_t = and_9_out ? 1'b1 : 1'bz;  // Controlled_Buffer controlled_buffer_12
  assign signals_t = and_9_out ? 5'b00100 : 5'bz;  // Controlled_Buffer controlled_buffer_13
  assign alu_t = and_10_out ? 1'b1 : 1'bz;  // Controlled_Buffer controlled_buffer_14
  assign signals_t = and_10_out ? 5'b00101 : 5'bz;  // Controlled_Buffer controlled_buffer_15
  assign alu_t = and_11_out ? 1'b1 : 1'bz;  // Controlled_Buffer controlled_buffer_16
  assign signals_t = and_11_out ? 5'b00110 : 5'bz;  // Controlled_Buffer controlled_buffer_17
  assign alu_t = and_12_out ? 1'b1 : 1'bz;  // Controlled_Buffer controlled_buffer_18
  assign signals_t = and_12_out ? 5'b00111 : 5'bz;  // Controlled_Buffer controlled_buffer_19
  assign alu_t = and_13_out ? 1'b1 : 1'bz;  // Controlled_Buffer controlled_buffer_20
  assign signals_t = and_13_out ? 5'b01000 : 5'bz;  // Controlled_Buffer controlled_buffer_21
  assign reg_address = and_14_out ? {src2[0], src2[1]} : 2'bz;  // Controlled_Buffer controlled_buffer_22
  Comparator #(.mode("unsigned"), .width(4)) comparator_1 (
    .a(src2[3:0]), .b(4'b0000), .eq(comparator_1_eq));  // open: gt, lt
  Comparator #(.mode("unsigned"), .width(4)) comparator_2 (
    .a(src2[3:0]), .b(4'b0001), .eq(comparator_2_eq));  // open: gt, lt
  Comparator #(.mode("unsigned"), .width(4)) comparator_3 (
    .a(src2[3:0]), .b(4'b0010), .eq(comparator_3_eq));  // open: gt, lt
  Comparator #(.mode("unsigned"), .width(4)) comparator_4 (
    .a(src2[3:0]), .b(4'b0011), .eq(comparator_4_eq));  // open: gt, lt
  Comparator #(.mode("unsigned"), .width(4)) comparator_5 (
    .a(src2[3:0]), .b(4'b0100), .eq(comparator_5_eq));  // open: gt, lt
  Comparator #(.mode("unsigned"), .width(4)) comparator_6 (
    .a(src2[3:0]), .b(4'b0101), .eq(comparator_6_eq));  // open: gt, lt
  Comparator #(.mode("unsigned"), .width(4)) comparator_7 (
    .a(src2[3:0]), .b(4'b0110), .eq(comparator_7_eq));  // open: gt, lt
  Comparator #(.mode("unsigned"), .width(4)) comparator_8 (
    .a(src2[3:0]), .b(4'b0111), .eq(comparator_8_eq));  // open: gt, lt
  Comparator #(.mode("unsigned"), .width(4)) comparator_9 (
    .a(src2[3:0]), .b(4'b1000), .eq(comparator_9_eq));  // open: gt, lt
  Pull_Resistor #(.pull(1)) pull_resistor_4 (.node(pull_resistor_4_node));
  assign ten_dest = nor_18_out ? pull_resistor_4_node : 1'bz;  // Controlled_Buffer controlled_buffer_23
  assign ten_src = nor_18_out ? pull_resistor_4_node : 1'bz;  // Controlled_Buffer controlled_buffer_24
  assign signals_t = nor_18_out ? {5{1'b0}} : 5'bz;  // Controlled_Buffer controlled_buffer_25
  assign mem = nor_18_out ? 1'b1 : 1'bz;  // Controlled_Buffer controlled_buffer_26
  assign signals_t = and_14_out ? 5'b00001 : 5'bz;  // Controlled_Buffer controlled_buffer_27
  assign mem = and_14_out ? 1'b1 : 1'bz;  // Controlled_Buffer controlled_buffer_28
  and and_16 (and_16_out, and_15_out, comparator_1_eq);
  and and_17 (and_17_out, and_15_out, comparator_2_eq);
  and and_18 (and_18_out, and_15_out, comparator_3_eq);
  and and_19 (and_19_out, and_15_out, comparator_4_eq);
  and and_20 (and_20_out, and_15_out, comparator_5_eq);
  and and_21 (and_21_out, and_15_out, comparator_6_eq);
  and and_22 (and_22_out, and_15_out, comparator_7_eq);
  and and_23 (and_23_out, and_15_out, comparator_8_eq);
  and and_24 (and_24_out, and_15_out, comparator_9_eq);
  and and_25 (and_25_out, nor_17_out, nor_7_out, nor_3_out);
  Comparator #(.mode("unsigned"), .width(4)) comparator_10 (
    .a(IR_q_2), .b(4'b0010), .eq(comparator_10_eq));  // open: gt, lt
  Comparator #(.mode("unsigned"), .width(4)) comparator_11 (
    .a(IR_q_2), .b(4'b0011), .eq(comparator_11_eq));  // open: gt, lt
  and and_26 (and_26_out, nor_17_out, nor_7_out, nor_4_out, nor_5_out);
  Pull_Resistor pull_resistor_5 (.node(pull_resistor_5_node[1]));
  and and_27 (and_27_out, nor_17_out, nor_7_out, nor_4_out, nor_2_out, nor_1_out);
  assign alu_t = and_16_out ? 1'b1 : 1'bz;  // Controlled_Buffer controlled_buffer_29
  assign signals_t = and_16_out ? 5'b01001 : 5'bz;  // Controlled_Buffer controlled_buffer_30
  assign alu_t = and_17_out ? 1'b1 : 1'bz;  // Controlled_Buffer controlled_buffer_31
  assign signals_t = and_17_out ? 5'b01010 : 5'bz;  // Controlled_Buffer controlled_buffer_32
  assign alu_t = and_18_out ? 1'b1 : 1'bz;  // Controlled_Buffer controlled_buffer_33
  assign signals_t = and_18_out ? 5'b01011 : 5'bz;  // Controlled_Buffer controlled_buffer_34
  assign alu_t = and_19_out ? 1'b1 : 1'bz;  // Controlled_Buffer controlled_buffer_35
  assign signals_t = and_19_out ? 5'b01100 : 5'bz;  // Controlled_Buffer controlled_buffer_36
  assign mem = and_20_out ? 1'b1 : 1'bz;  // Controlled_Buffer controlled_buffer_37
  assign signals_t = and_20_out ? 5'b00010 : 5'bz;  // Controlled_Buffer controlled_buffer_38
  assign mem = and_21_out ? 1'b1 : 1'bz;  // Controlled_Buffer controlled_buffer_39
  assign signals_t = and_21_out ? 5'b00011 : 5'bz;  // Controlled_Buffer controlled_buffer_40
  assign alu_t = and_22_out ? 1'b1 : 1'bz;  // Controlled_Buffer controlled_buffer_41
  assign signals_t = and_22_out ? 5'b01101 : 5'bz;  // Controlled_Buffer controlled_buffer_42
  assign alu_t = and_23_out ? 1'b1 : 1'bz;  // Controlled_Buffer controlled_buffer_43
  assign signals_t = and_23_out ? 5'b01110 : 5'bz;  // Controlled_Buffer controlled_buffer_44
  assign alu_t = and_24_out ? 1'b1 : 1'bz;  // Controlled_Buffer controlled_buffer_45
  assign signals_t = and_24_out ? 5'b01111 : 5'bz;  // Controlled_Buffer controlled_buffer_46
  and and_28 (and_28_out, and_25_out, comparator_10_eq);
  and and_29 (and_29_out, and_25_out, comparator_11_eq);
  assign mem = and_26_out ? 1'b1 : 1'bz;  // Controlled_Buffer controlled_buffer_47
  assign signals_t = and_26_out ? 5'b00100 : 5'bz;  // Controlled_Buffer controlled_buffer_48
  assign reg_address = and_26_out ? {pull_resistor_5_node[1], src2[0]} : 2'bz;  // Controlled_Buffer controlled_buffer_49
  assign mem = and_27_out ? 1'b1 : 1'bz;  // Controlled_Buffer controlled_buffer_50
  assign signals_t = and_27_out ? 5'b00101 : 5'bz;  // Controlled_Buffer controlled_buffer_51
  assign ten_dest = and_20_out ? and_20_out : 1'bz;  // Controlled_Buffer controlled_buffer_52
  assign ten_dest = and_21_out ? and_21_out : 1'bz;  // Controlled_Buffer controlled_buffer_53
  assign alu_t = and_28_out ? 1'b1 : 1'bz;  // Controlled_Buffer controlled_buffer_54
  assign signals_t = and_28_out ? 5'b10000 : 5'bz;  // Controlled_Buffer controlled_buffer_55
  assign alu_t = and_29_out ? 1'b1 : 1'bz;  // Controlled_Buffer controlled_buffer_56
  assign signals_t = and_29_out ? 5'b10001 : 5'bz;  // Controlled_Buffer controlled_buffer_57
  Pull_Resistor pull_resistor_6 (.node(cond_out));
  assign cond_out = valid ? conditin : 4'bz;  // Controlled_Buffer controlled_buffer_58
  Pull_Resistor pull_resistor_7 (.node(write_mem));
  assign write_mem = valid ? mem : 1'bz;  // Controlled_Buffer controlled_buffer_59
  Pull_Resistor pull_resistor_8 (.node(signals));
  assign signals = valid ? signals_t : 5'bz;  // Controlled_Buffer controlled_buffer_60
  Pull_Resistor pull_resistor_9 (.node(reg_addrs));
  assign reg_addrs = valid ? reg_address : 2'bz;  // Controlled_Buffer controlled_buffer_61
  Pull_Resistor pull_resistor_10 (.node(alu));
  assign alu = valid ? alu_t : 1'bz;  // Controlled_Buffer controlled_buffer_62

  // Notes on the sheet:
  //   0, alu
  //   1, mem
  //   0, mem
endmodule

module condition_check (
  input  clk,
  input  mem_busy,
  input  alu_busy,
  input  [31:0] reg_data,
  input  [3:0] condition,
  input  wr_mem,
  input  [4:0] signals,
  input  [1:0] reg_addrs,
  input  [4:0] source2,
  input  [9:0] destination,
  input  [9:0] source1,
  input  wr_alu,
  input  [31:0] data_in,
  output write_mem,
  output [9:0] destination_out,
  output [9:0] source1_out,
  output [4:0] signals_out,
  output [1:0] reg_address,
  output [4:0] source2_out,
  output write_alu,
  output [31:0] data_out,
  output condition_busy
);

  wire alu_q, and_1_out, and_2_out, and_3_out, and_4_out, and_5_out, and_6_out, and_7_out, and_9_out,
       comparator_1_eq, comparator_1_gt, comparator_1_lt, mem_q, multiplexer_1_out, not_1_out, or_1_out,
       or_2_out, pull_resistor_3_node;
  wire [3:0] register_1_q;
  wire [31:0] pull_resistor_2_node;

  Register #(.width(4)) register_1 (.D(condition), .en(not_1_out), .clk(clk), .Q(register_1_q));  // open: clr
  or or_1 (or_1_out, wr_alu, and_7_out);
  D_Flip_Flop mem (.D(or_2_out), .clk(clk), .Q(mem_q));  // open: Qn, preset, reset
  or or_2 (or_2_out, and_9_out, wr_mem);
  Register #(.width(5)) register_2 (.D(source2), .en(not_1_out), .clk(clk), .Q(source2_out));  // open: clr
  Register #(.width(10)) register_3 (.D(destination), .en(not_1_out), .clk(clk), .Q(destination_out));  // open: clr
  Register #(.width(10)) register_4 (.D(source1), .en(not_1_out), .clk(clk), .Q(source1_out));  // open: clr
  Register #(.width(5)) register_5 (.D(signals), .en(not_1_out), .clk(clk), .Q(signals_out));  // open: clr
  Register #(.width(2)) register_6 (.D(reg_addrs), .en(not_1_out), .clk(clk), .Q(reg_address));  // open: clr
  D_Flip_Flop alu (.D(or_1_out), .clk(clk), .Q(alu_q));  // open: Qn, preset, reset
  Register #(.width(32)) register_7 (.D(data_in), .en(not_1_out), .clk(clk), .Q(data_out));  // open: clr
  Pull_Resistor pull_resistor_1 (.node(reg_data));
  Pull_Resistor pull_resistor_2 (.node(pull_resistor_2_node));
  Comparator #(.width(32)) comparator_1 (
    .a(reg_data), .b(pull_resistor_2_node), .gt(comparator_1_gt), .eq(comparator_1_eq), .lt(comparator_1_lt));
  Pull_Resistor #(.pull(1)) pull_resistor_3 (.node(pull_resistor_3_node));
  Multiplexer #(.select(4)) multiplexer_1 (
    .in0(pull_resistor_3_node), .in1(comparator_1_gt), .in2(comparator_1_eq), .in3(comparator_1_lt),
    .in4(reg_data[0]), .in5(reg_data[30]), .in6(reg_data[31]), .out(multiplexer_1_out), .sel(register_1_q));  // open: in7, in8, in9, in10, in11, in12, in13, in14, in15
  and and_1 (and_1_out, multiplexer_1_out, mem_q);
  and and_2 (and_2_out, multiplexer_1_out, alu_q);
  and and_3 (and_3_out, mem_busy, wr_mem);
  and and_4 (and_4_out, alu_busy, wr_alu);
  and and_5 (and_5_out, and_1_out, wr_alu, mem_busy);
  and and_6 (and_6_out, alu_busy, wr_mem, and_2_out);
  and and_7 (and_7_out, and_2_out, alu_busy);
  and and_8 (write_alu, and_2_out, not_1_out);
  not not_1 (not_1_out, condition_busy);
  and and_9 (and_9_out, mem_busy, and_1_out);
  or or_3 (condition_busy, and_7_out, and_6_out, and_5_out, and_4_out, and_3_out, and_9_out);
  and and_10 (write_mem, and_1_out, ~condition_busy);  // AND_Gate
endmodule

module scheduler (
  input  clk,
  input  write_in,
  input  [9:0] destination,
  input  [9:0] source1,
  input  [9:0] source2,
  input  [4:0] signals,
  input  [31:0] imm_data,
  input  imm_valid,
  input  a_in,
  input  wr_mem_not_alu,
  output write_mem,
  output [9:0] destination_out,
  output [9:0] source1_out,
  output [9:0] source2_out,
  output [4:0] signals_out,
  output [31:0] imm_data_out,
  output a_out,
  output write_alu
);

  wire and_1_out, and_2_out, and_3_out, d_ff_1_q, d_ff_3_q, d_ff_3_qn;

  and and_1 (and_1_out, write_in, imm_valid);
  and and_2 (and_2_out, write_in, a_in);
  and and_3 (and_3_out, write_in, wr_mem_not_alu);
  D_Flip_Flop d_ff_1 (.D(write_in), .clk(clk), .Q(d_ff_1_q));  // open: Qn, preset, reset
  Register #(.width(10)) register_1 (.D(destination), .en(write_in), .clk(clk), .Q(destination_out));  // open: clr
  Register #(.width(10)) register_2 (.D(source1), .en(write_in), .clk(clk), .Q(source1_out));  // open: clr
  Register #(.width(10)) register_3 (.D(source2), .en(write_in), .clk(clk), .Q(source2_out));  // open: clr
  Register #(.width(5)) register_4 (.D(signals), .en(write_in), .clk(clk), .Q(signals_out));  // open: clr
  Register #(.width(32)) register_5 (.D(imm_data), .en(and_1_out), .clk(clk), .Q(imm_data_out));  // open: clr
  D_Flip_Flop d_ff_2 (.D(and_2_out), .clk(clk), .Q(a_out));  // open: Qn, preset, reset
  D_Flip_Flop d_ff_3 (.D(and_3_out), .clk(clk), .Q(d_ff_3_q), .Qn(d_ff_3_qn));  // open: preset, reset
  and and_4 (write_mem, d_ff_1_q, d_ff_3_q);
  and and_5 (write_alu, d_ff_1_q, d_ff_3_qn);
endmodule

module mem_handler (
  input  clk,
  input  [31:0] data_in,
  input  new_command,
  input  [9:0] destination,
  input  [9:0] source1,
  input  [4:0] signals,
  input  [1:0] reg_addrs,
  input  [31:0] reg_data_in_1,
  input  [31:0] reg_data_in_2,
  input  alu_reg_request,
  input  [31:0] SP,
  input  [31:0] imm_data_in,
  input  [31:0] ISP,
  input  soft_int_mask,
  output halt_decoder,
  output mem_busy,
  output alt_address,
  output [31:0] address_out,
  output [31:0] data_out,
  output write_mem,
  output write_reg,
  output [9:0] wr_select_reg,
  output [9:0] rd_select_reg,
  output [9:0] rd_select_reg_2,
  output allow_alu,
  output halt_PC,
  output alt_data,
  output inc_sp,
  output dec_sp,
  output inc_ISP,
  output interrupt
);

  wire and_2_out, and_3_out, and_4_out, and_5_out, and_6_out, and_7_out, d_ff_1_q, demultiplexer_1_out0,
       demultiplexer_1_out1, demultiplexer_1_out4, demultiplexer_1_out5, demultiplexer_1_out7, not_1_out,
       or_1_out, or_2_out, or_3_out, or_4_out, or_5_out, or_8_out, or_11_out, or_13_out, or_14_out,
       pull_resistor_1_node, t_ff_1_q, t_ff_1_qn;
  wire [1:0] register_2_q;
  wire [2:0] bit_extender_1_out;
  wire [4:0] register_1_q;
  wire [9:0] controlled_buffer_1_out, dest_q, multiplexer_4_out, src_q;
  wire [31:0] multiplexer_1_out, multiplexer_3_out, register_3_q;

  Register #(.width(5)) register_1 (.D(signals), .en(new_command), .clk(clk), .Q(register_1_q));  // open: clr
  Register #(.width(2)) register_2 (.D(reg_addrs), .en(new_command), .clk(clk), .Q(register_2_q));  // open: clr
  Multiplexer #(.width(32)) multiplexer_1 (.in0(SP), .in1(ISP), .out(multiplexer_1_out), .sel(inc_ISP));
  or or_1 (or_1_out, new_command, and_3_out);
  Register #(.width(10)) dest (.D(destination), .en(new_command), .clk(clk), .Q(dest_q));  // open: clr
  Register #(.width(10)) src (.D(source1), .en(new_command), .clk(clk), .Q(src_q));  // open: clr
  Multiplexer #(.width(32)) multiplexer_2 (
    .in0(reg_data_in_2), .in1(multiplexer_1_out), .out(address_out), .sel(or_2_out));
  or or_2 (or_2_out, inc_sp, inc_ISP, t_ff_1_q);
  Register #(.width(32)) register_3 (.D(imm_data_in), .en(new_command), .clk(clk), .Q(register_3_q));  // open: clr
  D_Flip_Flop d_ff_1 (.D(or_1_out), .clk(clk), .Q(d_ff_1_q), .Qn(allow_alu));  // open: preset, reset
  Bit_Extender #(.in_width(5), .out_width(3), .\type ("zero")) bit_extender_1 (
    .in(register_1_q), .out(bit_extender_1_out));
  and and_1 (inc_ISP, soft_int_mask, demultiplexer_1_out5);
  Demultiplexer #(.select(3)) demultiplexer_1 (
    .out0(demultiplexer_1_out0), .out1(demultiplexer_1_out1), .out2(inc_sp), .out3(dec_sp),
    .out4(demultiplexer_1_out4), .out5(demultiplexer_1_out5), .out7(demultiplexer_1_out7), .in(d_ff_1_q),
    .sel(bit_extender_1_out));  // open: out6
  and and_2 (and_2_out, demultiplexer_1_out1, ~register_2_q[1], ~register_2_q[0]);  // AND_Gate
  or or_3 (or_3_out, demultiplexer_1_out0, and_2_out);
  and and_3 (and_3_out, dec_sp, t_ff_1_qn);
  T_Flip_Flop t_ff_1 (.T(dec_sp), .clk(clk), .Q(t_ff_1_q), .Qn(t_ff_1_qn));  // open: reset, preset
  and and_4 (and_4_out, demultiplexer_1_out1, register_2_q[0], ~register_2_q[1]);  // AND_Gate
  and and_5 (and_5_out, demultiplexer_1_out1, ~register_2_q[0], register_2_q[1]);  // AND_Gate
  and and_6 (and_6_out, demultiplexer_1_out4, ~register_2_q[0]);  // AND_Gate
  and and_7 (and_7_out, demultiplexer_1_out4, register_2_q[0]);
  or or_4 (or_4_out, inc_ISP, demultiplexer_1_out7);
  Multiplexer #(.width(32)) multiplexer_3 (
    .in0(reg_data_in_1), .in1(register_3_q), .out(multiplexer_3_out), .sel(or_4_out));
  or or_5 (or_5_out, and_6_out, and_7_out);
  not not_1 (not_1_out, or_5_out);
  assign controlled_buffer_1_out = not_1_out ? dest_q : 10'bz;  // Controlled_Buffer controlled_buffer_1
  or or_6 (write_mem, and_5_out, inc_ISP, inc_sp);
  Pull_Resistor pull_resistor_1 (.node(pull_resistor_1_node));
  or or_7 (pull_resistor_1_node, and_4_out, inc_sp, and_7_out);
  or or_8 (or_8_out, and_5_out, or_5_out, or_3_out, and_4_out, inc_sp);
  or or_9 (alt_data, and_4_out, t_ff_1_q, and_7_out);
  or or_10 (alt_address, t_ff_1_q, and_4_out, and_7_out, and_5_out, inc_sp, inc_ISP);
  or or_11 (or_11_out, demultiplexer_1_out7, or_3_out, or_5_out, and_4_out, t_ff_1_q);
  Multiplexer #(.width(10)) multiplexer_4 (
    .in0(controlled_buffer_1_out), .in1(src_q), .out(multiplexer_4_out), .sel(pull_resistor_1_node));
  or or_12 (mem_busy, alu_reg_request, t_ff_1_q);
  or or_13 (or_13_out, inc_ISP, inc_sp, and_5_out, or_5_out, or_3_out, demultiplexer_1_out7);
  or or_14 (or_14_out, t_ff_1_q, and_4_out, or_5_out, or_3_out, demultiplexer_1_out7);
  Pull_Resistor pull_resistor_2 (.node(alt_address));
  Pull_Resistor pull_resistor_3 (.node(address_out));
  Pull_Resistor pull_resistor_4 (.node(multiplexer_3_out));
  assign data_out = or_13_out ? multiplexer_3_out : 32'bz;  // Controlled_Buffer controlled_buffer_2
  Pull_Resistor pull_resistor_5 (.node(or_11_out));
  Pull_Resistor pull_resistor_6 (.node(controlled_buffer_1_out));
  Pull_Resistor pull_resistor_7 (.node(src_q));
  Pull_Resistor pull_resistor_8 (.node(multiplexer_4_out));
  assign write_reg = or_11_out ? or_11_out : 1'bz;  // Controlled_Buffer controlled_buffer_3
  assign wr_select_reg = or_14_out ? controlled_buffer_1_out : 10'bz;  // Controlled_Buffer controlled_buffer_4
  assign rd_select_reg = or_8_out ? src_q : 10'bz;  // Controlled_Buffer controlled_buffer_5
  assign rd_select_reg_2 = or_8_out ? multiplexer_4_out : 10'bz;  // Controlled_Buffer controlled_buffer_6
  Pull_Resistor pull_resistor_9 (.node(allow_alu));
  Pull_Resistor pull_resistor_10 ();  // open: node
  Pull_Resistor pull_resistor_11 (.node(alt_data));
  Pull_Resistor pull_resistor_12 (.node(write_mem));

  assign interrupt = inc_ISP;

  // Notes on the sheet:
  //   to use register file
endmodule

module alu (
  input  clk,
  input  [9:0] destination,
  input  [9:0] source1,
  input  [4:0] source2,
  input  [4:0] signals,
  input  new_command,
  input  [31:0] reg_data_in_1,
  input  [31:0] reg_data_in_2,
  input  reg_request_granted,
  output reg_request,
  output [31:0] data_out,
  output write_reg,
  output [9:0] wr_select_reg,
  output [9:0] rd_select_reg,
  output [9:0] rd_select_reg_2,
  output alu_busy
);

  wire and_1_out, and_2_out, comparator_1_gt, or_1_out, pull_resistor_1_node, pull_resistor_2_node,
       pull_resistor_3_node;
  wire [4:0] bit_extender_2_out, register_1_q, register_4_q;
  wire [7:0] adder_2_out, adder_3_out, adder_4_out, adder_5_out;
  wire [9:0] bit_extender_1_out, pull_resistor_9_node, register_2_q, register_3_q;
  wire [15:0] subtractor_6_out, subtractor_7_out;
  wire [31:0] adder_1_out, adder_6_out, adder_8_out, and_4_out, and_5_out, demultiplexer_1_out0,
       demultiplexer_2_out0, demultiplexer_3_out0, multiplexer_1_out, or_2_out, or_3_out, shifter_1_out,
       shifter_2_out, shifter_3_out, shifter_4_out, subtractor_1_out, subtractor_2_out, subtractor_8_out,
       xor_1_out, xor_2_out;

  Register #(.width(5)) register_1 (.D(signals), .en(and_1_out), .clk(clk), .Q(register_1_q));  // open: clr
  and and_1 (and_1_out, ~alu_busy, new_command);  // AND_Gate
  D_Flip_Flop d_ff_1 (.D(or_1_out), .clk(clk), .Q(reg_request));  // open: Qn, preset, reset
  or or_1 (or_1_out, new_command, alu_busy);
  Register #(.width(10)) register_2 (.D(destination), .en(and_1_out), .clk(clk), .Q(register_2_q));  // open: clr
  Register #(.width(10)) register_3 (.D(source1), .en(and_1_out), .clk(clk), .Q(register_3_q));  // open: clr
  Register #(.width(5)) register_4 (.D(source2), .en(and_1_out), .clk(clk), .Q(register_4_q));  // open: clr
  Comparator #(.mode("unsigned"), .width(5)) comparator_1 (
    .a(5'b01000), .b(register_1_q), .gt(comparator_1_gt));  // open: eq, lt
  and and_2 (and_2_out, reg_request, reg_request_granted);
  and and_3 (alu_busy, reg_request, ~reg_request_granted);  // AND_Gate
  Adder #(.width(32)) adder_1 (.a(reg_data_in_1), .b(reg_data_in_2), .out(adder_1_out));  // open: cin, cout
  Subtractor #(.width(32)) subtractor_1 (
    .a(reg_data_in_1), .b(reg_data_in_2), .out(subtractor_1_out));  // open: bin, bout
  assign and_4_out = reg_data_in_1 & reg_data_in_2;  // AND_Gate and_4, 32 bits wide
  assign or_2_out = reg_data_in_1 | reg_data_in_2;  // OR_Gate or_2, 32 bits wide
  assign xor_1_out = reg_data_in_1 ^ reg_data_in_2;  // XOR_Gate xor_1, 32 bits wide
  Adder adder_2 (.a(reg_data_in_1[7:0]), .b(reg_data_in_2[7:0]), .out(adder_2_out));  // open: cin, cout
  Adder adder_3 (.a(reg_data_in_1[15:8]), .b(reg_data_in_2[15:8]), .out(adder_3_out));  // open: cin, cout
  Adder adder_4 (.a(reg_data_in_1[23:16]), .b(reg_data_in_2[23:16]), .out(adder_4_out));  // open: cin, cout
  Adder adder_5 (.a(reg_data_in_1[31:24]), .b(reg_data_in_2[31:24]), .out(adder_5_out));  // open: cin, cout
  Pull_Resistor #(.pull(1)) pull_resistor_1 (.node(pull_resistor_1_node));
  Demultiplexer #(.select(5)) demultiplexer_1 (
    .out0(demultiplexer_1_out0[0]), .out1(demultiplexer_1_out0[1]), .out2(demultiplexer_1_out0[2]),
    .out3(demultiplexer_1_out0[3]), .out4(demultiplexer_1_out0[4]), .out5(demultiplexer_1_out0[5]),
    .out6(demultiplexer_1_out0[6]), .out7(demultiplexer_1_out0[7]), .out8(demultiplexer_1_out0[8]),
    .out9(demultiplexer_1_out0[9]), .out10(demultiplexer_1_out0[10]), .out11(demultiplexer_1_out0[11]),
    .out12(demultiplexer_1_out0[12]), .out13(demultiplexer_1_out0[13]), .out14(demultiplexer_1_out0[14]),
    .out15(demultiplexer_1_out0[15]), .out16(demultiplexer_1_out0[16]), .out17(demultiplexer_1_out0[17]),
    .out18(demultiplexer_1_out0[18]), .out19(demultiplexer_1_out0[19]), .out20(demultiplexer_1_out0[20]),
    .out21(demultiplexer_1_out0[21]), .out22(demultiplexer_1_out0[22]), .out23(demultiplexer_1_out0[23]),
    .out24(demultiplexer_1_out0[24]), .out25(demultiplexer_1_out0[25]), .out26(demultiplexer_1_out0[26]),
    .out27(demultiplexer_1_out0[27]), .out28(demultiplexer_1_out0[28]), .out29(demultiplexer_1_out0[29]),
    .out30(demultiplexer_1_out0[30]), .out31(demultiplexer_1_out0[31]), .in(pull_resistor_1_node),
    .sel(bit_extender_2_out));
  Multiplexer #(.select(5), .width(32)) multiplexer_1 (
    .in0(adder_1_out), .in1(subtractor_1_out), .in2(and_4_out), .in3(or_2_out), .in4(xor_1_out),
    .in5({adder_5_out, adder_4_out, adder_3_out, adder_2_out}), .in6(adder_6_out), .in7(subtractor_2_out),
    .in8({subtractor_7_out, subtractor_6_out}), .in9(shifter_1_out), .in10(shifter_2_out),
    .in11(shifter_3_out), .in12(shifter_4_out), .in13(or_3_out), .in14(and_5_out), .in15(xor_2_out),
    .in16(adder_8_out), .in17(subtractor_8_out), .out(multiplexer_1_out), .sel(register_1_q));  // open: in18, in19, in20, in21, in22, in23, in24, in25, in26, in27, in28, in29, in30, in31
  Adder #(.width(16)) adder_6 (
    .a(reg_data_in_1[15:0]), .b(reg_data_in_2[15:0]), .out(adder_6_out[15:0]));  // open: cin, cout
  Adder #(.width(16)) adder_7 (
    .a(reg_data_in_1[31:16]), .b(reg_data_in_2[31:16]), .out(adder_6_out[31:16]));  // open: cin, cout
  Subtractor subtractor_2 (
    .a(reg_data_in_1[7:0]), .b(reg_data_in_2[7:0]), .out(subtractor_2_out[7:0]));  // open: bin, bout
  Subtractor subtractor_3 (
    .a(reg_data_in_1[15:8]), .b(reg_data_in_2[15:8]), .out(subtractor_2_out[15:8]));  // open: bin, bout
  Subtractor subtractor_4 (
    .a(reg_data_in_1[23:16]), .b(reg_data_in_2[23:16]), .out(subtractor_2_out[23:16]));  // open: bin, bout
  Subtractor subtractor_5 (
    .a(reg_data_in_1[31:24]), .b(reg_data_in_2[31:24]), .out(subtractor_2_out[31:24]));  // open: bin, bout
  assign or_3_out = reg_data_in_1 | demultiplexer_1_out0;  // OR_Gate or_3, 32 bits wide
  Subtractor #(.width(16)) subtractor_6 (
    .a(reg_data_in_1[15:0]), .b(reg_data_in_2[15:0]), .out(subtractor_6_out));  // open: bin, bout
  Subtractor #(.width(16)) subtractor_7 (
    .a(reg_data_in_1[31:16]), .b(reg_data_in_2[31:16]), .out(subtractor_7_out));  // open: bin, bout
  Pull_Resistor pull_resistor_2 (.node(pull_resistor_2_node));
  Demultiplexer #(.select(5)) demultiplexer_2 (
    .out0(demultiplexer_2_out0[0]), .out1(demultiplexer_2_out0[1]), .out2(demultiplexer_2_out0[2]),
    .out3(demultiplexer_2_out0[3]), .out4(demultiplexer_2_out0[4]), .out5(demultiplexer_2_out0[5]),
    .out6(demultiplexer_2_out0[6]), .out7(demultiplexer_2_out0[7]), .out8(demultiplexer_2_out0[8]),
    .out9(demultiplexer_2_out0[9]), .out10(demultiplexer_2_out0[10]), .out11(demultiplexer_2_out0[11]),
    .out12(demultiplexer_2_out0[12]), .out13(demultiplexer_2_out0[13]), .out14(demultiplexer_2_out0[14]),
    .out15(demultiplexer_2_out0[15]), .out16(demultiplexer_2_out0[16]), .out17(demultiplexer_2_out0[17]),
    .out18(demultiplexer_2_out0[18]), .out19(demultiplexer_2_out0[19]), .out20(demultiplexer_2_out0[20]),
    .out21(demultiplexer_2_out0[21]), .out22(demultiplexer_2_out0[22]), .out23(demultiplexer_2_out0[23]),
    .out24(demultiplexer_2_out0[24]), .out25(demultiplexer_2_out0[25]), .out26(demultiplexer_2_out0[26]),
    .out27(demultiplexer_2_out0[27]), .out28(demultiplexer_2_out0[28]), .out29(demultiplexer_2_out0[29]),
    .out30(demultiplexer_2_out0[30]), .out31(demultiplexer_2_out0[31]), .in(pull_resistor_2_node),
    .sel(bit_extender_2_out));
  assign and_5_out = reg_data_in_1 & demultiplexer_2_out0;  // AND_Gate and_5, 32 bits wide
  Pull_Resistor #(.pull(1)) pull_resistor_3 (.node(pull_resistor_3_node));
  Demultiplexer #(.select(5)) demultiplexer_3 (
    .out0(demultiplexer_3_out0[0]), .out1(demultiplexer_3_out0[1]), .out2(demultiplexer_3_out0[2]),
    .out3(demultiplexer_3_out0[3]), .out4(demultiplexer_3_out0[4]), .out5(demultiplexer_3_out0[5]),
    .out6(demultiplexer_3_out0[6]), .out7(demultiplexer_3_out0[7]), .out8(demultiplexer_3_out0[8]),
    .out9(demultiplexer_3_out0[9]), .out10(demultiplexer_3_out0[10]), .out11(demultiplexer_3_out0[11]),
    .out12(demultiplexer_3_out0[12]), .out13(demultiplexer_3_out0[13]), .out14(demultiplexer_3_out0[14]),
    .out15(demultiplexer_3_out0[15]), .out16(demultiplexer_3_out0[16]), .out17(demultiplexer_3_out0[17]),
    .out18(demultiplexer_3_out0[18]), .out19(demultiplexer_3_out0[19]), .out20(demultiplexer_3_out0[20]),
    .out21(demultiplexer_3_out0[21]), .out22(demultiplexer_3_out0[22]), .out23(demultiplexer_3_out0[23]),
    .out24(demultiplexer_3_out0[24]), .out25(demultiplexer_3_out0[25]), .out26(demultiplexer_3_out0[26]),
    .out27(demultiplexer_3_out0[27]), .out28(demultiplexer_3_out0[28]), .out29(demultiplexer_3_out0[29]),
    .out30(demultiplexer_3_out0[30]), .out31(demultiplexer_3_out0[31]), .in(pull_resistor_3_node),
    .sel(bit_extender_2_out));
  assign bit_extender_1_out = {{5{1'b0}}, register_4_q};  // Bit_Extender bit_extender_1
  Bit_Extender #(.in_width(10), .out_width(5), .\type ("zero")) bit_extender_2 (
    .in(register_3_q), .out(bit_extender_2_out));
  Adder #(.width(32)) adder_8 (.a(reg_data_in_1), .b(32'h1), .out(adder_8_out));  // open: cin, cout
  Shifter #(.width(32)) shifter_1 (.in(reg_data_in_1), .\dist (bit_extender_2_out), .out(shifter_1_out));
  assign xor_2_out = reg_data_in_1 ^ demultiplexer_3_out0;  // XOR_Gate xor_2, 32 bits wide
  Pull_Resistor pull_resistor_4 (.node(reg_request));
  Pull_Resistor pull_resistor_5 (.node(multiplexer_1_out));
  assign data_out = and_2_out ? multiplexer_1_out : 32'bz;  // Controlled_Buffer controlled_buffer_1
  Pull_Resistor pull_resistor_6 (.node(and_2_out));
  assign write_reg = and_2_out ? and_2_out : 1'bz;  // Controlled_Buffer controlled_buffer_2
  Pull_Resistor pull_resistor_7 (.node(and_2_out));
  Pull_Resistor pull_resistor_8 (.node(register_2_q));
  assign wr_select_reg = and_2_out ? register_2_q : 10'bz;  // Controlled_Buffer controlled_buffer_3
  Pull_Resistor pull_resistor_9 (.node(pull_resistor_9_node));
  assign rd_select_reg = and_2_out ? pull_resistor_9_node : 10'bz;  // Controlled_Buffer controlled_buffer_4
  Multiplexer #(.width(10)) multiplexer_2 (
    .in0(register_2_q), .in1(register_3_q), .out(pull_resistor_9_node), .sel(comparator_1_gt));
  Pull_Resistor pull_resistor_10 (.node(bit_extender_1_out));
  assign rd_select_reg_2 = and_2_out ? bit_extender_1_out : 10'bz;  // Controlled_Buffer controlled_buffer_5
  Subtractor #(.width(32)) subtractor_8 (.a(reg_data_in_1), .b(32'h1), .out(subtractor_8_out));  // open: bin, bout
  Shifter #(.shift("lr"), .width(32)) shifter_2 (.in(reg_data_in_1), .\dist (bit_extender_2_out), .out(shifter_2_out));
  Shifter #(.shift("rl"), .width(32)) shifter_3 (.in(reg_data_in_1), .\dist (bit_extender_2_out), .out(shifter_3_out));
  Shifter #(.shift("rr"), .width(32)) shifter_4 (.in(reg_data_in_1), .\dist (bit_extender_2_out), .out(shifter_4_out));
endmodule

module idk_decoder_imm_thing (
  input  imm,
  input  clk,
  output imm_out
);

  wire and_1_out, and_2_out, d_ff_1_q, d_ff_2_q, d_ff_2_qn, pull_resistor_1_node;

  D_Flip_Flop d_ff_1 (.D(pull_resistor_1_node), .clk(imm), .Q(d_ff_1_q), .reset(d_ff_2_q));  // open: Qn, preset
  Pull_Resistor #(.pull(1)) pull_resistor_1 (.node(pull_resistor_1_node));
  D_Flip_Flop d_ff_2 (.D(d_ff_1_q), .clk(clk), .Q(d_ff_2_q), .Qn(d_ff_2_qn));  // open: preset, reset
  and and_1 (and_1_out, d_ff_2_qn, ~imm);  // AND_Gate
  and and_2 (and_2_out, d_ff_2_q, imm);
  or or_1 (imm_out, and_1_out, and_2_out);
endmodule

module controlled_in_sub (
  input  [9:0] signal_in,
  input  control,
  output [9:0] signal_out
);

  assign signal_out = control ? signal_in : 10'bz;  // Controlled_Buffer controlled_buffer_1
endmodule
