// Logisim project PLRU_cache_test.circ as structural Verilog: 1 circuit, main circuit main
module main (
  input  write
);

  wire and_1_out, and_2_out, and_3_out, and_4_out, and_5_out, and_6_out, and_7_out, and_8_out, clock_1_out,
       clock_2_out, clock_3_out, decoder_1_out0, decoder_1_out1, decoder_1_out2, decoder_1_out3, MRU_q,
       nand_1_out, not_1_out, pull_resistor_1_node, pull_resistor_2_node, pull_resistor_3_node,
       pull_resistor_4_node, pull_resistor_5_node, s_r_ff_1_q, s_r_ff_2_q, s_r_ff_3_q, s_r_ff_4_q,
       s_r_ff_5_q, s_r_ff_6_q, VALID_q;
  wire [1:0] controlled_buffer_5_out, counter_2_q, multiplexer_1_out;
  wire [7:0] counter_1_q;

  Counter counter_1 (.clk(clock_1_out), .Q(counter_1_q));  // open: clr, load, up, count, D, carry
  Clock clock_1 (.out(clock_1_out));
  Pull_Resistor pull_resistor_1 (.node(pull_resistor_1_node));
  assign pull_resistor_1_node = decoder_1_out0 ? decoder_1_out0 : 1'bz;  // Controlled_Buffer controlled_buffer_1
  assign pull_resistor_1_node = decoder_1_out1 ? decoder_1_out1 : 1'bz;  // Controlled_Buffer controlled_buffer_2
  assign pull_resistor_1_node = decoder_1_out2 ? decoder_1_out2 : 1'bz;  // Controlled_Buffer controlled_buffer_3
  assign pull_resistor_1_node = decoder_1_out3 ? decoder_1_out3 : 1'bz;  // Controlled_Buffer controlled_buffer_4
  Clock clock_2 (.out(clock_2_out));
  and and_1 (and_1_out, ~decoder_1_out0, pull_resistor_1_node);  // AND_Gate
  and and_2 (and_2_out, ~decoder_1_out1, pull_resistor_1_node);  // AND_Gate
  and and_3 (and_3_out, ~decoder_1_out2, pull_resistor_1_node);  // AND_Gate
  and and_4 (and_4_out, ~decoder_1_out3, pull_resistor_1_node);  // AND_Gate
  Register register_1 (.D(counter_1_q), .en(decoder_1_out0), .clk(clock_2_out));  // open: Q, clr
  Register register_2 (.D(counter_1_q), .en(decoder_1_out1), .clk(clock_2_out));  // open: Q, clr
  Register register_3 (.D(counter_1_q), .en(decoder_1_out2), .clk(clock_2_out));  // open: Q, clr
  Register register_4 (.D(counter_1_q), .en(decoder_1_out3), .clk(clock_2_out));  // open: Q, clr
  S_R_Flip_Flop MRU (.S(decoder_1_out0), .R(and_1_out), .clk(clock_2_out), .Q(MRU_q));  // open: reset, Qn, preset
  S_R_Flip_Flop s_r_ff_1 (
    .S(decoder_1_out1), .R(and_2_out), .clk(clock_2_out), .Q(s_r_ff_1_q));  // open: reset, Qn, preset
  S_R_Flip_Flop s_r_ff_2 (
    .S(decoder_1_out2), .R(and_3_out), .clk(clock_2_out), .Q(s_r_ff_2_q));  // open: reset, Qn, preset
  S_R_Flip_Flop s_r_ff_3 (
    .S(decoder_1_out3), .R(and_4_out), .clk(clock_2_out), .Q(s_r_ff_3_q));  // open: reset, Qn, preset
  Pull_Resistor pull_resistor_2 (.node(pull_resistor_2_node));
  Pull_Resistor pull_resistor_3 (.node(pull_resistor_3_node));
  Pull_Resistor pull_resistor_4 (.node(pull_resistor_4_node));
  Pull_Resistor pull_resistor_5 (.node(pull_resistor_5_node));
  S_R_Flip_Flop VALID (
    .S(decoder_1_out0), .R(pull_resistor_2_node), .clk(clock_2_out), .Q(VALID_q));  // open: reset, Qn, preset
  S_R_Flip_Flop s_r_ff_4 (
    .S(decoder_1_out1), .R(pull_resistor_3_node), .clk(clock_2_out), .Q(s_r_ff_4_q));  // open: reset, Qn, preset
  S_R_Flip_Flop s_r_ff_5 (
    .S(decoder_1_out2), .R(pull_resistor_4_node), .clk(clock_2_out), .Q(s_r_ff_5_q));  // open: reset, Qn, preset
  S_R_Flip_Flop s_r_ff_6 (
    .S(decoder_1_out3), .R(pull_resistor_5_node), .clk(clock_2_out), .Q(s_r_ff_6_q));  // open: reset, Qn, preset
  nand nand_1 (nand_1_out, VALID_q, s_r_ff_4_q, s_r_ff_5_q, s_r_ff_6_q);
  Decoder #(.select(2)) decoder_1 (
    .out0(decoder_1_out0), .out1(decoder_1_out1), .out2(decoder_1_out2), .out3(decoder_1_out3),
    .sel(multiplexer_1_out), .en(write));
  Multiplexer #(.width(2)) multiplexer_1 (
    .in0(controlled_buffer_5_out), .in1(counter_2_q), .out(multiplexer_1_out), .sel(nand_1_out));
  assign controlled_buffer_5_out = not_1_out ? 2'b00 : 2'bz;  // Controlled_Buffer controlled_buffer_5
  not not_1 (not_1_out, MRU_q);
  and and_5 (and_5_out, write, nand_1_out);
  Clock clock_3 (.out(clock_3_out));
  assign controlled_buffer_5_out = and_6_out ? 2'b01 : 2'bz;  // Controlled_Buffer controlled_buffer_6
  and and_6 (and_6_out, MRU_q, ~s_r_ff_1_q);  // AND_Gate
  Counter #(.max('h3), .width(2)) counter_2 (
    .count(and_5_out), .clk(clock_3_out), .Q(counter_2_q));  // open: clr, load, up, D, carry
  assign controlled_buffer_5_out = and_7_out ? 2'b10 : 2'bz;  // Controlled_Buffer controlled_buffer_7
  and and_7 (and_7_out, MRU_q, s_r_ff_1_q, ~s_r_ff_2_q);  // AND_Gate
  and and_8 (and_8_out, MRU_q, s_r_ff_1_q, s_r_ff_2_q, ~s_r_ff_3_q);  // AND_Gate
  assign controlled_buffer_5_out = and_8_out ? 2'b11 : 2'bz;  // Controlled_Buffer controlled_buffer_8
endmodule
